// Logisim project cpu24.circ as structural Verilog: 26 circuits, main circuit ◇单周期MIPS
module \单周期MIPS  (
);

  wire and_1_out, and_2_out, and_3_out, and_4_out, and_5_out, BAC, CLK, comparator_1_eq, comparator_2_eq,
       comparator_2_lt, counter_1_q, Enable, Go, JMP, LH, mips_alu_1_equal, not_3_out, or_1_out, or_2_out,
       RST, SignedExt, SRLV, Stop, \硬布线控制器_1_alu_src , \硬布线控制器_1_beq , \硬布线控制器_1_blez , \硬布线控制器_1_bne ,
       \硬布线控制器_1_jal , \硬布线控制器_1_jr , \硬布线控制器_1_memtoreg , \硬布线控制器_1_memwrite , \硬布线控制器_1_regdst ,
       \硬布线控制器_1_regwrite , \硬布线控制器_1_syscall ;
  wire [3:0] \硬布线控制器_1_alu_op ;
  wire [4:0] multiplexer_4_out, multiplexer_5_out, multiplexer_6_out, multiplexer_7_out, multiplexer_11_out,
       rom_1_data_2;
  wire [11:0] multiplexer_2_out, PC_q;
  wire [15:0] mips_ram_1_p6, mips_ram_1_p6_2, multiplexer_12_out, \总周期数 , \无条件分支数 , \条件分支成功数 ;
  wire [31:0] adder_1_out, adder_2_out, bit_extender_1_out, bit_extender_2_out, bit_extender_3_out,
       bit_extender_4_out, LedData, mips_alu_1_result, mips_regifile_1_r1, mips_regifile_1_r2,
       multiplexer_1_out, multiplexer_3_out, multiplexer_8_out, multiplexer_9_out, multiplexer_10_out,
       multiplexer_13_out, multiplexer_14_out, rom_1_data, shifter_1_out, shifter_2_out;
  wire [31:12] multiplexer_2_out_2, PC_q_2;

  Button \u_总复位  (.out(RST));
  Button \u_继续运行  (.out(Go));
  Clock clock_1 (.out(CLK));
  Hex_Digit_Display hex_digit_display_1 (.value(LedData[31:28]));  // open: dp
  Hex_Digit_Display hex_digit_display_2 (.value(LedData[27:24]));  // open: dp
  Multiplexer #(.width(32), .enable("false")) multiplexer_1 (
    .in0(adder_1_out), .in1(adder_2_out), .out(multiplexer_1_out), .sel(BAC));
  // Probe on multiplexer_2_out
  Multiplexer #(.width(32), .enable("false")) multiplexer_2 (
    .in0(shifter_1_out), .in1(mips_regifile_1_r1), .out({multiplexer_2_out_2, multiplexer_2_out}),
    .sel(\硬布线控制器_1_jr ));
  Hex_Digit_Display hex_digit_display_3 (.value(LedData[23:20]));  // open: dp
  Hex_Digit_Display hex_digit_display_4 (.value(LedData[19:16]));  // open: dp
  Multiplexer #(.width(32), .enable("false")) multiplexer_3 (
    .in0(multiplexer_1_out), .in1({multiplexer_2_out_2, multiplexer_2_out}), .out(multiplexer_3_out),
    .sel(JMP));
  // Probe on multiplexer_3_out[11:0]
  // Probe on PC_q
  Hex_Digit_Display hex_digit_display_5 (.value(LedData[11:8]));  // open: dp
  Hex_Digit_Display hex_digit_display_6 (.value(LedData[15:12]));  // open: dp
  and and_1 (and_1_out, Stop, \硬布线控制器_1_syscall );
  Register #(.width(32)) PC (.D(multiplexer_3_out), .en(Enable), .Q({PC_q_2, PC_q}), .clk(CLK), .clr(RST));
  Hex_Digit_Display hex_digit_display_7 (.value(LedData[7:4]));  // open: dp
  Hex_Digit_Display hex_digit_display_8 (.value(LedData[3:0]));  // open: dp
  Counter #(.width(1), .max('h1)) counter_1 (
    .D(\硬布线控制器_1_syscall ), .count(and_1_out), .Q(counter_1_q), .clk(CLK), .clr(or_1_out));  // open: load, carry
  not not_1 (Enable, counter_1_q);
  or or_1 (or_1_out, RST, Go);
  ROM #(.addrWidth(10), .dataWidth(32)) rom_1 (
    .addr(PC_q[11:2]), .data({rom_1_data[31:11], rom_1_data_2, rom_1_data[5:0]}));  // open: sel
  Adder #(.width(32)) adder_1 (.a({PC_q_2, PC_q}), .b(32'h4), .out(adder_1_out));  // open: cin, cout
  // Probe on \总周期数 
  // Probe on \无条件分支数 
  // Probe on \条件分支成功数 
  \硬布线控制器  \u_硬布线控制器_1  (
    .Func(rom_1_data[5:0]), .OP(rom_1_data[31:26]), .ALU_OP(\硬布线控制器_1_alu_op ),
    .MemToReg(\硬布线控制器_1_memtoreg ), .MemWrite(\硬布线控制器_1_memwrite ), .ALU_SRC(\硬布线控制器_1_alu_src ),
    .RegWrite(\硬布线控制器_1_regwrite ), .SysCALL(\硬布线控制器_1_syscall ), .SignedExt(SignedExt),
    .RegDst(\硬布线控制器_1_regdst ), .JR(\硬布线控制器_1_jr ), .JMP(JMP), .Beq(\硬布线控制器_1_beq ), .JAL(\硬布线控制器_1_jal ),
    .Bne(\硬布线控制器_1_bne ), .LH(LH), .BLEZ(\硬布线控制器_1_blez ), .SRLV(SRLV));  // open: ERET, MFC0, MTC0, MF
  Multiplexer #(.width(5), .enable("false")) multiplexer_4 (
    .in0(rom_1_data[25:21]), .in1(5'b00100), .out(multiplexer_4_out), .sel(\硬布线控制器_1_syscall ));
  Multiplexer #(.width(5), .enable("false")) multiplexer_5 (
    .in0(rom_1_data[20:16]), .in1(5'b00010), .out(multiplexer_5_out), .sel(\硬布线控制器_1_syscall ));
  Multiplexer #(.width(5), .enable("false")) multiplexer_6 (
    .in0(rom_1_data[20:16]), .in1(rom_1_data[15:11]), .out(multiplexer_6_out), .sel(\硬布线控制器_1_regdst ));
  Multiplexer #(.width(5), .enable("false")) multiplexer_7 (
    .in0(multiplexer_6_out), .in1({5{1'b1}}), .out(multiplexer_7_out), .sel(\硬布线控制器_1_jal ));
  assign bit_extender_1_out = {{16{1'b0}}, {rom_1_data[15:11], rom_1_data_2, rom_1_data[5:0]}};  // Bit_Extender bit_extender_1
  assign bit_extender_2_out = {{16{rom_1_data[15]}}, {rom_1_data[15:11], rom_1_data_2, rom_1_data[5:0]}};  // Bit_Extender bit_extender_2
  assign bit_extender_3_out = {{6{rom_1_data[25]}}, {rom_1_data[25:11], rom_1_data_2, rom_1_data[5:0]}};  // Bit_Extender bit_extender_3
  Multiplexer #(.width(32), .enable("false")) multiplexer_8 (
    .in0(multiplexer_13_out), .in1(adder_1_out), .out(multiplexer_8_out), .sel(\硬布线控制器_1_jal ));
  Multiplexer #(.width(32), .enable("false")) multiplexer_9 (
    .in0(bit_extender_1_out), .in1(bit_extender_2_out), .out(multiplexer_9_out), .sel(SignedExt));
  Shifter #(.width(32)) shifter_1 (.in(bit_extender_3_out), .\dist (5'b00010), .out(shifter_1_out));
  Shifter #(.width(32)) shifter_2 (.in(multiplexer_9_out), .\dist (5'b00010), .out(shifter_2_out));
  Counter #(.width(16), .max('hffff)) counter_2 (
    .count(Enable), .Q(\总周期数 ), .clk(CLK), .clr(RST));  // open: load, D, carry
  not not_2 (Stop, comparator_1_eq);
  Register #(.width(32)) register_1 (.D(mips_regifile_1_r1), .en(and_2_out), .Q(LedData), .clk(CLK), .clr(RST));
  and and_2 (and_2_out, comparator_1_eq, \硬布线控制器_1_syscall );
  MIPS_Regifile mips_regifile_1 (
    .Din(multiplexer_8_out), .Clk(CLK), .R1(mips_regifile_1_r1), .R2(mips_regifile_1_r2),
    .WE(\硬布线控制器_1_regwrite ), .W_num(multiplexer_7_out), .R1_num(multiplexer_4_out),
    .R2_num(multiplexer_5_out));
  Comparator #(.width(32)) comparator_1 (.a(32'h22), .b(mips_regifile_1_r2), .eq(comparator_1_eq));  // open: gt, lt
  Multiplexer #(.width(32), .enable("false")) multiplexer_10 (
    .in0(mips_regifile_1_r2), .in1(multiplexer_9_out), .out(multiplexer_10_out), .sel(\硬布线控制器_1_alu_src ));
  Adder #(.width(32)) adder_2 (.a(shifter_2_out), .b(adder_1_out), .out(adder_2_out));  // open: cin, cout
  Comparator #(.width(32)) comparator_2 (
    .a(mips_regifile_1_r1), .b({32{1'b0}}), .eq(comparator_2_eq), .lt(comparator_2_lt));  // open: gt
  MIPS_ALU mips_alu_1 (
    .X(mips_regifile_1_r1), .Y(multiplexer_10_out), .AluOP(\硬布线控制器_1_alu_op ), .Equal(mips_alu_1_equal),
    .Result(mips_alu_1_result), .shamt(multiplexer_11_out));  // open: Result_2
  Multiplexer #(.width(5), .enable("false")) multiplexer_11 (
    .in0(rom_1_data_2), .in1(mips_regifile_1_r1[4:0]), .out(multiplexer_11_out), .sel(SRLV));
  Counter #(.width(16), .max('hffff)) counter_3 (
    .count(JMP), .Q(\无条件分支数 ), .clk(CLK), .clr(RST));  // open: load, D, carry
  or or_2 (or_2_out, comparator_2_eq, comparator_2_lt);
  and and_3 (and_3_out, or_2_out, \硬布线控制器_1_blez );
  and and_4 (and_4_out, mips_alu_1_equal, \硬布线控制器_1_beq );
  not not_3 (not_3_out, mips_alu_1_equal);
  and and_5 (and_5_out, not_3_out, \硬布线控制器_1_bne );
  or or_3 (BAC, and_4_out, and_3_out, and_5_out);
  Multiplexer #(.width(16), .enable("false")) multiplexer_12 (
    .in0(mips_ram_1_p6), .in1(mips_ram_1_p6_2), .out(multiplexer_12_out), .sel(mips_alu_1_result[1]));
  Counter #(.width(16), .max('hffff)) counter_4 (
    .count(BAC), .Q(\条件分支成功数 ), .clk(CLK), .clr(RST));  // open: load, D, carry
  // MIPS_RAM mips_ram_1: pin names not known; wires that end beside it: mips_alu_1_result[11:2], mips_regifile_1_r2, \硬布线控制器_1_memwrite , CLK, RST, {mips_ram_1_p6_2, mips_ram_1_p6}
  assign bit_extender_4_out = {{16{multiplexer_12_out[15]}}, multiplexer_12_out};  // Bit_Extender bit_extender_4
  Multiplexer #(.width(32), .enable("false")) multiplexer_13 (
    .in0(mips_alu_1_result), .in1(multiplexer_14_out), .out(multiplexer_13_out), .sel(\硬布线控制器_1_memtoreg ));
  Multiplexer #(.width(32), .enable("false")) multiplexer_14 (
    .in0({mips_ram_1_p6_2, mips_ram_1_p6}), .in1(bit_extender_4_out), .out(multiplexer_14_out), .sel(LH));

  // Notes on the sheet:
  //   数码管输出应该用寄存器锁存，否则显示数据只能一闪而过
  //   可以通过项目增加Logisim库的方式将前几次实验完成的电路作为子电路引入到本电路中使用
  //   数码管输出
  //   指令存储器
  //   指令字
  //   contents of rom_1 (hex, n*v repeats v):
  //   20110001 8100005 20110001 20120002 20130003 8100009 20110001 20120002 20130003 810000d 20110001
  //   20120002 20130003 8100011 20110001 20120002 20130003 c1000f6 20100001 20110001 118fc0 112020
  //   20020022 c 118882 12200001 8100015 112020 20020022 c 20110001 118880 112020 20020022 c 12200001
  //   810001f 20110001 118fc0 112020 20020022 c 1188c3 112020 20020022 c 118903 112020 20020022 c 118903
  //   112020 20020022 c 118903 112020 20020022 c 118903 112020 20020022 c 118903 112020 20020022 c 118903
  //   112020 20020022 c 118903 112020 20020022 c 20100001 109fc0 139fc3 8021 2012000c 24160003 26100001
  //   3210000f 20080008 20090001 139900 2709825 132020 20020022 c 1094022 1500fff9 22100001 2018000f
  //   2188024 108700 20080008 20090001 139902 2709825 132021 20020022 c 1094022 1500fff9 108702 2c9b022
  //   12c00001 8100050 4020 1084027 84400 3508ffff 82021 20020022 c 2010ffff 20110000 ae300000 22100001
  //   22310004 ae300000 22100001 22310004 ae300000 22100001 22310004 ae300000 22100001 22310004 ae300000
  //   22100001 22310004 ae300000 22100001 22310004 ae300000 22100001 22310004 ae300000 22100001 22310004
  //   ae300000 22100001 22310004 ae300000 22100001 22310004 ae300000 22100001 22310004 ae300000 22100001
  //   22310004 ae300000 22100001 22310004 ae300000 22100001 22310004 ae300000 22100001 22310004 ae300000
  //   22100001 22310004 22100001 8020 2011003c 8e130000 8e340000 274402a 11000002 ae330000 ae140000
  //   2231fffc 1611fff8 102020 20020022 c 22100004 2011003c 1611fff2 20020032 c 20080001 20090003 20110876
  //   118d00 112020 20020022 c 200b0008 1118806 1318806 112020 20020022 c 216bffff 1560fff9 2002000a c
  //   2008ffff 20090000 20111997 112020 20020022 c 2288820 2e291949 1120fffa 2002000a c 20090000 200b0010
  //   34118483 20120404 118c00 129400 36318281 22520404 ad310000 2328820 21290004 216bffff 1560fffb
  //   200b0020 20090000 85310000 112020 20020022 c 21290002 216bffff 1560fff9 2002000a c 2011fff1 112020
  //   20020022 c 22310001 1a20fffb 2002000a c 2002000a c 20100000 22100001 102020 20020022 c 22100002
  //   102020 20020022 c 22100003 102020 20020022 c 22100004 102020 20020022 c 22100005 102020 20020022 c
  //   22100006 102020 20020022 c 22100007 102020 20020022 c 22100008 102020 20020022 20020022 c 3e00008
  //   JMP
  //   JR
  //   BLEZ
  //   OP
  //   Func
  //   Syscall
  //   OP
  //   Func
  //   rs
  //   rt
  //   rd
  //   Shamt
  //   总复位信号应将除ROM以外所有存储组件全部清零
  //   Beq
  //   Bne
  //   MemToReg
  //   MemWrite
  //   AluOP
  //   AluSrcB
  //   RegWrite
  //   JAL
  //   RegDst
  //   $a0
  //   $v0
endmodule

// 单周期硬布线控制器
module \硬布线控制器  (
  input  [5:0] OP,
  input  [5:0] Func,
  input  [4:0] MF,
  output [3:0] ALU_OP,
  output MemToReg,
  output MemWrite,
  output ALU_SRC,
  output RegWrite,
  output SysCALL,
  output SignedExt,
  output RegDst,
  output Beq,
  output Bne,
  output JR,
  output JMP,
  output JAL,
  output LH,
  output BLEZ,
  output SRLV,
  output ERET,
  output MFC0,
  output MTC0
);

  wire comparator_1_eq, comparator_2_eq, comparator_3_eq, \控制信号生成_1_regwrite ;

  Comparator #(.width(6)) comparator_1 (.a(OP), .b(6'b010000), .eq(comparator_1_eq));  // open: gt, lt
  Comparator #(.width(5)) comparator_2 (.a(MF), .b({5{1'b0}}), .eq(comparator_2_eq));  // open: gt, lt
  Comparator #(.width(5)) comparator_3 (.a(MF), .b(5'b00100), .eq(comparator_3_eq));  // open: gt, lt
  \运算控制器  \u_运算控制器_1  (
    .OP0(OP[0]), .OP1(OP[1]), .OP2(OP[2]), .OP3(OP[3]), .OP4(OP[4]), .OP5(OP[5]), .F0(Func[0]), .F1(Func[1]),
    .F2(Func[2]), .F3(Func[3]), .F4(Func[4]), .F5(Func[5]), .S0(ALU_OP[0]), .S1(ALU_OP[1]), .S2(ALU_OP[2]),
    .S3(ALU_OP[3]));
  \控制信号生成  \u_控制信号生成_1  (
    .OP0(OP[0]), .OP1(OP[1]), .OP2(OP[2]), .OP3(OP[3]), .OP4(OP[4]), .OP5(OP[5]), .F0(Func[0]), .F1(Func[1]),
    .F2(Func[2]), .F3(Func[3]), .F4(Func[4]), .F5(Func[5]), .MemToReg(MemToReg), .MemWrite(MemWrite),
    .ALU_SRC(ALU_SRC), .RegWrite(\控制信号生成_1_regwrite ), .SysCALL(SysCALL), .SignedExt(SignedExt),
    .RegDst(RegDst), .BEQ(Beq), .BNE(Bne), .JR(JR), .JMP(JMP), .JAL(JAL));
  \信号生成2  \u_信号生成2_1  (
    .OP0(OP[0]), .OP1(OP[1]), .OP2(OP[2]), .OP3(OP[3]), .OP4(OP[4]), .OP5(OP[5]), .F0(Func[0]), .F1(Func[1]),
    .F2(Func[2]), .F3(Func[3]), .F4(Func[4]), .F5(Func[5]), .LH(LH), .BLEZ(BLEZ), .SRLV(SRLV), .ERET(ERET));
  and and_1 (MFC0, comparator_2_eq, comparator_1_eq);
  and and_2 (MTC0, comparator_3_eq, comparator_1_eq);
  or or_1 (RegWrite, MFC0, \控制信号生成_1_regwrite );

  // Other names for the same wires on the sheet: OP_CODE[5:0] = OP

  // Notes on the sheet:
  //   运算器控制器，根据指令生成运算器功能选择信号
  //   控制信号生成，产生数据通路需要的其他控制信号
endmodule

// 运算器控制器
module \运算控制器  (
  input  OP0,
  input  OP1,
  input  OP2,
  input  OP3,
  input  OP4,
  input  OP5,
  input  F0,
  input  F1,
  input  F2,
  input  F3,
  input  F4,
  input  F5,
  output S0,
  output S1,
  output S2,
  output S3
);

  wire and_1_out, and_2_out, and_3_out, and_4_out, and_5_out, and_6_out, and_7_out, and_8_out, and_9_out,
       and_10_out, and_11_out, and_12_out, and_13_out, and_14_out, and_15_out, and_16_out, and_17_out,
       and_18_out, and_19_out, and_20_out, and_21_out, and_22_out, and_23_out, and_24_out, and_25_out,
       and_26_out, and_27_out, and_28_out, and_29_out, and_30_out, and_31_out, and_32_out, and_33_out,
       and_34_out, and_35_out, and_36_out, and_37_out, and_38_out, and_39_out, and_40_out, and_41_out,
       and_42_out, and_43_out, and_44_out, and_45_out, and_46_out, not_1_out, not_2_out, not_3_out,
       not_4_out, not_5_out, not_6_out, not_7_out, not_8_out, not_9_out, not_10_out, not_11_out, not_12_out,
       not_13_out, not_14_out, not_15_out, not_16_out, not_17_out, not_18_out, not_19_out, not_20_out,
       not_21_out, not_22_out, not_23_out, not_24_out, not_25_out, not_26_out, not_27_out, not_28_out,
       not_29_out, not_30_out, not_31_out, not_32_out, not_33_out, not_34_out, not_35_out, not_36_out,
       not_37_out, not_38_out, not_39_out, not_40_out, not_41_out, not_42_out, not_43_out, not_44_out,
       not_45_out, not_46_out, not_47_out, not_48_out, not_49_out, not_50_out, not_51_out, not_52_out,
       not_53_out, not_54_out, not_55_out, not_56_out, not_57_out, not_58_out, not_59_out, not_60_out,
       not_61_out, not_62_out, not_63_out, not_64_out, not_65_out, not_66_out, not_67_out, not_68_out,
       not_69_out, not_70_out, not_71_out, not_72_out, not_73_out, not_74_out, not_75_out, not_76_out,
       not_77_out, not_78_out, not_79_out, not_80_out, not_81_out, not_82_out, not_83_out, not_84_out,
       not_85_out, not_86_out, not_87_out, not_88_out, not_89_out, not_90_out, not_91_out, not_92_out,
       not_93_out, not_94_out, not_95_out, not_96_out, not_97_out, not_98_out, not_99_out, not_100_out,
       not_101_out, not_102_out, not_103_out, not_104_out, not_105_out, not_106_out, not_107_out,
       not_108_out, not_109_out, not_110_out, not_111_out, not_112_out, not_113_out, not_114_out,
       not_115_out, not_116_out, not_117_out, not_118_out, not_119_out, not_120_out, not_121_out,
       not_122_out, not_123_out, not_124_out, not_125_out, not_126_out, not_127_out, not_128_out,
       not_129_out, not_130_out, not_131_out, not_132_out, not_133_out, not_134_out, not_135_out,
       not_136_out, not_137_out, not_138_out, not_139_out, not_140_out, not_141_out, not_142_out,
       not_143_out, not_144_out, not_145_out, not_146_out, not_147_out, not_148_out, not_149_out,
       not_150_out, not_151_out, not_152_out, not_153_out, not_154_out, not_155_out, not_156_out,
       not_157_out, not_158_out, not_159_out, not_160_out, not_161_out, not_162_out, not_163_out,
       not_164_out, not_165_out, not_166_out, not_167_out, not_168_out, not_169_out, not_170_out,
       not_171_out, not_172_out, not_173_out, not_174_out, not_175_out, not_176_out, not_177_out,
       not_178_out, not_179_out, not_180_out, not_181_out, not_182_out, not_183_out, not_184_out,
       not_185_out, not_186_out, not_187_out, not_188_out, not_189_out, not_190_out, not_191_out,
       not_192_out, not_193_out, not_194_out, not_195_out, not_196_out, not_197_out, not_198_out,
       not_199_out, not_200_out, not_201_out, not_202_out, not_203_out, not_204_out, not_205_out,
       not_206_out, not_207_out, not_208_out, not_209_out, not_210_out, not_211_out, not_212_out,
       not_213_out, not_214_out, not_215_out, not_216_out, not_217_out, not_218_out, not_219_out,
       not_220_out, not_221_out, not_222_out, not_223_out, not_224_out, not_225_out, not_226_out,
       not_227_out, not_228_out, not_229_out, not_230_out, not_231_out, not_232_out, not_233_out,
       not_234_out, not_235_out, not_236_out, not_237_out, not_238_out, not_239_out, not_240_out,
       not_241_out, not_242_out, not_243_out, not_244_out, not_245_out, not_246_out, not_247_out,
       not_248_out, not_249_out, not_250_out, not_251_out, not_252_out, not_253_out, not_254_out,
       not_255_out, not_256_out, not_257_out, not_258_out, not_259_out, not_260_out, not_261_out,
       not_262_out, not_263_out, not_264_out, not_265_out, not_266_out, not_267_out, not_268_out,
       not_269_out, not_270_out, not_271_out, not_272_out, not_273_out, not_274_out, not_275_out,
       not_276_out, not_277_out, not_278_out, not_279_out, not_280_out, not_281_out, not_282_out,
       not_283_out, not_284_out, not_285_out, not_286_out, not_287_out, not_288_out, not_289_out,
       not_290_out, not_291_out, not_292_out, not_293_out, not_294_out, not_295_out, not_296_out,
       not_297_out, not_298_out, not_299_out, not_300_out, not_301_out, not_302_out, not_303_out, not_304_out;

  not not_1 (not_1_out, OP5);
  not not_2 (not_2_out, OP4);
  not not_3 (not_3_out, OP3);
  not not_4 (not_4_out, OP2);
  not not_5 (not_5_out, OP1);
  not not_6 (not_6_out, OP0);
  not not_7 (not_7_out, F5);
  not not_8 (not_8_out, F4);
  not not_9 (not_9_out, F3);
  not not_10 (not_10_out, F2);
  not not_11 (not_11_out, OP5);
  not not_12 (not_12_out, OP4);
  not not_13 (not_13_out, OP3);
  not not_14 (not_14_out, OP2);
  not not_15 (not_15_out, OP1);
  not not_16 (not_16_out, OP0);
  not not_17 (not_17_out, F4);
  not not_18 (not_18_out, F3);
  not not_19 (not_19_out, F2);
  not not_20 (not_20_out, F1);
  not not_21 (not_21_out, F0);
  not not_22 (not_22_out, OP5);
  not not_23 (not_23_out, OP4);
  not not_24 (not_24_out, OP3);
  not not_25 (not_25_out, OP2);
  not not_26 (not_26_out, OP1);
  not not_27 (not_27_out, OP0);
  not not_28 (not_28_out, F4);
  not not_29 (not_29_out, F3);
  not not_30 (not_30_out, F2);
  not not_31 (not_31_out, F1);
  not not_32 (not_32_out, OP5);
  not not_33 (not_33_out, OP4);
  not not_34 (not_34_out, OP3);
  not not_35 (not_35_out, OP2);
  not not_36 (not_36_out, OP1);
  not not_37 (not_37_out, OP0);
  not not_38 (not_38_out, F4);
  not not_39 (not_39_out, F3);
  not not_40 (not_40_out, F1);
  not not_41 (not_41_out, F0);
  not not_42 (not_42_out, OP5);
  not not_43 (not_43_out, OP4);
  not not_44 (not_44_out, OP3);
  not not_45 (not_45_out, OP2);
  not not_46 (not_46_out, OP1);
  not not_47 (not_47_out, OP0);
  not not_48 (not_48_out, F4);
  not not_49 (not_49_out, F2);
  not not_50 (not_50_out, F0);
  not not_51 (not_51_out, OP5);
  not not_52 (not_52_out, OP4);
  not not_53 (not_53_out, OP2);
  not not_54 (not_54_out, OP1);
  not not_55 (not_55_out, OP0);
  not not_56 (not_56_out, OP5);
  not not_57 (not_57_out, OP4);
  not not_58 (not_58_out, OP1);
  not not_59 (not_59_out, OP0);
  not not_60 (not_60_out, OP5);
  not not_61 (not_61_out, OP4);
  not not_62 (not_62_out, OP2);
  not not_63 (not_63_out, OP1);
  not not_64 (not_64_out, OP5);
  not not_65 (not_65_out, OP4);
  not not_66 (not_66_out, OP2);
  not not_67 (not_67_out, OP0);
  not not_68 (not_68_out, OP4);
  not not_69 (not_69_out, OP3);
  not not_70 (not_70_out, OP2);
  not not_71 (not_71_out, OP4);
  not not_72 (not_72_out, OP2);
  not not_73 (not_73_out, OP4);
  not not_74 (not_74_out, OP3);
  not not_75 (not_75_out, OP2);
  not not_76 (not_76_out, OP1);
  not not_77 (not_77_out, OP5);
  not not_78 (not_78_out, OP4);
  not not_79 (not_79_out, OP3);
  not not_80 (not_80_out, OP2);
  not not_81 (not_81_out, OP1);
  not not_82 (not_82_out, OP0);
  not not_83 (not_83_out, F5);
  not not_84 (not_84_out, F4);
  not not_85 (not_85_out, F3);
  not not_86 (not_86_out, F2);
  not not_87 (not_87_out, F0);
  not not_88 (not_88_out, OP5);
  not not_89 (not_89_out, OP4);
  not not_90 (not_90_out, OP3);
  not not_91 (not_91_out, OP2);
  not not_92 (not_92_out, OP1);
  not not_93 (not_93_out, OP0);
  not not_94 (not_94_out, F4);
  not not_95 (not_95_out, F3);
  not not_96 (not_96_out, F2);
  not not_97 (not_97_out, F0);
  not not_98 (not_98_out, OP5);
  not not_99 (not_99_out, OP4);
  not not_100 (not_100_out, OP3);
  not not_101 (not_101_out, OP2);
  not not_102 (not_102_out, OP1);
  not not_103 (not_103_out, OP0);
  not not_104 (not_104_out, F4);
  not not_105 (not_105_out, F3);
  not not_106 (not_106_out, F1);
  not not_107 (not_107_out, F0);
  not not_108 (not_108_out, OP5);
  not not_109 (not_109_out, OP4);
  not not_110 (not_110_out, OP3);
  not not_111 (not_111_out, OP2);
  not not_112 (not_112_out, OP1);
  not not_113 (not_113_out, OP0);
  not not_114 (not_114_out, F4);
  not not_115 (not_115_out, F3);
  not not_116 (not_116_out, OP5);
  not not_117 (not_117_out, OP4);
  not not_118 (not_118_out, OP3);
  not not_119 (not_119_out, OP2);
  not not_120 (not_120_out, OP1);
  not not_121 (not_121_out, OP0);
  not not_122 (not_122_out, F4);
  not not_123 (not_123_out, F2);
  not not_124 (not_124_out, F0);
  not not_125 (not_125_out, OP5);
  not not_126 (not_126_out, OP4);
  not not_127 (not_127_out, OP1);
  not not_128 (not_128_out, OP0);
  not not_129 (not_129_out, OP5);
  not not_130 (not_130_out, OP4);
  not not_131 (not_131_out, OP2);
  not not_132 (not_132_out, OP0);
  not not_133 (not_133_out, OP5);
  not not_134 (not_134_out, OP4);
  not not_135 (not_135_out, OP3);
  not not_136 (not_136_out, OP2);
  not not_137 (not_137_out, OP1);
  not not_138 (not_138_out, OP0);
  not not_139 (not_139_out, F5);
  not not_140 (not_140_out, F4);
  not not_141 (not_141_out, F3);
  not not_142 (not_142_out, F0);
  not not_143 (not_143_out, OP5);
  not not_144 (not_144_out, OP4);
  not not_145 (not_145_out, OP3);
  not not_146 (not_146_out, OP2);
  not not_147 (not_147_out, OP1);
  not not_148 (not_148_out, OP0);
  not not_149 (not_149_out, F4);
  not not_150 (not_150_out, F3);
  not not_151 (not_151_out, F2);
  not not_152 (not_152_out, F1);
  not not_153 (not_153_out, F0);
  not not_154 (not_154_out, OP5);
  not not_155 (not_155_out, OP4);
  not not_156 (not_156_out, OP3);
  not not_157 (not_157_out, OP2);
  not not_158 (not_158_out, OP1);
  not not_159 (not_159_out, OP0);
  not not_160 (not_160_out, F4);
  not not_161 (not_161_out, F3);
  not not_162 (not_162_out, F2);
  not not_163 (not_163_out, F1);
  not not_164 (not_164_out, OP5);
  not not_165 (not_165_out, OP4);
  not not_166 (not_166_out, OP3);
  not not_167 (not_167_out, OP2);
  not not_168 (not_168_out, OP1);
  not not_169 (not_169_out, OP0);
  not not_170 (not_170_out, F4);
  not not_171 (not_171_out, F3);
  not not_172 (not_172_out, F2);
  not not_173 (not_173_out, F0);
  not not_174 (not_174_out, OP5);
  not not_175 (not_175_out, OP4);
  not not_176 (not_176_out, OP3);
  not not_177 (not_177_out, OP2);
  not not_178 (not_178_out, OP1);
  not not_179 (not_179_out, OP0);
  not not_180 (not_180_out, F4);
  not not_181 (not_181_out, F3);
  not not_182 (not_182_out, F1);
  not not_183 (not_183_out, F0);
  not not_184 (not_184_out, OP5);
  not not_185 (not_185_out, OP4);
  not not_186 (not_186_out, OP3);
  not not_187 (not_187_out, OP2);
  not not_188 (not_188_out, OP1);
  not not_189 (not_189_out, OP0);
  not not_190 (not_190_out, F4);
  not not_191 (not_191_out, F2);
  not not_192 (not_192_out, OP5);
  not not_193 (not_193_out, OP4);
  not not_194 (not_194_out, OP2);
  not not_195 (not_195_out, OP1);
  not not_196 (not_196_out, OP0);
  not not_197 (not_197_out, OP5);
  not not_198 (not_198_out, OP4);
  not not_199 (not_199_out, OP1);
  not not_200 (not_200_out, OP0);
  not not_201 (not_201_out, OP5);
  not not_202 (not_202_out, OP4);
  not not_203 (not_203_out, OP2);
  not not_204 (not_204_out, OP1);
  not not_205 (not_205_out, OP4);
  not not_206 (not_206_out, OP3);
  not not_207 (not_207_out, OP2);
  not not_208 (not_208_out, OP4);
  not not_209 (not_209_out, OP2);
  not not_210 (not_210_out, OP5);
  not not_211 (not_211_out, OP4);
  not not_212 (not_212_out, OP2);
  not not_213 (not_213_out, OP4);
  not not_214 (not_214_out, OP3);
  not not_215 (not_215_out, OP2);
  not not_216 (not_216_out, OP1);
  not not_217 (not_217_out, OP5);
  not not_218 (not_218_out, OP4);
  not not_219 (not_219_out, OP3);
  not not_220 (not_220_out, OP2);
  not not_221 (not_221_out, OP1);
  not not_222 (not_222_out, OP0);
  not not_223 (not_223_out, F4);
  not not_224 (not_224_out, F3);
  not not_225 (not_225_out, F1);
  not not_226 (not_226_out, OP5);
  not not_227 (not_227_out, OP4);
  not not_228 (not_228_out, OP3);
  not not_229 (not_229_out, OP2);
  not not_230 (not_230_out, OP1);
  not not_231 (not_231_out, OP0);
  not not_232 (not_232_out, F4);
  not not_233 (not_233_out, F3);
  not not_234 (not_234_out, OP5);
  not not_235 (not_235_out, OP4);
  not not_236 (not_236_out, OP3);
  not not_237 (not_237_out, OP2);
  not not_238 (not_238_out, OP1);
  not not_239 (not_239_out, OP0);
  not not_240 (not_240_out, F4);
  not not_241 (not_241_out, F2);
  not not_242 (not_242_out, F0);
  not not_243 (not_243_out, OP5);
  not not_244 (not_244_out, OP4);
  not not_245 (not_245_out, OP3);
  not not_246 (not_246_out, OP2);
  not not_247 (not_247_out, OP1);
  not not_248 (not_248_out, OP0);
  not not_249 (not_249_out, F4);
  not not_250 (not_250_out, F2);
  not not_251 (not_251_out, OP5);
  not not_252 (not_252_out, OP4);
  not not_253 (not_253_out, OP2);
  not not_254 (not_254_out, OP0);
  not not_255 (not_255_out, OP5);
  not not_256 (not_256_out, OP4);
  not not_257 (not_257_out, OP1);
  not not_258 (not_258_out, OP5);
  not not_259 (not_259_out, OP4);
  not not_260 (not_260_out, OP2);
  not not_261 (not_261_out, OP5);
  not not_262 (not_262_out, OP4);
  not not_263 (not_263_out, OP3);
  not not_264 (not_264_out, OP2);
  not not_265 (not_265_out, OP1);
  not not_266 (not_266_out, OP0);
  not not_267 (not_267_out, F4);
  not not_268 (not_268_out, F3);
  not not_269 (not_269_out, F1);
  not not_270 (not_270_out, OP5);
  not not_271 (not_271_out, OP4);
  not not_272 (not_272_out, OP3);
  not not_273 (not_273_out, OP2);
  not not_274 (not_274_out, OP1);
  not not_275 (not_275_out, OP0);
  not not_276 (not_276_out, F4);
  not not_277 (not_277_out, F3);
  not not_278 (not_278_out, OP5);
  not not_279 (not_279_out, OP4);
  not not_280 (not_280_out, OP3);
  not not_281 (not_281_out, OP2);
  not not_282 (not_282_out, OP1);
  not not_283 (not_283_out, OP0);
  not not_284 (not_284_out, F4);
  not not_285 (not_285_out, F2);
  not not_286 (not_286_out, F0);
  not not_287 (not_287_out, OP5);
  not not_288 (not_288_out, OP4);
  not not_289 (not_289_out, OP3);
  not not_290 (not_290_out, OP2);
  not not_291 (not_291_out, OP1);
  not not_292 (not_292_out, OP0);
  not not_293 (not_293_out, F4);
  not not_294 (not_294_out, F2);
  not not_295 (not_295_out, OP5);
  not not_296 (not_296_out, OP4);
  not not_297 (not_297_out, OP2);
  not not_298 (not_298_out, OP0);
  not not_299 (not_299_out, OP5);
  not not_300 (not_300_out, OP4);
  not not_301 (not_301_out, OP1);
  not not_302 (not_302_out, OP5);
  not not_303 (not_303_out, OP4);
  not not_304 (not_304_out, OP2);
  and and_1 (and_1_out, not_1_out, not_2_out, not_3_out, not_4_out, not_5_out, not_6_out, not_7_out, not_8_out, not_9_out, not_10_out, F1, F0);
  and and_2 (and_2_out, not_11_out, not_12_out, not_13_out, not_14_out, not_15_out, not_16_out, F5, not_17_out, not_18_out, not_19_out, not_20_out, not_21_out);
  and and_3 (and_3_out, not_22_out, not_23_out, not_24_out, not_25_out, not_26_out, not_27_out, F5, not_28_out, not_29_out, not_30_out, not_31_out, F0);
  and and_4 (and_4_out, not_32_out, not_33_out, not_34_out, not_35_out, not_36_out, not_37_out, F5, not_38_out, not_39_out, F2, not_40_out, not_41_out);
  and and_5 (and_5_out, not_42_out, not_43_out, not_44_out, not_45_out, not_46_out, not_47_out, F5, not_48_out, F3, not_49_out, F1, not_50_out);
  and and_6 (and_6_out, not_51_out, not_52_out, OP3, not_53_out, not_54_out, not_55_out);
  and and_7 (and_7_out, not_56_out, not_57_out, OP3, OP2, not_58_out, not_59_out);
  and and_8 (and_8_out, not_60_out, not_61_out, OP3, not_62_out, not_63_out, OP0);
  and and_9 (and_9_out, not_64_out, not_65_out, OP3, not_66_out, OP1, not_67_out);
  and and_10 (and_10_out, OP5, not_68_out, not_69_out, not_70_out, OP1, OP0);
  and and_11 (and_11_out, OP5, not_71_out, OP3, not_72_out, OP1, OP0);
  and and_12 (and_12_out, OP5, not_73_out, not_74_out, not_75_out, not_76_out, OP0);
  and and_13 (and_13_out, not_77_out, not_78_out, not_79_out, not_80_out, not_81_out, not_82_out, not_83_out, not_84_out, not_85_out, not_86_out, F1, not_87_out);
  and and_14 (and_14_out, not_88_out, not_89_out, not_90_out, not_91_out, not_92_out, not_93_out, F5, not_94_out, not_95_out, not_96_out, F1, not_97_out);
  and and_15 (and_15_out, not_98_out, not_99_out, not_100_out, not_101_out, not_102_out, not_103_out, F5, not_104_out, not_105_out, F2, not_106_out, not_107_out);
  and and_16 (and_16_out, not_108_out, not_109_out, not_110_out, not_111_out, not_112_out, not_113_out, F5, not_114_out, not_115_out, F2, F1, F0);
  and and_17 (and_17_out, not_116_out, not_117_out, not_118_out, not_119_out, not_120_out, not_121_out, F5, not_122_out, F3, not_123_out, F1, not_124_out);
  and and_18 (and_18_out, not_125_out, not_126_out, OP3, OP2, not_127_out, not_128_out);
  and and_19 (and_19_out, not_129_out, not_130_out, OP3, not_131_out, OP1, not_132_out);
  and and_20 (and_20_out, not_133_out, not_134_out, not_135_out, not_136_out, not_137_out, not_138_out, not_139_out, not_140_out, not_141_out, F2, F1, not_142_out);
  and and_21 (and_21_out, not_143_out, not_144_out, not_145_out, not_146_out, not_147_out, not_148_out, F5, not_149_out, not_150_out, not_151_out, not_152_out, not_153_out);
  and and_22 (and_22_out, not_154_out, not_155_out, not_156_out, not_157_out, not_158_out, not_159_out, F5, not_160_out, not_161_out, not_162_out, not_163_out, F0);
  and and_23 (and_23_out, not_164_out, not_165_out, not_166_out, not_167_out, not_168_out, not_169_out, F5, not_170_out, not_171_out, not_172_out, F1, not_173_out);
  and and_24 (and_24_out, not_174_out, not_175_out, not_176_out, not_177_out, not_178_out, not_179_out, F5, not_180_out, not_181_out, F2, not_182_out, not_183_out);
  and and_25 (and_25_out, not_184_out, not_185_out, not_186_out, not_187_out, not_188_out, not_189_out, F5, not_190_out, F3, not_191_out, F1, F0);
  and and_26 (and_26_out, not_192_out, not_193_out, OP3, not_194_out, not_195_out, not_196_out);
  and and_27 (and_27_out, not_197_out, not_198_out, OP3, OP2, not_199_out, not_200_out);
  and and_28 (and_28_out, not_201_out, not_202_out, OP3, not_203_out, not_204_out, OP0);
  and and_29 (and_29_out, OP5, not_205_out, not_206_out, not_207_out, OP1, OP0);
  and and_30 (and_30_out, OP5, not_208_out, OP3, not_209_out, OP1, OP0);
  and and_31 (and_31_out, not_210_out, not_211_out, OP3, not_212_out, OP1, OP0);
  and and_32 (and_32_out, OP5, not_213_out, not_214_out, not_215_out, not_216_out, OP0);
  and and_33 (and_33_out, not_217_out, not_218_out, not_219_out, not_220_out, not_221_out, not_222_out, F5, not_223_out, not_224_out, F2, not_225_out, F0);
  and and_34 (and_34_out, not_226_out, not_227_out, not_228_out, not_229_out, not_230_out, not_231_out, F5, not_232_out, not_233_out, F2, F1, F0);
  and and_35 (and_35_out, not_234_out, not_235_out, not_236_out, not_237_out, not_238_out, not_239_out, F5, not_240_out, F3, not_241_out, F1, not_242_out);
  and and_36 (and_36_out, not_243_out, not_244_out, not_245_out, not_246_out, not_247_out, not_248_out, F5, not_249_out, F3, not_250_out, F1, F0);
  and and_37 (and_37_out, not_251_out, not_252_out, OP3, not_253_out, OP1, not_254_out);
  and and_38 (and_38_out, not_255_out, not_256_out, OP3, OP2, not_257_out, OP0);
  and and_39 (and_39_out, not_258_out, not_259_out, OP3, not_260_out, OP1, OP0);
  and and_40 (and_40_out, not_261_out, not_262_out, not_263_out, not_264_out, not_265_out, not_266_out, F5, not_267_out, not_268_out, F2, not_269_out, F0);
  and and_41 (and_41_out, not_270_out, not_271_out, not_272_out, not_273_out, not_274_out, not_275_out, F5, not_276_out, not_277_out, F2, F1, F0);
  and and_42 (and_42_out, not_278_out, not_279_out, not_280_out, not_281_out, not_282_out, not_283_out, F5, not_284_out, F3, not_285_out, F1, not_286_out);
  and and_43 (and_43_out, not_287_out, not_288_out, not_289_out, not_290_out, not_291_out, not_292_out, F5, not_293_out, F3, not_294_out, F1, F0);
  and and_44 (and_44_out, not_295_out, not_296_out, OP3, not_297_out, OP1, not_298_out);
  and and_45 (and_45_out, not_299_out, not_300_out, OP3, OP2, not_301_out, OP0);
  and and_46 (and_46_out, not_302_out, not_303_out, OP3, not_304_out, OP1, OP0);
  or or_1 (S1, and_13_out, and_14_out, and_15_out, and_16_out, and_17_out, and_18_out, and_19_out, and_20_out);
  or or_2 (S0, and_1_out, and_2_out, and_3_out, and_4_out, and_5_out, and_6_out, and_7_out, and_8_out, and_9_out, and_10_out, and_11_out, and_12_out);
  or or_3 (S2, and_21_out, and_22_out, and_23_out, and_24_out, and_25_out, and_26_out, and_27_out, and_28_out, and_29_out, and_30_out, and_31_out, and_32_out);
  or or_4 (S3, and_33_out, and_34_out, and_35_out, and_36_out, and_37_out, and_38_out, and_39_out, and_40_out, and_41_out, and_42_out, and_43_out, and_44_out, and_45_out, and_46_out);
endmodule

// 控制信号生成
module \控制信号生成  (
  input  OP0,
  input  OP1,
  input  OP2,
  input  OP3,
  input  OP4,
  input  OP5,
  input  F0,
  input  F1,
  input  F2,
  input  F3,
  input  F4,
  input  F5,
  output MemToReg,
  output MemWrite,
  output ALU_SRC,
  output RegWrite,
  output SysCALL,
  output SignedExt,
  output RegDst,
  output BEQ,
  output BNE,
  output JR,
  output JMP,
  output JAL
);

  wire and_1_out, and_2_out, and_4_out, and_5_out, and_6_out, and_7_out, and_8_out, and_9_out, and_10_out,
       and_11_out, and_12_out, and_13_out, and_14_out, and_15_out, and_16_out, and_17_out, and_18_out,
       and_19_out, and_20_out, and_21_out, and_22_out, and_23_out, and_24_out, and_25_out, and_26_out,
       and_27_out, and_28_out, and_29_out, and_30_out, and_31_out, and_32_out, and_33_out, and_35_out,
       and_36_out, and_37_out, and_38_out, and_39_out, and_40_out, and_41_out, and_42_out, and_43_out,
       and_44_out, and_45_out, and_46_out, and_47_out, and_48_out, and_49_out, and_50_out, and_51_out,
       and_52_out, and_53_out, and_57_out, and_58_out, and_59_out, not_1_out, not_2_out, not_3_out,
       not_4_out, not_5_out, not_6_out, not_7_out, not_8_out, not_9_out, not_10_out, not_11_out, not_12_out,
       not_13_out, not_14_out, not_15_out, not_16_out, not_17_out, not_18_out, not_19_out, not_20_out,
       not_21_out, not_22_out, not_23_out, not_24_out, not_25_out, not_26_out, not_27_out, not_28_out,
       not_29_out, not_30_out, not_31_out, not_32_out, not_33_out, not_34_out, not_35_out, not_36_out,
       not_37_out, not_38_out, not_39_out, not_40_out, not_41_out, not_42_out, not_43_out, not_44_out,
       not_45_out, not_46_out, not_47_out, not_48_out, not_49_out, not_50_out, not_51_out, not_52_out,
       not_53_out, not_54_out, not_55_out, not_56_out, not_57_out, not_58_out, not_59_out, not_60_out,
       not_61_out, not_62_out, not_63_out, not_64_out, not_65_out, not_66_out, not_67_out, not_68_out,
       not_69_out, not_70_out, not_71_out, not_72_out, not_73_out, not_74_out, not_75_out, not_76_out,
       not_77_out, not_78_out, not_79_out, not_80_out, not_81_out, not_82_out, not_83_out, not_84_out,
       not_85_out, not_86_out, not_87_out, not_88_out, not_89_out, not_90_out, not_91_out, not_92_out,
       not_93_out, not_94_out, not_95_out, not_96_out, not_97_out, not_98_out, not_99_out, not_100_out,
       not_101_out, not_102_out, not_103_out, not_104_out, not_105_out, not_106_out, not_107_out,
       not_108_out, not_109_out, not_110_out, not_111_out, not_112_out, not_113_out, not_114_out,
       not_115_out, not_116_out, not_117_out, not_118_out, not_119_out, not_120_out, not_121_out,
       not_122_out, not_123_out, not_124_out, not_125_out, not_126_out, not_127_out, not_128_out,
       not_129_out, not_130_out, not_131_out, not_132_out, not_133_out, not_134_out, not_135_out,
       not_136_out, not_137_out, not_138_out, not_139_out, not_140_out, not_141_out, not_142_out,
       not_143_out, not_144_out, not_145_out, not_146_out, not_147_out, not_148_out, not_149_out,
       not_150_out, not_151_out, not_152_out, not_153_out, not_154_out, not_155_out, not_156_out,
       not_157_out, not_158_out, not_159_out, not_160_out, not_161_out, not_162_out, not_163_out,
       not_164_out, not_165_out, not_166_out, not_167_out, not_168_out, not_169_out, not_170_out,
       not_171_out, not_172_out, not_173_out, not_174_out, not_175_out, not_176_out, not_177_out,
       not_178_out, not_179_out, not_180_out, not_181_out, not_182_out, not_183_out, not_184_out,
       not_185_out, not_186_out, not_187_out, not_188_out, not_189_out, not_190_out, not_191_out,
       not_192_out, not_193_out, not_194_out, not_195_out, not_196_out, not_197_out, not_198_out,
       not_199_out, not_200_out, not_201_out, not_202_out, not_203_out, not_204_out, not_205_out,
       not_206_out, not_207_out, not_208_out, not_209_out, not_210_out, not_211_out, not_212_out,
       not_213_out, not_214_out, not_215_out, not_216_out, not_217_out, not_218_out, not_219_out,
       not_220_out, not_221_out, not_222_out, not_223_out, not_224_out, not_225_out, not_226_out,
       not_227_out, not_228_out, not_229_out, not_230_out, not_231_out, not_232_out, not_233_out,
       not_234_out, not_235_out, not_236_out, not_237_out, not_238_out, not_239_out, not_240_out,
       not_241_out, not_242_out, not_243_out, not_244_out, not_245_out, not_246_out, not_247_out,
       not_248_out, not_249_out, not_250_out, not_251_out, not_252_out, not_253_out, not_254_out,
       not_255_out, not_256_out, not_257_out, not_258_out, not_259_out, not_260_out, not_261_out,
       not_262_out, not_263_out, not_264_out, not_265_out, not_266_out, not_267_out, not_268_out,
       not_269_out, not_270_out, not_271_out, not_272_out, not_273_out, not_274_out, not_275_out,
       not_276_out, not_277_out, not_278_out, not_279_out, not_280_out, not_281_out, not_282_out,
       not_283_out, not_284_out, not_285_out, not_286_out, not_287_out, not_288_out, not_289_out,
       not_290_out, not_291_out, not_292_out, not_293_out, not_294_out, not_295_out, not_296_out,
       not_297_out, not_298_out, not_299_out, not_300_out, not_301_out, not_302_out, not_303_out,
       not_304_out, not_305_out, not_306_out, not_307_out, not_308_out, not_309_out, not_310_out,
       not_311_out, not_312_out, not_313_out, not_314_out, not_315_out, not_316_out, not_317_out,
       not_318_out, not_319_out, not_320_out, not_321_out, not_322_out, not_323_out, not_324_out,
       not_325_out, not_326_out, not_327_out, not_328_out, not_329_out, not_330_out, not_331_out,
       not_332_out, not_333_out, not_334_out, not_335_out, not_336_out, not_337_out, not_338_out,
       not_339_out, not_340_out, not_341_out, not_342_out, not_343_out, not_344_out, not_345_out,
       not_346_out, not_347_out, not_348_out, not_349_out, not_350_out, not_351_out, not_352_out,
       not_353_out, not_354_out, not_355_out, not_356_out, not_357_out, not_358_out, not_359_out,
       not_360_out, not_361_out, not_362_out, not_363_out, not_364_out, not_365_out, not_366_out,
       not_367_out, not_368_out, not_369_out, not_370_out, not_371_out, not_372_out, not_373_out,
       not_374_out, not_375_out, not_376_out, not_377_out, not_378_out, not_379_out, not_380_out,
       not_381_out, not_382_out, not_383_out, not_384_out, not_385_out, not_386_out, not_387_out,
       not_388_out, not_389_out, not_390_out;

  not not_1 (not_1_out, OP4);
  not not_2 (not_2_out, OP3);
  not not_3 (not_3_out, OP2);
  not not_4 (not_4_out, OP4);
  not not_5 (not_5_out, OP3);
  not not_6 (not_6_out, OP2);
  not not_7 (not_7_out, OP1);
  not not_8 (not_8_out, OP4);
  not not_9 (not_9_out, OP2);
  not not_10 (not_10_out, OP5);
  not not_11 (not_11_out, OP4);
  not not_12 (not_12_out, OP2);
  not not_13 (not_13_out, OP1);
  not not_14 (not_14_out, OP0);
  not not_15 (not_15_out, OP5);
  not not_16 (not_16_out, OP4);
  not not_17 (not_17_out, OP1);
  not not_18 (not_18_out, OP0);
  not not_19 (not_19_out, OP5);
  not not_20 (not_20_out, OP4);
  not not_21 (not_21_out, OP2);
  not not_22 (not_22_out, OP1);
  not not_23 (not_23_out, OP5);
  not not_24 (not_24_out, OP4);
  not not_25 (not_25_out, OP2);
  not not_26 (not_26_out, OP0);
  not not_27 (not_27_out, OP5);
  not not_28 (not_28_out, OP4);
  not not_29 (not_29_out, OP1);
  not not_30 (not_30_out, OP4);
  not not_31 (not_31_out, OP3);
  not not_32 (not_32_out, OP2);
  not not_33 (not_33_out, OP4);
  not not_34 (not_34_out, OP2);
  not not_35 (not_35_out, OP5);
  not not_36 (not_36_out, OP4);
  not not_37 (not_37_out, OP2);
  not not_38 (not_38_out, OP4);
  not not_39 (not_39_out, OP3);
  not not_40 (not_40_out, OP2);
  not not_41 (not_41_out, OP1);
  not not_42 (not_42_out, OP5);
  not not_43 (not_43_out, OP4);
  not not_44 (not_44_out, OP3);
  not not_45 (not_45_out, OP2);
  not not_46 (not_46_out, OP1);
  not not_47 (not_47_out, OP0);
  not not_48 (not_48_out, F5);
  not not_49 (not_49_out, F4);
  not not_50 (not_50_out, F3);
  not not_51 (not_51_out, F2);
  not not_52 (not_52_out, F1);
  not not_53 (not_53_out, F0);
  not not_54 (not_54_out, OP5);
  not not_55 (not_55_out, OP4);
  not not_56 (not_56_out, OP3);
  not not_57 (not_57_out, OP2);
  not not_58 (not_58_out, OP1);
  not not_59 (not_59_out, OP0);
  not not_60 (not_60_out, F5);
  not not_61 (not_61_out, F4);
  not not_62 (not_62_out, F3);
  not not_63 (not_63_out, F2);
  not not_64 (not_64_out, OP5);
  not not_65 (not_65_out, OP4);
  not not_66 (not_66_out, OP3);
  not not_67 (not_67_out, OP2);
  not not_68 (not_68_out, OP1);
  not not_69 (not_69_out, OP0);
  not not_70 (not_70_out, F5);
  not not_71 (not_71_out, F4);
  not not_72 (not_72_out, F3);
  not not_73 (not_73_out, F2);
  not not_74 (not_74_out, F0);
  not not_75 (not_75_out, OP5);
  not not_76 (not_76_out, OP4);
  not not_77 (not_77_out, OP3);
  not not_78 (not_78_out, OP2);
  not not_79 (not_79_out, OP1);
  not not_80 (not_80_out, OP0);
  not not_81 (not_81_out, F4);
  not not_82 (not_82_out, F3);
  not not_83 (not_83_out, F2);
  not not_84 (not_84_out, F1);
  not not_85 (not_85_out, F0);
  not not_86 (not_86_out, OP5);
  not not_87 (not_87_out, OP4);
  not not_88 (not_88_out, OP3);
  not not_89 (not_89_out, OP2);
  not not_90 (not_90_out, OP1);
  not not_91 (not_91_out, OP0);
  not not_92 (not_92_out, F4);
  not not_93 (not_93_out, F3);
  not not_94 (not_94_out, F2);
  not not_95 (not_95_out, F1);
  not not_96 (not_96_out, OP5);
  not not_97 (not_97_out, OP4);
  not not_98 (not_98_out, OP3);
  not not_99 (not_99_out, OP2);
  not not_100 (not_100_out, OP1);
  not not_101 (not_101_out, OP0);
  not not_102 (not_102_out, F4);
  not not_103 (not_103_out, F3);
  not not_104 (not_104_out, F2);
  not not_105 (not_105_out, F0);
  not not_106 (not_106_out, OP5);
  not not_107 (not_107_out, OP4);
  not not_108 (not_108_out, OP3);
  not not_109 (not_109_out, OP2);
  not not_110 (not_110_out, OP1);
  not not_111 (not_111_out, OP0);
  not not_112 (not_112_out, F4);
  not not_113 (not_113_out, F3);
  not not_114 (not_114_out, F1);
  not not_115 (not_115_out, F0);
  not not_116 (not_116_out, OP5);
  not not_117 (not_117_out, OP4);
  not not_118 (not_118_out, OP3);
  not not_119 (not_119_out, OP2);
  not not_120 (not_120_out, OP1);
  not not_121 (not_121_out, OP0);
  not not_122 (not_122_out, F4);
  not not_123 (not_123_out, F3);
  not not_124 (not_124_out, F1);
  not not_125 (not_125_out, OP5);
  not not_126 (not_126_out, OP4);
  not not_127 (not_127_out, OP3);
  not not_128 (not_128_out, OP2);
  not not_129 (not_129_out, OP1);
  not not_130 (not_130_out, OP0);
  not not_131 (not_131_out, F4);
  not not_132 (not_132_out, F3);
  not not_133 (not_133_out, OP5);
  not not_134 (not_134_out, OP4);
  not not_135 (not_135_out, OP3);
  not not_136 (not_136_out, OP2);
  not not_137 (not_137_out, OP1);
  not not_138 (not_138_out, OP0);
  not not_139 (not_139_out, F4);
  not not_140 (not_140_out, F2);
  not not_141 (not_141_out, F0);
  not not_142 (not_142_out, OP5);
  not not_143 (not_143_out, OP4);
  not not_144 (not_144_out, OP3);
  not not_145 (not_145_out, OP2);
  not not_146 (not_146_out, OP1);
  not not_147 (not_147_out, OP0);
  not not_148 (not_148_out, F4);
  not not_149 (not_149_out, F2);
  not not_150 (not_150_out, OP5);
  not not_151 (not_151_out, OP4);
  not not_152 (not_152_out, OP3);
  not not_153 (not_153_out, OP2);
  not not_154 (not_154_out, OP5);
  not not_155 (not_155_out, OP4);
  not not_156 (not_156_out, OP2);
  not not_157 (not_157_out, OP1);
  not not_158 (not_158_out, OP0);
  not not_159 (not_159_out, OP5);
  not not_160 (not_160_out, OP4);
  not not_161 (not_161_out, OP1);
  not not_162 (not_162_out, OP0);
  not not_163 (not_163_out, OP5);
  not not_164 (not_164_out, OP4);
  not not_165 (not_165_out, OP2);
  not not_166 (not_166_out, OP1);
  not not_167 (not_167_out, OP5);
  not not_168 (not_168_out, OP4);
  not not_169 (not_169_out, OP2);
  not not_170 (not_170_out, OP0);
  not not_171 (not_171_out, OP5);
  not not_172 (not_172_out, OP4);
  not not_173 (not_173_out, OP1);
  not not_174 (not_174_out, OP4);
  not not_175 (not_175_out, OP3);
  not not_176 (not_176_out, OP2);
  not not_177 (not_177_out, OP5);
  not not_178 (not_178_out, OP4);
  not not_179 (not_179_out, OP3);
  not not_180 (not_180_out, OP2);
  not not_181 (not_181_out, OP1);
  not not_182 (not_182_out, OP0);
  not not_183 (not_183_out, F5);
  not not_184 (not_184_out, F4);
  not not_185 (not_185_out, F3);
  not not_186 (not_186_out, F0);
  not not_187 (not_187_out, OP5);
  not not_188 (not_188_out, OP4);
  not not_189 (not_189_out, OP2);
  not not_190 (not_190_out, OP4);
  not not_191 (not_191_out, OP3);
  not not_192 (not_192_out, OP2);
  not not_193 (not_193_out, OP1);
  not not_194 (not_194_out, OP5);
  not not_195 (not_195_out, OP4);
  not not_196 (not_196_out, OP3);
  not not_197 (not_197_out, OP2);
  not not_198 (not_198_out, OP1);
  not not_199 (not_199_out, OP0);
  not not_200 (not_200_out, F5);
  not not_201 (not_201_out, F4);
  not not_202 (not_202_out, F1);
  not not_203 (not_203_out, F0);
  not not_204 (not_204_out, OP5);
  not not_205 (not_205_out, OP4);
  not not_206 (not_206_out, OP2);
  not not_207 (not_207_out, OP1);
  not not_208 (not_208_out, OP0);
  not not_209 (not_209_out, OP5);
  not not_210 (not_210_out, OP4);
  not not_211 (not_211_out, OP2);
  not not_212 (not_212_out, OP1);
  not not_213 (not_213_out, OP5);
  not not_214 (not_214_out, OP4);
  not not_215 (not_215_out, OP2);
  not not_216 (not_216_out, OP0);
  not not_217 (not_217_out, OP4);
  not not_218 (not_218_out, OP3);
  not not_219 (not_219_out, OP2);
  not not_220 (not_220_out, OP4);
  not not_221 (not_221_out, OP2);
  not not_222 (not_222_out, OP5);
  not not_223 (not_223_out, OP4);
  not not_224 (not_224_out, OP2);
  not not_225 (not_225_out, OP4);
  not not_226 (not_226_out, OP3);
  not not_227 (not_227_out, OP2);
  not not_228 (not_228_out, OP1);
  not not_229 (not_229_out, OP5);
  not not_230 (not_230_out, OP4);
  not not_231 (not_231_out, OP3);
  not not_232 (not_232_out, OP2);
  not not_233 (not_233_out, OP1);
  not not_234 (not_234_out, OP0);
  not not_235 (not_235_out, F5);
  not not_236 (not_236_out, F4);
  not not_237 (not_237_out, F3);
  not not_238 (not_238_out, F2);
  not not_239 (not_239_out, F1);
  not not_240 (not_240_out, F0);
  not not_241 (not_241_out, OP5);
  not not_242 (not_242_out, OP4);
  not not_243 (not_243_out, OP3);
  not not_244 (not_244_out, OP2);
  not not_245 (not_245_out, OP1);
  not not_246 (not_246_out, OP0);
  not not_247 (not_247_out, F5);
  not not_248 (not_248_out, F4);
  not not_249 (not_249_out, F3);
  not not_250 (not_250_out, F2);
  not not_251 (not_251_out, OP5);
  not not_252 (not_252_out, OP4);
  not not_253 (not_253_out, OP3);
  not not_254 (not_254_out, OP2);
  not not_255 (not_255_out, OP1);
  not not_256 (not_256_out, OP0);
  not not_257 (not_257_out, F5);
  not not_258 (not_258_out, F4);
  not not_259 (not_259_out, F3);
  not not_260 (not_260_out, F2);
  not not_261 (not_261_out, F0);
  not not_262 (not_262_out, OP5);
  not not_263 (not_263_out, OP4);
  not not_264 (not_264_out, OP3);
  not not_265 (not_265_out, OP2);
  not not_266 (not_266_out, OP1);
  not not_267 (not_267_out, OP0);
  not not_268 (not_268_out, F4);
  not not_269 (not_269_out, F3);
  not not_270 (not_270_out, F2);
  not not_271 (not_271_out, F1);
  not not_272 (not_272_out, F0);
  not not_273 (not_273_out, OP5);
  not not_274 (not_274_out, OP4);
  not not_275 (not_275_out, OP3);
  not not_276 (not_276_out, OP2);
  not not_277 (not_277_out, OP1);
  not not_278 (not_278_out, OP0);
  not not_279 (not_279_out, F4);
  not not_280 (not_280_out, F3);
  not not_281 (not_281_out, F2);
  not not_282 (not_282_out, F1);
  not not_283 (not_283_out, OP5);
  not not_284 (not_284_out, OP4);
  not not_285 (not_285_out, OP3);
  not not_286 (not_286_out, OP2);
  not not_287 (not_287_out, OP1);
  not not_288 (not_288_out, OP0);
  not not_289 (not_289_out, F4);
  not not_290 (not_290_out, F3);
  not not_291 (not_291_out, F2);
  not not_292 (not_292_out, F0);
  not not_293 (not_293_out, OP5);
  not not_294 (not_294_out, OP4);
  not not_295 (not_295_out, OP3);
  not not_296 (not_296_out, OP2);
  not not_297 (not_297_out, OP1);
  not not_298 (not_298_out, OP0);
  not not_299 (not_299_out, F4);
  not not_300 (not_300_out, F3);
  not not_301 (not_301_out, F1);
  not not_302 (not_302_out, F0);
  not not_303 (not_303_out, OP5);
  not not_304 (not_304_out, OP4);
  not not_305 (not_305_out, OP3);
  not not_306 (not_306_out, OP2);
  not not_307 (not_307_out, OP1);
  not not_308 (not_308_out, OP0);
  not not_309 (not_309_out, F4);
  not not_310 (not_310_out, F3);
  not not_311 (not_311_out, F1);
  not not_312 (not_312_out, OP5);
  not not_313 (not_313_out, OP4);
  not not_314 (not_314_out, OP3);
  not not_315 (not_315_out, OP2);
  not not_316 (not_316_out, OP1);
  not not_317 (not_317_out, OP0);
  not not_318 (not_318_out, F4);
  not not_319 (not_319_out, F3);
  not not_320 (not_320_out, OP5);
  not not_321 (not_321_out, OP4);
  not not_322 (not_322_out, OP3);
  not not_323 (not_323_out, OP2);
  not not_324 (not_324_out, OP1);
  not not_325 (not_325_out, OP0);
  not not_326 (not_326_out, F4);
  not not_327 (not_327_out, F2);
  not not_328 (not_328_out, F0);
  not not_329 (not_329_out, OP5);
  not not_330 (not_330_out, OP4);
  not not_331 (not_331_out, OP3);
  not not_332 (not_332_out, OP2);
  not not_333 (not_333_out, OP1);
  not not_334 (not_334_out, OP0);
  not not_335 (not_335_out, F4);
  not not_336 (not_336_out, F2);
  not not_337 (not_337_out, OP5);
  not not_338 (not_338_out, OP4);
  not not_339 (not_339_out, OP3);
  not not_340 (not_340_out, OP2);
  not not_341 (not_341_out, OP1);
  not not_342 (not_342_out, OP0);
  not not_343 (not_343_out, F5);
  not not_344 (not_344_out, F4);
  not not_345 (not_345_out, F3);
  not not_346 (not_346_out, F0);
  not not_347 (not_347_out, OP5);
  not not_348 (not_348_out, OP4);
  not not_349 (not_349_out, OP3);
  not not_350 (not_350_out, OP1);
  not not_351 (not_351_out, OP0);
  not not_352 (not_352_out, OP5);
  not not_353 (not_353_out, OP4);
  not not_354 (not_354_out, OP3);
  not not_355 (not_355_out, OP1);
  not not_356 (not_356_out, OP5);
  not not_357 (not_357_out, OP4);
  not not_358 (not_358_out, OP3);
  not not_359 (not_359_out, OP2);
  not not_360 (not_360_out, OP1);
  not not_361 (not_361_out, OP0);
  not not_362 (not_362_out, F5);
  not not_363 (not_363_out, F4);
  not not_364 (not_364_out, F2);
  not not_365 (not_365_out, F1);
  not not_366 (not_366_out, F0);
  not not_367 (not_367_out, OP5);
  not not_368 (not_368_out, OP4);
  not not_369 (not_369_out, OP3);
  not not_370 (not_370_out, OP2);
  not not_371 (not_371_out, OP1);
  not not_372 (not_372_out, OP0);
  not not_373 (not_373_out, F5);
  not not_374 (not_374_out, F4);
  not not_375 (not_375_out, F2);
  not not_376 (not_376_out, F1);
  not not_377 (not_377_out, F0);
  not not_378 (not_378_out, OP5);
  not not_379 (not_379_out, OP4);
  not not_380 (not_380_out, OP3);
  not not_381 (not_381_out, OP2);
  not not_382 (not_382_out, OP0);
  not not_383 (not_383_out, OP5);
  not not_384 (not_384_out, OP4);
  not not_385 (not_385_out, OP3);
  not not_386 (not_386_out, OP2);
  not not_387 (not_387_out, OP5);
  not not_388 (not_388_out, OP4);
  not not_389 (not_389_out, OP3);
  not not_390 (not_390_out, OP2);
  and and_1 (and_1_out, OP5, not_1_out, not_2_out, not_3_out, OP1, OP0);
  and and_2 (and_2_out, OP5, not_4_out, not_5_out, not_6_out, not_7_out, OP0);
  and and_3 (MemWrite, OP5, not_8_out, OP3, not_9_out, OP1, OP0);
  and and_4 (and_4_out, not_10_out, not_11_out, OP3, not_12_out, not_13_out, not_14_out);
  and and_5 (and_5_out, not_15_out, not_16_out, OP3, OP2, not_17_out, not_18_out);
  and and_6 (and_6_out, not_19_out, not_20_out, OP3, not_21_out, not_22_out, OP0);
  and and_7 (and_7_out, not_23_out, not_24_out, OP3, not_25_out, OP1, not_26_out);
  and and_8 (and_8_out, not_27_out, not_28_out, OP3, OP2, not_29_out, OP0);
  and and_9 (and_9_out, OP5, not_30_out, not_31_out, not_32_out, OP1, OP0);
  and and_10 (and_10_out, OP5, not_33_out, OP3, not_34_out, OP1, OP0);
  and and_11 (and_11_out, not_35_out, not_36_out, OP3, not_37_out, OP1, OP0);
  and and_12 (and_12_out, OP5, not_38_out, not_39_out, not_40_out, not_41_out, OP0);
  and and_13 (and_13_out, not_42_out, not_43_out, not_44_out, not_45_out, not_46_out, not_47_out, not_48_out, not_49_out, not_50_out, not_51_out, not_52_out, not_53_out);
  and and_14 (and_14_out, not_54_out, not_55_out, not_56_out, not_57_out, not_58_out, not_59_out, not_60_out, not_61_out, not_62_out, not_63_out, F1, F0);
  and and_15 (and_15_out, not_64_out, not_65_out, not_66_out, not_67_out, not_68_out, not_69_out, not_70_out, not_71_out, not_72_out, not_73_out, F1, not_74_out);
  and and_16 (and_16_out, not_75_out, not_76_out, not_77_out, not_78_out, not_79_out, not_80_out, F5, not_81_out, not_82_out, not_83_out, not_84_out, not_85_out);
  and and_17 (and_17_out, not_86_out, not_87_out, not_88_out, not_89_out, not_90_out, not_91_out, F5, not_92_out, not_93_out, not_94_out, not_95_out, F0);
  and and_18 (and_18_out, not_96_out, not_97_out, not_98_out, not_99_out, not_100_out, not_101_out, F5, not_102_out, not_103_out, not_104_out, F1, not_105_out);
  and and_19 (and_19_out, not_106_out, not_107_out, not_108_out, not_109_out, not_110_out, not_111_out, F5, not_112_out, not_113_out, F2, not_114_out, not_115_out);
  and and_20 (and_20_out, not_116_out, not_117_out, not_118_out, not_119_out, not_120_out, not_121_out, F5, not_122_out, not_123_out, F2, not_124_out, F0);
  and and_21 (and_21_out, not_125_out, not_126_out, not_127_out, not_128_out, not_129_out, not_130_out, F5, not_131_out, not_132_out, F2, F1, F0);
  and and_22 (and_22_out, not_133_out, not_134_out, not_135_out, not_136_out, not_137_out, not_138_out, F5, not_139_out, F3, not_140_out, F1, not_141_out);
  and and_23 (and_23_out, not_142_out, not_143_out, not_144_out, not_145_out, not_146_out, not_147_out, F5, not_148_out, F3, not_149_out, F1, F0);
  and and_24 (and_24_out, not_150_out, not_151_out, not_152_out, not_153_out, OP1, OP0);
  and and_25 (and_25_out, not_154_out, not_155_out, OP3, not_156_out, not_157_out, not_158_out);
  and and_26 (and_26_out, not_159_out, not_160_out, OP3, OP2, not_161_out, not_162_out);
  and and_27 (and_27_out, not_163_out, not_164_out, OP3, not_165_out, not_166_out, OP0);
  and and_28 (and_28_out, not_167_out, not_168_out, OP3, not_169_out, OP1, not_170_out);
  and and_29 (and_29_out, not_171_out, not_172_out, OP3, OP2, not_173_out, OP0);
  and and_30 (and_30_out, OP5, not_174_out, not_175_out, not_176_out, OP1, OP0);
  and and_31 (and_31_out, not_177_out, not_178_out, not_179_out, not_180_out, not_181_out, not_182_out, not_183_out, not_184_out, not_185_out, F2, F1, not_186_out);
  and and_32 (and_32_out, not_187_out, not_188_out, OP3, not_189_out, OP1, OP0);
  and and_33 (and_33_out, OP5, not_190_out, not_191_out, not_192_out, not_193_out, OP0);
  and and_34 (SysCALL, not_194_out, not_195_out, not_196_out, not_197_out, not_198_out, not_199_out, not_200_out, not_201_out, F3, F2, not_202_out, not_203_out);
  and and_35 (and_35_out, not_204_out, not_205_out, OP3, not_206_out, not_207_out, not_208_out);
  and and_36 (and_36_out, not_209_out, not_210_out, OP3, not_211_out, not_212_out, OP0);
  and and_37 (and_37_out, not_213_out, not_214_out, OP3, not_215_out, OP1, not_216_out);
  and and_38 (and_38_out, OP5, not_217_out, not_218_out, not_219_out, OP1, OP0);
  and and_39 (and_39_out, OP5, not_220_out, OP3, not_221_out, OP1, OP0);
  and and_40 (and_40_out, not_222_out, not_223_out, OP3, not_224_out, OP1, OP0);
  and and_41 (and_41_out, OP5, not_225_out, not_226_out, not_227_out, not_228_out, OP0);
  and and_42 (and_42_out, not_229_out, not_230_out, not_231_out, not_232_out, not_233_out, not_234_out, not_235_out, not_236_out, not_237_out, not_238_out, not_239_out, not_240_out);
  and and_43 (and_43_out, not_241_out, not_242_out, not_243_out, not_244_out, not_245_out, not_246_out, not_247_out, not_248_out, not_249_out, not_250_out, F1, F0);
  and and_44 (and_44_out, not_251_out, not_252_out, not_253_out, not_254_out, not_255_out, not_256_out, not_257_out, not_258_out, not_259_out, not_260_out, F1, not_261_out);
  and and_45 (and_45_out, not_262_out, not_263_out, not_264_out, not_265_out, not_266_out, not_267_out, F5, not_268_out, not_269_out, not_270_out, not_271_out, not_272_out);
  and and_46 (and_46_out, not_273_out, not_274_out, not_275_out, not_276_out, not_277_out, not_278_out, F5, not_279_out, not_280_out, not_281_out, not_282_out, F0);
  and and_47 (and_47_out, not_283_out, not_284_out, not_285_out, not_286_out, not_287_out, not_288_out, F5, not_289_out, not_290_out, not_291_out, F1, not_292_out);
  and and_48 (and_48_out, not_293_out, not_294_out, not_295_out, not_296_out, not_297_out, not_298_out, F5, not_299_out, not_300_out, F2, not_301_out, not_302_out);
  and and_49 (and_49_out, not_303_out, not_304_out, not_305_out, not_306_out, not_307_out, not_308_out, F5, not_309_out, not_310_out, F2, not_311_out, F0);
  and and_50 (and_50_out, not_312_out, not_313_out, not_314_out, not_315_out, not_316_out, not_317_out, F5, not_318_out, not_319_out, F2, F1, F0);
  and and_51 (and_51_out, not_320_out, not_321_out, not_322_out, not_323_out, not_324_out, not_325_out, F5, not_326_out, F3, not_327_out, F1, not_328_out);
  and and_52 (and_52_out, not_329_out, not_330_out, not_331_out, not_332_out, not_333_out, not_334_out, F5, not_335_out, F3, not_336_out, F1, F0);
  and and_53 (and_53_out, not_337_out, not_338_out, not_339_out, not_340_out, not_341_out, not_342_out, not_343_out, not_344_out, not_345_out, F2, F1, not_346_out);
  and and_54 (BEQ, not_347_out, not_348_out, not_349_out, OP2, not_350_out, not_351_out);
  and and_55 (BNE, not_352_out, not_353_out, not_354_out, OP2, not_355_out, OP0);
  and and_56 (JR, not_356_out, not_357_out, not_358_out, not_359_out, not_360_out, not_361_out, not_362_out, not_363_out, F3, not_364_out, not_365_out, not_366_out);
  and and_57 (and_57_out, not_367_out, not_368_out, not_369_out, not_370_out, not_371_out, not_372_out, not_373_out, not_374_out, F3, not_375_out, not_376_out, not_377_out);
  and and_58 (and_58_out, not_378_out, not_379_out, not_380_out, not_381_out, OP1, not_382_out);
  and and_59 (and_59_out, not_383_out, not_384_out, not_385_out, not_386_out, OP1, OP0);
  and and_60 (JAL, not_387_out, not_388_out, not_389_out, not_390_out, OP1, OP0);
  or or_1 (MemToReg, and_1_out, and_2_out);
  or or_2 (ALU_SRC, and_4_out, and_5_out, and_6_out, and_7_out, and_8_out, and_9_out, and_10_out, and_11_out, and_12_out);
  or or_3 (SignedExt, and_35_out, and_36_out, and_37_out, and_38_out, and_39_out, and_40_out, and_41_out);
  or or_4 (JMP, and_57_out, and_58_out, and_59_out);
  or or_5 (RegWrite, and_13_out, and_14_out, and_15_out, and_16_out, and_17_out, and_18_out, and_19_out, and_20_out, and_21_out, and_22_out, and_23_out, and_24_out, and_25_out, and_26_out, and_27_out, and_28_out, and_29_out, and_30_out, and_31_out, and_32_out, and_33_out);
  or or_6 (RegDst, and_42_out, and_43_out, and_44_out, and_45_out, and_46_out, and_47_out, and_48_out, and_49_out, and_50_out, and_51_out, and_52_out, and_53_out);
endmodule

// ALU
module MIPS_ALU (
  input  [4:0] shamt,
  input  [31:0] X,
  input  [31:0] Y,
  input  [3:0] AluOP,
  output Equal,
  output [31:0] Result,
  output [31:0] Result_2
);

  wire [0:0] comparator_1_lt, comparator_2_lt;
  wire [31:0] adder_1_out, AND_out, divider_1_out, divider_1_rem, multiplier_1_cout, multiplier_1_out,
       NOR_out, OR_out, shifter_1_out, shifter_2_out, shifter_3_out, subtractor_1_out, XOR_out;

  assign AND_out = X & Y;  // AND_Gate AND, 32 bits wide
  assign OR_out = X | Y;  // OR_Gate OR, 32 bits wide
  Shifter #(.width(32)) shifter_1 (.in(Y), .\dist (shamt), .out(shifter_1_out));
  Shifter #(.width(32), .shift("ar")) shifter_2 (.in(Y), .\dist (shamt), .out(shifter_2_out));
  Shifter #(.width(32), .shift("lr")) shifter_3 (.in(Y), .\dist (shamt), .out(shifter_3_out));
  Multiplier #(.width(32)) multiplier_1 (.a(X), .b(Y), .out(multiplier_1_out), .cout(multiplier_1_cout));  // open: cin
  Divider #(.width(32)) divider_1 (.a(X), .b(Y), .out(divider_1_out), .rem(divider_1_rem));  // open: upper
  Adder #(.width(32)) adder_1 (.a(X), .b(Y), .out(adder_1_out));  // open: cin, cout
  Subtractor #(.width(32)) subtractor_1 (.a(X), .b(Y), .out(subtractor_1_out));  // open: bin, bout
  assign XOR_out = X ^ Y;  // XOR_Gate XOR, 32 bits wide
  assign NOR_out = ~(X | Y);  // NOR_Gate NOR, 32 bits wide
  Comparator #(.width(32)) comparator_1 (.a(X), .b(Y), .eq(Equal), .lt(comparator_1_lt[0]));  // open: gt
  Comparator #(.width(32), .mode("unsigned")) comparator_2 (.a(X), .b(Y), .lt(comparator_2_lt[0]));  // open: gt, eq
  Multiplexer #(.select(4), .width(32), .enable("false")) multiplexer_1 (
    .in0(shifter_1_out), .in1(shifter_2_out), .in2(shifter_3_out), .in3(multiplier_1_out),
    .in4(divider_1_out), .in5(adder_1_out), .in6(subtractor_1_out), .in7(AND_out), .in8(OR_out),
    .in9(XOR_out), .in10(NOR_out), .in11({{31{1'b0}}, comparator_1_lt[0]}),
    .in12({{31{1'b0}}, comparator_2_lt[0]}), .in13({32{1'b0}}), .in14({32{1'b0}}), .in15({32{1'b0}}),
    .out(Result), .sel(AluOP));
  Multiplexer #(.select(4), .width(32), .enable("false")) multiplexer_2 (
    .in0({32{1'b0}}), .in1({32{1'b0}}), .in2({32{1'b0}}), .in3(multiplier_1_cout), .in4(divider_1_rem),
    .in5({32{1'b0}}), .in6({32{1'b0}}), .in7({32{1'b0}}), .in8({32{1'b0}}), .in9({32{1'b0}}),
    .in10({32{1'b0}}), .in11({32{1'b0}}), .in12({32{1'b0}}), .in13({32{1'b0}}), .in14({32{1'b0}}),
    .in15({32{1'b0}}), .out(Result_2), .sel(AluOP));

  // Other names for the same wires on the sheet: Result2[31:0] = Result_2; S[3:0] = AluOP

  // Notes on the sheet:
  //   不要改变此引脚区域内容，也不要改变ALU封装形式
  //   输入引脚
  //   输出引脚
endmodule

module MIPS_Regifile (
  input  [31:0] Din,
  input  Clk,
  input  WE,
  input  [4:0] R1_num,
  input  [4:0] W_num,
  input  [4:0] R2_num,
  output [31:0] R1,
  output [31:0] R2
);

  // RegisterFile registerfile_1: pin names not known; wires that end beside it: Din, Clk, WE, W_num, R1_num, R2_num, R1, R2
endmodule

module \理想流水线  (
);

  wire and_1_out, and_2_out, and_3_out, and_4_out, and_5_out, BAC, CLK, comparator_1_eq, comparator_2_eq,
       comparator_2_lt, ex_mem_1_halt_out, ex_mem_1_jal_out, ex_mem_1_lh_out, ex_mem_1_memtoreg_out,
       ex_mem_1_memwrite_out, ex_mem_1_regdst_out, ex_mem_1_regwrite_out, ex_mem_1_syscall_out, Go, Halt,
       id_ex_1_alusrcb_out, id_ex_1_beq_out, id_ex_1_blez_out, id_ex_1_bne_out, id_ex_1_halt_out,
       id_ex_1_jal_out, id_ex_1_lh_out, id_ex_1_memtoreg_out, id_ex_1_memwrite_out, id_ex_1_regdst_out,
       id_ex_1_regwrite_out, id_ex_1_syscall_out, IR1, IR2, IR3, JMP, JR, mem_wb_1_halt_out,
       mem_wb_1_jal_out, mem_wb_1_memtoreg_out, mem_wb_1_regdst_out, mips_alu_1_equal, not_1_out, not_2_out,
       or_1_out, or_2_out, RegW, RST, SignedExt, SRLV, SysC, W1, W2, W3, \硬布线控制器_1_alu_src , \硬布线控制器_1_beq ,
       \硬布线控制器_1_blez , \硬布线控制器_1_bne , \硬布线控制器_1_jal , \硬布线控制器_1_jmp , \硬布线控制器_1_jr , \硬布线控制器_1_lh ,
       \硬布线控制器_1_memtoreg , \硬布线控制器_1_memwrite , \硬布线控制器_1_regdst , \硬布线控制器_1_regwrite , \硬布线控制器_1_srlv ,
       \硬布线控制器_1_syscall ;
  wire [3:0] id_ex_1_aluop_out, \硬布线控制器_1_alu_op ;
  wire [4:0] id_ex_1_shamt_out, multiplexer_5_out, multiplexer_6_out, multiplexer_8_out, multiplexer_12_out,
       multiplexer_14_out;
  wire [15:0] \LoadUse次数 , mips_ram_1_p6, mips_ram_1_p6_2, multiplexer_9_out, \总周期数 , \插入气泡数 , \无条件分支数 ,
       \条件分支成功数 ;
  wire [31:0] adder_2_out, bit_extender_1_out, bit_extender_2_out, bit_extender_3_out, bit_extender_4_out,
       ex_mem_1_alur_out, ex_mem_1_ir_out, ex_mem_1_r2_out, EX_PC, id_ex_1_address_out, id_ex_1_imm_out,
       id_ex_1_ir_out, id_ex_1_r1_out, id_ex_1_r2_out, ID_PC, if_id_1_ir_out, IF_PC, LedData, MEM_PC,
       mem_wb_1_alur_out, mem_wb_1_ir_out, mem_wb_1_memd_out, mips_alu_1_result, mips_regifile_1_r1,
       mips_regifile_1_r2, multiplexer_1_out, multiplexer_2_out, multiplexer_3_out, multiplexer_4_out,
       multiplexer_7_out, multiplexer_10_out, multiplexer_11_out, multiplexer_13_out, PC_q, rom_1_data,
       shifter_1_out, shifter_2_out, WB_PC;

  Button \u_总复位  (.out(RST));
  Button _1 (.out(IR1));
  Button _2 (.out(IR2));
  Button _3 (.out(IR3));
  Button \u_继续运行  (.out(Go));
  LED led_1 (.in(W1));
  LED led_2 (.in(W2));
  LED led_3 (.in(W3));
  Multiplexer #(.width(32), .enable("false")) multiplexer_1 (
    .in0(IF_PC), .in1(adder_2_out), .out(multiplexer_1_out), .sel(BAC));
  Multiplexer #(.width(32), .enable("false")) multiplexer_2 (
    .in0(multiplexer_1_out), .in1(multiplexer_3_out), .out(multiplexer_2_out), .sel(JMP));
  Multiplexer #(.width(32), .enable("false")) multiplexer_3 (
    .in0(id_ex_1_address_out), .in1(id_ex_1_r1_out), .out(multiplexer_3_out), .sel(JR));
  Hex_Digit_Display hex_digit_display_1 (.value(LedData[31:28]));  // open: dp
  or or_1 (or_1_out, Halt, Go);
  Counter #(.width(16), .max('hffff)) counter_1 (
    .count(or_1_out), .Q(\总周期数 ), .clk(CLK), .clr(RST));  // open: load, D, carry
  Register #(.width(32)) PC (.D(multiplexer_2_out), .en(or_1_out), .Q(PC_q), .clk(CLK), .clr(RST));
  Hex_Digit_Display hex_digit_display_2 (.value(LedData[23:20]));  // open: dp
  Hex_Digit_Display hex_digit_display_3 (.value(LedData[27:24]));  // open: dp
  Hex_Digit_Display hex_digit_display_4 (.value(LedData[19:16]));  // open: dp
  Hex_Digit_Display hex_digit_display_5 (.value(LedData[15:12]));  // open: dp
  ROM #(.addrWidth(10), .dataWidth(32)) rom_1 (.addr(PC_q[11:2]), .data(rom_1_data));  // open: sel
  Adder #(.width(32)) adder_1 (.a(PC_q), .b(32'h4), .out(IF_PC));  // open: cin, cout
  Hex_Digit_Display hex_digit_display_6 (.value(LedData[7:4]));  // open: dp
  Hex_Digit_Display hex_digit_display_7 (.value(LedData[11:8]));  // open: dp
  Clock clock_1 (.out(CLK));
  IF_ID if_id_1 (
    .PC_in(IF_PC), .IR_in(rom_1_data), .PC_out(ID_PC), .IR_out(if_id_1_ir_out), .Reset(RST), .CLK(CLK),
    .Enable(Halt));  // open: PCr_in, PCr_out, PC_G_in, PC_G_out, HG_in, HG_out
  Hex_Digit_Display hex_digit_display_8 (.value(LedData[3:0]));  // open: dp
  assign bit_extender_1_out = {{16{1'b0}}, if_id_1_ir_out[15:0]};  // Bit_Extender bit_extender_1
  Multiplexer #(.width(32), .enable("false")) multiplexer_4 (
    .in0(bit_extender_1_out), .in1(bit_extender_2_out), .out(multiplexer_4_out), .sel(SignedExt));
  assign bit_extender_2_out = {{16{if_id_1_ir_out[15]}}, if_id_1_ir_out[15:0]};  // Bit_Extender bit_extender_2
  assign bit_extender_3_out = {{6{if_id_1_ir_out[25]}}, if_id_1_ir_out[25:0]};  // Bit_Extender bit_extender_3
  // Probe on \总周期数 
  // Probe on \无条件分支数 
  // Probe on \条件分支成功数 
  // Probe on \插入气泡数 
  // Probe on \LoadUse次数 
  \硬布线控制器  \u_硬布线控制器_1  (
    .Func(if_id_1_ir_out[5:0]), .OP(if_id_1_ir_out[31:26]), .ALU_OP(\硬布线控制器_1_alu_op ),
    .MemToReg(\硬布线控制器_1_memtoreg ), .MemWrite(\硬布线控制器_1_memwrite ), .ALU_SRC(\硬布线控制器_1_alu_src ),
    .RegWrite(\硬布线控制器_1_regwrite ), .SysCALL(\硬布线控制器_1_syscall ), .SignedExt(SignedExt),
    .RegDst(\硬布线控制器_1_regdst ), .JR(\硬布线控制器_1_jr ), .JMP(\硬布线控制器_1_jmp ), .Beq(\硬布线控制器_1_beq ),
    .JAL(\硬布线控制器_1_jal ), .Bne(\硬布线控制器_1_bne ), .LH(\硬布线控制器_1_lh ), .BLEZ(\硬布线控制器_1_blez ),
    .SRLV(\硬布线控制器_1_srlv ));  // open: ERET, MFC0, MTC0, MF
  Multiplexer #(.width(5), .enable("false")) multiplexer_5 (
    .in0(if_id_1_ir_out[25:21]), .in1(5'b00100), .out(multiplexer_5_out), .sel(\硬布线控制器_1_syscall ));
  Multiplexer #(.width(5), .enable("false")) multiplexer_6 (
    .in0(if_id_1_ir_out[20:16]), .in1(5'b00010), .out(multiplexer_6_out), .sel(\硬布线控制器_1_syscall ));
  Shifter #(.width(32)) shifter_1 (.in(bit_extender_3_out), .\dist (5'b00010), .out(shifter_1_out));
  // Probe on IF_PC[11:0]
  and and_1 (and_1_out, comparator_1_eq, \硬布线控制器_1_syscall );
  not not_1 (not_1_out, comparator_1_eq);
  // Probe on ID_PC[11:0]
  MIPS_Regifile mips_regifile_1 (
    .Din(multiplexer_13_out), .Clk(CLK), .R1(mips_regifile_1_r1), .R2(mips_regifile_1_r2), .WE(RegW),
    .W_num(multiplexer_14_out), .R1_num(multiplexer_5_out), .R2_num(multiplexer_6_out));
  Register #(.width(32)) register_1 (.D(mips_regifile_1_r1), .en(and_1_out), .Q(LedData), .clk(CLK), .clr(RST));
  // Probe on MEM_PC[11:0]
  // Probe on EX_PC[11:0]
  Comparator #(.width(32)) comparator_1 (.a(32'h22), .b(mips_regifile_1_r2), .eq(comparator_1_eq));  // open: gt, lt
  and and_2 (and_2_out, \硬布线控制器_1_syscall , not_1_out);
  // Probe on WB_PC[11:0]
  ID_EX id_ex_1 (
    .BNE_in(\硬布线控制器_1_bne ), .IR_in(if_id_1_ir_out), .MemToReg_in(\硬布线控制器_1_memtoreg ), .PC_in(ID_PC),
    .MemWrite_in(\硬布线控制器_1_memwrite ), .R1_in(mips_regifile_1_r1), .AluSrcB_in(\硬布线控制器_1_alu_src ),
    .R2_in(mips_regifile_1_r2), .RegWrite_in(\硬布线控制器_1_regwrite ), .Imm_in(multiplexer_4_out),
    .JAL_in(\硬布线控制器_1_jal ), .Address_in(shifter_1_out), .RegDst_in(\硬布线控制器_1_regdst ),
    .AluOP_in(\硬布线控制器_1_alu_op ), .Syscall_in(\硬布线控制器_1_syscall ), .Shamt_in(if_id_1_ir_out[10:6]),
    .JMP_in(\硬布线控制器_1_jmp ), .Halt_in(and_2_out), .JR_in(\硬布线控制器_1_jr ), .LH_in(\硬布线控制器_1_lh ),
    .SRLV_in(\硬布线控制器_1_srlv ), .BNE_out(id_ex_1_bne_out), .IR_out(id_ex_1_ir_out),
    .MemToReg_out(id_ex_1_memtoreg_out), .PC_out(EX_PC), .MemWrite_out(id_ex_1_memwrite_out),
    .R1_out(id_ex_1_r1_out), .AluSrcB_out(id_ex_1_alusrcb_out), .R2_out(id_ex_1_r2_out),
    .RegWrite_out(id_ex_1_regwrite_out), .Imm_out(id_ex_1_imm_out), .JAL_out(id_ex_1_jal_out),
    .Address_out(id_ex_1_address_out), .RegDst_out(id_ex_1_regdst_out), .AluOP_out(id_ex_1_aluop_out),
    .Syscall_out(id_ex_1_syscall_out), .Shamt_out(id_ex_1_shamt_out), .JMP_out(JMP),
    .Halt_out(id_ex_1_halt_out), .JR_out(JR), .LH_out(id_ex_1_lh_out), .SRLV_out(SRLV), .Reset(RST),
    .Enable(Halt), .CLK(CLK), .BEQ_in(\硬布线控制器_1_beq ), .BEQ_out(id_ex_1_beq_out), .BLEZ_in(\硬布线控制器_1_blez ),
    .BLEZ_out(id_ex_1_blez_out));  // open: W__in, W__out, PCr_in, PCr_out, HG_in, HG_out, PCG_in, PCG_out, Interrupt_in, Interrupt_out
  Multiplexer #(.width(32), .enable("false")) multiplexer_7 (
    .in0(id_ex_1_r2_out), .in1(id_ex_1_imm_out), .out(multiplexer_7_out), .sel(id_ex_1_alusrcb_out));
  Multiplexer #(.width(5), .enable("false")) multiplexer_8 (
    .in0(id_ex_1_shamt_out), .in1(id_ex_1_r1_out[4:0]), .out(multiplexer_8_out), .sel(SRLV));
  Comparator #(.width(32)) comparator_2 (
    .a(id_ex_1_r1_out), .b({32{1'b0}}), .eq(comparator_2_eq), .lt(comparator_2_lt));  // open: gt
  or or_2 (or_2_out, comparator_2_eq, comparator_2_lt);
  not not_2 (not_2_out, mips_alu_1_equal);
  MIPS_ALU mips_alu_1 (
    .X(id_ex_1_r1_out), .Y(multiplexer_7_out), .AluOP(id_ex_1_aluop_out), .Equal(mips_alu_1_equal),
    .Result(mips_alu_1_result), .shamt(multiplexer_8_out));  // open: Result_2
  Shifter #(.width(32)) shifter_2 (.in(id_ex_1_imm_out), .\dist (5'b00010), .out(shifter_2_out));
  Adder #(.width(32)) adder_2 (.a(shifter_2_out), .b(EX_PC), .out(adder_2_out));  // open: cin, cout
  and and_3 (and_3_out, or_2_out, id_ex_1_blez_out);
  and and_4 (and_4_out, mips_alu_1_equal, id_ex_1_beq_out);
  and and_5 (and_5_out, not_2_out, id_ex_1_bne_out);
  or or_3 (BAC, and_4_out, and_3_out, and_5_out);
  EX_MEM ex_mem_1 (
    .MemToReg_in(id_ex_1_memtoreg_out), .IR_in(id_ex_1_ir_out), .MemWrite_in(id_ex_1_memwrite_out),
    .PC_in(EX_PC), .RegWrite_in(id_ex_1_regwrite_out), .R2_in(id_ex_1_r2_out), .JAL_in(id_ex_1_jal_out),
    .AluR_in(mips_alu_1_result), .RegDst_in(id_ex_1_regdst_out), .Halt_in(id_ex_1_halt_out),
    .Syscall_in(id_ex_1_syscall_out), .LH_in(id_ex_1_lh_out), .MemToReg_out(ex_mem_1_memtoreg_out),
    .IR_out(ex_mem_1_ir_out), .MemWrite_out(ex_mem_1_memwrite_out), .PC_out(MEM_PC),
    .RegWrite_out(ex_mem_1_regwrite_out), .R2_out(ex_mem_1_r2_out), .JAL_out(ex_mem_1_jal_out),
    .AluR_out(ex_mem_1_alur_out), .RegDst_out(ex_mem_1_regdst_out), .Halt_out(ex_mem_1_halt_out),
    .Syscall_out(ex_mem_1_syscall_out), .LH_out(ex_mem_1_lh_out), .Reset(RST), .Enable(Halt), .CLK(CLK));  // open: W__in, W__out, PCr_in, PCr_out, Interrupt_in, Interrupt_out
  Counter #(.width(16), .max('hffff)) counter_2 (
    .count(JMP), .Q(\无条件分支数 ), .clk(CLK), .clr(RST));  // open: load, D, carry
  Multiplexer #(.width(16), .enable("false")) multiplexer_9 (
    .in0(mips_ram_1_p6), .in1(mips_ram_1_p6_2), .out(multiplexer_9_out), .sel(ex_mem_1_alur_out[1]));
  assign bit_extender_4_out = {{16{multiplexer_9_out[15]}}, multiplexer_9_out};  // Bit_Extender bit_extender_4
  Counter #(.width(16), .max('hffff)) counter_3 (
    .count(BAC), .Q(\条件分支成功数 ), .clk(CLK), .clr(RST));  // open: load, D, carry
  // MIPS_RAM mips_ram_1: pin names not known; wires that end beside it: ex_mem_1_alur_out[11:2], ex_mem_1_r2_out, ex_mem_1_memwrite_out, CLK, RST, {mips_ram_1_p6_2, mips_ram_1_p6}, mem_wb_1_ir_out[15:11]
  Multiplexer #(.width(32), .enable("false")) multiplexer_10 (
    .in0({mips_ram_1_p6_2, mips_ram_1_p6}), .in1(bit_extender_4_out), .out(multiplexer_10_out),
    .sel(ex_mem_1_lh_out));
  MEM_WB mem_wb_1 (
    .MemToReg_in(ex_mem_1_memtoreg_out), .IR_in(ex_mem_1_ir_out), .RegWrite_in(ex_mem_1_regwrite_out),
    .PC_in(MEM_PC), .JAL_in(ex_mem_1_jal_out), .MemD_in(multiplexer_10_out), .RegDst_in(ex_mem_1_regdst_out),
    .AluR_in(ex_mem_1_alur_out), .Syscall_in(ex_mem_1_syscall_out), .Halt_in(ex_mem_1_halt_out),
    .MemToReg_out(mem_wb_1_memtoreg_out), .IR_out(mem_wb_1_ir_out), .RegWrite_out(RegW), .PC_out(WB_PC),
    .JAL_out(mem_wb_1_jal_out), .MemD_out(mem_wb_1_memd_out), .RegDst_out(mem_wb_1_regdst_out),
    .AluR_out(mem_wb_1_alur_out), .Syscall_out(SysC), .Halt_out(mem_wb_1_halt_out), .Reset(RST),
    .Enable(Halt), .CLK(CLK));  // open: W__in, W__out, PCr_in, PCr_out, Interrupt_in, Interrupt_out, R2_in, R2_out
  Multiplexer #(.width(32), .enable("false")) multiplexer_11 (
    .in0(mem_wb_1_alur_out), .in1(mem_wb_1_memd_out), .out(multiplexer_11_out), .sel(mem_wb_1_memtoreg_out));
  not not_3 (Halt, mem_wb_1_halt_out);
  Multiplexer #(.width(5), .enable("false")) multiplexer_12 (
    .in0(mem_wb_1_ir_out[20:16]), .in1(mem_wb_1_ir_out[15:11]), .out(multiplexer_12_out),
    .sel(mem_wb_1_regdst_out));
  Multiplexer #(.width(32), .enable("false")) multiplexer_13 (
    .in0(multiplexer_11_out), .in1(WB_PC), .out(multiplexer_13_out), .sel(mem_wb_1_jal_out));
  Multiplexer #(.width(5), .enable("false")) multiplexer_14 (
    .in0(multiplexer_12_out), .in1({5{1'b1}}), .out(multiplexer_14_out), .sel(mem_wb_1_jal_out));

  // Notes on the sheet:
  //   中断源
  //   中断等待指示
  //   数码管输出
  //   指令存储器
  //   contents of rom_1 (hex, n*v repeats v):
  //   20100000 20110001 20120002 20130003 36100000 36310001 36520002 36730003 ae100000 ae110004 ae120008
  //   ae13000c 2002000a 0 0 0 c
  //   指令字
  //   OP
  //   Func
  //   rs
  //   rt
  //   rd
  //   Shamt
  //   JMP
  //   JR
  //   BLEZ
  //   Syscall
  //   $a0
  //   $v0
  //   Beq
  //   Bne
  //   MemToReg
  //   MemWrite
  //   AluOP
  //   AluSrcB
  //   RegWrite
  //   JAL
  //   RegDst
  //   流水调试日志用
  //   rt
  //   rd
  //   Din
  //   W#
endmodule

// 源寄存器使用情况
module \源寄存器使用情况  (
  input  OP0,
  input  OP1,
  input  OP2,
  input  OP3,
  input  OP4,
  input  OP5,
  input  F0,
  input  F1,
  input  F2,
  input  F3,
  input  F4,
  input  F5,
  output R1_Used,
  output R2_Used
);

  wire and_1_out, and_2_out, and_3_out, and_4_out, and_5_out, and_6_out, and_7_out, and_8_out, and_9_out,
       and_10_out, and_11_out, and_12_out, and_13_out, and_14_out, and_15_out, and_16_out, and_17_out,
       and_18_out, and_19_out, and_20_out, and_21_out, and_22_out, and_23_out, and_24_out, and_25_out,
       and_26_out, and_27_out, and_28_out, and_29_out, and_30_out, and_31_out, and_32_out, and_33_out,
       and_34_out, and_35_out, and_36_out, and_37_out, and_38_out, and_39_out, not_1_out, not_2_out,
       not_3_out, not_4_out, not_5_out, not_6_out, not_7_out, not_8_out, not_9_out, not_10_out, not_11_out,
       not_12_out, not_13_out, not_14_out, not_15_out, not_16_out, not_17_out, not_18_out, not_19_out,
       not_20_out, not_21_out, not_22_out, not_23_out, not_24_out, not_25_out, not_26_out, not_27_out,
       not_28_out, not_29_out, not_30_out, not_31_out, not_32_out, not_33_out, not_34_out, not_35_out,
       not_36_out, not_37_out, not_38_out, not_39_out, not_40_out, not_41_out, not_42_out, not_43_out,
       not_44_out, not_45_out, not_46_out, not_47_out, not_48_out, not_49_out, not_50_out, not_51_out,
       not_52_out, not_53_out, not_54_out, not_55_out, not_56_out, not_57_out, not_58_out, not_59_out,
       not_60_out, not_61_out, not_62_out, not_63_out, not_64_out, not_65_out, not_66_out, not_67_out,
       not_68_out, not_69_out, not_70_out, not_71_out, not_72_out, not_73_out, not_74_out, not_75_out,
       not_76_out, not_77_out, not_78_out, not_79_out, not_80_out, not_81_out, not_82_out, not_83_out,
       not_84_out, not_85_out, not_86_out, not_87_out, not_88_out, not_89_out, not_90_out, not_91_out,
       not_92_out, not_93_out, not_94_out, not_95_out, not_96_out, not_97_out, not_98_out, not_99_out,
       not_100_out, not_101_out, not_102_out, not_103_out, not_104_out, not_105_out, not_106_out,
       not_107_out, not_108_out, not_109_out, not_110_out, not_111_out, not_112_out, not_113_out,
       not_114_out, not_115_out, not_116_out, not_117_out, not_118_out, not_119_out, not_120_out,
       not_121_out, not_122_out, not_123_out, not_124_out, not_125_out, not_126_out, not_127_out,
       not_128_out, not_129_out, not_130_out, not_131_out, not_132_out, not_133_out, not_134_out,
       not_135_out, not_136_out, not_137_out, not_138_out, not_139_out, not_140_out, not_141_out,
       not_142_out, not_143_out, not_144_out, not_145_out, not_146_out, not_147_out, not_148_out,
       not_149_out, not_150_out, not_151_out, not_152_out, not_153_out, not_154_out, not_155_out,
       not_156_out, not_157_out, not_158_out, not_159_out, not_160_out, not_161_out, not_162_out,
       not_163_out, not_164_out, not_165_out, not_166_out, not_167_out, not_168_out, not_169_out,
       not_170_out, not_171_out, not_172_out, not_173_out, not_174_out, not_175_out, not_176_out,
       not_177_out, not_178_out, not_179_out, not_180_out, not_181_out, not_182_out, not_183_out,
       not_184_out, not_185_out, not_186_out, not_187_out, not_188_out, not_189_out, not_190_out,
       not_191_out, not_192_out, not_193_out, not_194_out, not_195_out, not_196_out, not_197_out,
       not_198_out, not_199_out, not_200_out, not_201_out, not_202_out, not_203_out, not_204_out,
       not_205_out, not_206_out, not_207_out, not_208_out, not_209_out, not_210_out, not_211_out,
       not_212_out, not_213_out, not_214_out, not_215_out, not_216_out, not_217_out, not_218_out,
       not_219_out, not_220_out, not_221_out, not_222_out, not_223_out, not_224_out, not_225_out,
       not_226_out, not_227_out, not_228_out, not_229_out, not_230_out, not_231_out, not_232_out,
       not_233_out, not_234_out, not_235_out, not_236_out, not_237_out, not_238_out, not_239_out,
       not_240_out, not_241_out, not_242_out, not_243_out, not_244_out, not_245_out, not_246_out,
       not_247_out, not_248_out, not_249_out, not_250_out, not_251_out, not_252_out, not_253_out,
       not_254_out, not_255_out, not_256_out, not_257_out, not_258_out, not_259_out, not_260_out,
       not_261_out, not_262_out, not_263_out, not_264_out, not_265_out, not_266_out, not_267_out,
       not_268_out, not_269_out, not_270_out, not_271_out, not_272_out, not_273_out, not_274_out,
       not_275_out, not_276_out, not_277_out, not_278_out, not_279_out, not_280_out, not_281_out,
       not_282_out, not_283_out, not_284_out, not_285_out, not_286_out, not_287_out, not_288_out,
       not_289_out, not_290_out;

  not not_1 (not_1_out, OP5);
  not not_2 (not_2_out, OP4);
  not not_3 (not_3_out, OP3);
  not not_4 (not_4_out, OP2);
  not not_5 (not_5_out, OP1);
  not not_6 (not_6_out, OP0);
  not not_7 (not_7_out, F4);
  not not_8 (not_8_out, F3);
  not not_9 (not_9_out, F2);
  not not_10 (not_10_out, F1);
  not not_11 (not_11_out, F0);
  not not_12 (not_12_out, OP5);
  not not_13 (not_13_out, OP4);
  not not_14 (not_14_out, OP3);
  not not_15 (not_15_out, OP2);
  not not_16 (not_16_out, OP1);
  not not_17 (not_17_out, OP0);
  not not_18 (not_18_out, F4);
  not not_19 (not_19_out, F3);
  not not_20 (not_20_out, F2);
  not not_21 (not_21_out, F1);
  not not_22 (not_22_out, OP5);
  not not_23 (not_23_out, OP4);
  not not_24 (not_24_out, OP3);
  not not_25 (not_25_out, OP2);
  not not_26 (not_26_out, OP1);
  not not_27 (not_27_out, OP0);
  not not_28 (not_28_out, F4);
  not not_29 (not_29_out, F3);
  not not_30 (not_30_out, F2);
  not not_31 (not_31_out, F0);
  not not_32 (not_32_out, OP5);
  not not_33 (not_33_out, OP4);
  not not_34 (not_34_out, OP3);
  not not_35 (not_35_out, OP2);
  not not_36 (not_36_out, OP1);
  not not_37 (not_37_out, OP0);
  not not_38 (not_38_out, F4);
  not not_39 (not_39_out, F3);
  not not_40 (not_40_out, F1);
  not not_41 (not_41_out, F0);
  not not_42 (not_42_out, OP5);
  not not_43 (not_43_out, OP4);
  not not_44 (not_44_out, OP3);
  not not_45 (not_45_out, OP2);
  not not_46 (not_46_out, OP1);
  not not_47 (not_47_out, OP0);
  not not_48 (not_48_out, F4);
  not not_49 (not_49_out, F3);
  not not_50 (not_50_out, F1);
  not not_51 (not_51_out, OP5);
  not not_52 (not_52_out, OP4);
  not not_53 (not_53_out, OP3);
  not not_54 (not_54_out, OP2);
  not not_55 (not_55_out, OP1);
  not not_56 (not_56_out, OP0);
  not not_57 (not_57_out, F4);
  not not_58 (not_58_out, F3);
  not not_59 (not_59_out, OP5);
  not not_60 (not_60_out, OP4);
  not not_61 (not_61_out, OP3);
  not not_62 (not_62_out, OP2);
  not not_63 (not_63_out, OP1);
  not not_64 (not_64_out, OP0);
  not not_65 (not_65_out, F4);
  not not_66 (not_66_out, F2);
  not not_67 (not_67_out, F0);
  not not_68 (not_68_out, OP5);
  not not_69 (not_69_out, OP4);
  not not_70 (not_70_out, OP3);
  not not_71 (not_71_out, OP2);
  not not_72 (not_72_out, OP1);
  not not_73 (not_73_out, OP0);
  not not_74 (not_74_out, F4);
  not not_75 (not_75_out, F2);
  not not_76 (not_76_out, OP5);
  not not_77 (not_77_out, OP4);
  not not_78 (not_78_out, OP3);
  not not_79 (not_79_out, OP2);
  not not_80 (not_80_out, OP1);
  not not_81 (not_81_out, OP0);
  not not_82 (not_82_out, F5);
  not not_83 (not_83_out, F4);
  not not_84 (not_84_out, F2);
  not not_85 (not_85_out, F1);
  not not_86 (not_86_out, F0);
  not not_87 (not_87_out, OP5);
  not not_88 (not_88_out, OP4);
  not not_89 (not_89_out, OP3);
  not not_90 (not_90_out, OP2);
  not not_91 (not_91_out, OP1);
  not not_92 (not_92_out, OP0);
  not not_93 (not_93_out, F5);
  not not_94 (not_94_out, F4);
  not not_95 (not_95_out, F1);
  not not_96 (not_96_out, F0);
  not not_97 (not_97_out, OP5);
  not not_98 (not_98_out, OP4);
  not not_99 (not_99_out, OP3);
  not not_100 (not_100_out, OP1);
  not not_101 (not_101_out, OP0);
  not not_102 (not_102_out, OP5);
  not not_103 (not_103_out, OP4);
  not not_104 (not_104_out, OP3);
  not not_105 (not_105_out, OP1);
  not not_106 (not_106_out, OP5);
  not not_107 (not_107_out, OP4);
  not not_108 (not_108_out, OP2);
  not not_109 (not_109_out, OP1);
  not not_110 (not_110_out, OP0);
  not not_111 (not_111_out, OP5);
  not not_112 (not_112_out, OP4);
  not not_113 (not_113_out, OP1);
  not not_114 (not_114_out, OP0);
  not not_115 (not_115_out, OP5);
  not not_116 (not_116_out, OP4);
  not not_117 (not_117_out, OP2);
  not not_118 (not_118_out, OP1);
  not not_119 (not_119_out, OP5);
  not not_120 (not_120_out, OP4);
  not not_121 (not_121_out, OP2);
  not not_122 (not_122_out, OP0);
  not not_123 (not_123_out, OP5);
  not not_124 (not_124_out, OP4);
  not not_125 (not_125_out, OP1);
  not not_126 (not_126_out, OP4);
  not not_127 (not_127_out, OP3);
  not not_128 (not_128_out, OP2);
  not not_129 (not_129_out, OP4);
  not not_130 (not_130_out, OP2);
  not not_131 (not_131_out, OP5);
  not not_132 (not_132_out, OP4);
  not not_133 (not_133_out, OP3);
  not not_134 (not_134_out, OP2);
  not not_135 (not_135_out, OP1);
  not not_136 (not_136_out, OP0);
  not not_137 (not_137_out, F5);
  not not_138 (not_138_out, F4);
  not not_139 (not_139_out, F3);
  not not_140 (not_140_out, F0);
  not not_141 (not_141_out, OP5);
  not not_142 (not_142_out, OP4);
  not not_143 (not_143_out, OP2);
  not not_144 (not_144_out, OP4);
  not not_145 (not_145_out, OP3);
  not not_146 (not_146_out, OP2);
  not not_147 (not_147_out, OP1);
  not not_148 (not_148_out, OP5);
  not not_149 (not_149_out, OP4);
  not not_150 (not_150_out, OP3);
  not not_151 (not_151_out, OP0);
  not not_152 (not_152_out, OP5);
  not not_153 (not_153_out, OP4);
  not not_154 (not_154_out, OP3);
  not not_155 (not_155_out, OP2);
  not not_156 (not_156_out, OP1);
  not not_157 (not_157_out, OP0);
  not not_158 (not_158_out, F5);
  not not_159 (not_159_out, F4);
  not not_160 (not_160_out, F3);
  not not_161 (not_161_out, F2);
  not not_162 (not_162_out, F1);
  not not_163 (not_163_out, F0);
  not not_164 (not_164_out, OP5);
  not not_165 (not_165_out, OP4);
  not not_166 (not_166_out, OP3);
  not not_167 (not_167_out, OP2);
  not not_168 (not_168_out, OP1);
  not not_169 (not_169_out, OP0);
  not not_170 (not_170_out, F5);
  not not_171 (not_171_out, F4);
  not not_172 (not_172_out, F3);
  not not_173 (not_173_out, F2);
  not not_174 (not_174_out, OP5);
  not not_175 (not_175_out, OP4);
  not not_176 (not_176_out, OP3);
  not not_177 (not_177_out, OP2);
  not not_178 (not_178_out, OP1);
  not not_179 (not_179_out, OP0);
  not not_180 (not_180_out, F5);
  not not_181 (not_181_out, F4);
  not not_182 (not_182_out, F3);
  not not_183 (not_183_out, F2);
  not not_184 (not_184_out, F0);
  not not_185 (not_185_out, OP5);
  not not_186 (not_186_out, OP4);
  not not_187 (not_187_out, OP3);
  not not_188 (not_188_out, OP2);
  not not_189 (not_189_out, OP1);
  not not_190 (not_190_out, OP0);
  not not_191 (not_191_out, F4);
  not not_192 (not_192_out, F3);
  not not_193 (not_193_out, F2);
  not not_194 (not_194_out, F1);
  not not_195 (not_195_out, F0);
  not not_196 (not_196_out, OP5);
  not not_197 (not_197_out, OP4);
  not not_198 (not_198_out, OP3);
  not not_199 (not_199_out, OP2);
  not not_200 (not_200_out, OP1);
  not not_201 (not_201_out, OP0);
  not not_202 (not_202_out, F4);
  not not_203 (not_203_out, F3);
  not not_204 (not_204_out, F2);
  not not_205 (not_205_out, F1);
  not not_206 (not_206_out, OP5);
  not not_207 (not_207_out, OP4);
  not not_208 (not_208_out, OP3);
  not not_209 (not_209_out, OP2);
  not not_210 (not_210_out, OP1);
  not not_211 (not_211_out, OP0);
  not not_212 (not_212_out, F4);
  not not_213 (not_213_out, F3);
  not not_214 (not_214_out, F2);
  not not_215 (not_215_out, F0);
  not not_216 (not_216_out, OP5);
  not not_217 (not_217_out, OP4);
  not not_218 (not_218_out, OP3);
  not not_219 (not_219_out, OP2);
  not not_220 (not_220_out, OP1);
  not not_221 (not_221_out, OP0);
  not not_222 (not_222_out, F4);
  not not_223 (not_223_out, F3);
  not not_224 (not_224_out, F1);
  not not_225 (not_225_out, F0);
  not not_226 (not_226_out, OP5);
  not not_227 (not_227_out, OP4);
  not not_228 (not_228_out, OP3);
  not not_229 (not_229_out, OP2);
  not not_230 (not_230_out, OP1);
  not not_231 (not_231_out, OP0);
  not not_232 (not_232_out, F4);
  not not_233 (not_233_out, F3);
  not not_234 (not_234_out, F1);
  not not_235 (not_235_out, OP5);
  not not_236 (not_236_out, OP4);
  not not_237 (not_237_out, OP3);
  not not_238 (not_238_out, OP2);
  not not_239 (not_239_out, OP1);
  not not_240 (not_240_out, OP0);
  not not_241 (not_241_out, F4);
  not not_242 (not_242_out, F3);
  not not_243 (not_243_out, OP5);
  not not_244 (not_244_out, OP4);
  not not_245 (not_245_out, OP3);
  not not_246 (not_246_out, OP2);
  not not_247 (not_247_out, OP1);
  not not_248 (not_248_out, OP0);
  not not_249 (not_249_out, F4);
  not not_250 (not_250_out, F2);
  not not_251 (not_251_out, F0);
  not not_252 (not_252_out, OP5);
  not not_253 (not_253_out, OP4);
  not not_254 (not_254_out, OP3);
  not not_255 (not_255_out, OP2);
  not not_256 (not_256_out, OP1);
  not not_257 (not_257_out, OP0);
  not not_258 (not_258_out, F4);
  not not_259 (not_259_out, F2);
  not not_260 (not_260_out, OP5);
  not not_261 (not_261_out, OP4);
  not not_262 (not_262_out, OP3);
  not not_263 (not_263_out, OP2);
  not not_264 (not_264_out, OP1);
  not not_265 (not_265_out, OP0);
  not not_266 (not_266_out, F5);
  not not_267 (not_267_out, F4);
  not not_268 (not_268_out, F1);
  not not_269 (not_269_out, F0);
  not not_270 (not_270_out, OP5);
  not not_271 (not_271_out, OP4);
  not not_272 (not_272_out, OP3);
  not not_273 (not_273_out, OP1);
  not not_274 (not_274_out, OP0);
  not not_275 (not_275_out, OP5);
  not not_276 (not_276_out, OP4);
  not not_277 (not_277_out, OP3);
  not not_278 (not_278_out, OP1);
  not not_279 (not_279_out, OP4);
  not not_280 (not_280_out, OP2);
  not not_281 (not_281_out, OP5);
  not not_282 (not_282_out, OP4);
  not not_283 (not_283_out, OP3);
  not not_284 (not_284_out, OP2);
  not not_285 (not_285_out, OP1);
  not not_286 (not_286_out, OP0);
  not not_287 (not_287_out, F5);
  not not_288 (not_288_out, F4);
  not not_289 (not_289_out, F3);
  not not_290 (not_290_out, F0);
  and and_1 (and_1_out, not_1_out, not_2_out, not_3_out, not_4_out, not_5_out, not_6_out, F5, not_7_out, not_8_out, not_9_out, not_10_out, not_11_out);
  and and_2 (and_2_out, not_12_out, not_13_out, not_14_out, not_15_out, not_16_out, not_17_out, F5, not_18_out, not_19_out, not_20_out, not_21_out, F0);
  and and_3 (and_3_out, not_22_out, not_23_out, not_24_out, not_25_out, not_26_out, not_27_out, F5, not_28_out, not_29_out, not_30_out, F1, not_31_out);
  and and_4 (and_4_out, not_32_out, not_33_out, not_34_out, not_35_out, not_36_out, not_37_out, F5, not_38_out, not_39_out, F2, not_40_out, not_41_out);
  and and_5 (and_5_out, not_42_out, not_43_out, not_44_out, not_45_out, not_46_out, not_47_out, F5, not_48_out, not_49_out, F2, not_50_out, F0);
  and and_6 (and_6_out, not_51_out, not_52_out, not_53_out, not_54_out, not_55_out, not_56_out, F5, not_57_out, not_58_out, F2, F1, F0);
  and and_7 (and_7_out, not_59_out, not_60_out, not_61_out, not_62_out, not_63_out, not_64_out, F5, not_65_out, F3, not_66_out, F1, not_67_out);
  and and_8 (and_8_out, not_68_out, not_69_out, not_70_out, not_71_out, not_72_out, not_73_out, F5, not_74_out, F3, not_75_out, F1, F0);
  and and_9 (and_9_out, not_76_out, not_77_out, not_78_out, not_79_out, not_80_out, not_81_out, not_82_out, not_83_out, F3, not_84_out, not_85_out, not_86_out);
  and and_10 (and_10_out, not_87_out, not_88_out, not_89_out, not_90_out, not_91_out, not_92_out, not_93_out, not_94_out, F3, F2, not_95_out, not_96_out);
  and and_11 (and_11_out, not_97_out, not_98_out, not_99_out, OP2, not_100_out, not_101_out);
  and and_12 (and_12_out, not_102_out, not_103_out, not_104_out, OP2, not_105_out, OP0);
  and and_13 (and_13_out, not_106_out, not_107_out, OP3, not_108_out, not_109_out, not_110_out);
  and and_14 (and_14_out, not_111_out, not_112_out, OP3, OP2, not_113_out, not_114_out);
  and and_15 (and_15_out, not_115_out, not_116_out, OP3, not_117_out, not_118_out, OP0);
  and and_16 (and_16_out, not_119_out, not_120_out, OP3, not_121_out, OP1, not_122_out);
  and and_17 (and_17_out, not_123_out, not_124_out, OP3, OP2, not_125_out, OP0);
  and and_18 (and_18_out, OP5, not_126_out, not_127_out, not_128_out, OP1, OP0);
  and and_19 (and_19_out, OP5, not_129_out, OP3, not_130_out, OP1, OP0);
  and and_20 (and_20_out, not_131_out, not_132_out, not_133_out, not_134_out, not_135_out, not_136_out, not_137_out, not_138_out, not_139_out, F2, F1, not_140_out);
  and and_21 (and_21_out, not_141_out, not_142_out, OP3, not_143_out, OP1, OP0);
  and and_22 (and_22_out, OP5, not_144_out, not_145_out, not_146_out, not_147_out, OP0);
  and and_23 (and_23_out, not_148_out, not_149_out, not_150_out, OP2, OP1, not_151_out);
  and and_24 (and_24_out, not_152_out, not_153_out, not_154_out, not_155_out, not_156_out, not_157_out, not_158_out, not_159_out, not_160_out, not_161_out, not_162_out, not_163_out);
  and and_25 (and_25_out, not_164_out, not_165_out, not_166_out, not_167_out, not_168_out, not_169_out, not_170_out, not_171_out, not_172_out, not_173_out, F1, F0);
  and and_26 (and_26_out, not_174_out, not_175_out, not_176_out, not_177_out, not_178_out, not_179_out, not_180_out, not_181_out, not_182_out, not_183_out, F1, not_184_out);
  and and_27 (and_27_out, not_185_out, not_186_out, not_187_out, not_188_out, not_189_out, not_190_out, F5, not_191_out, not_192_out, not_193_out, not_194_out, not_195_out);
  and and_28 (and_28_out, not_196_out, not_197_out, not_198_out, not_199_out, not_200_out, not_201_out, F5, not_202_out, not_203_out, not_204_out, not_205_out, F0);
  and and_29 (and_29_out, not_206_out, not_207_out, not_208_out, not_209_out, not_210_out, not_211_out, F5, not_212_out, not_213_out, not_214_out, F1, not_215_out);
  and and_30 (and_30_out, not_216_out, not_217_out, not_218_out, not_219_out, not_220_out, not_221_out, F5, not_222_out, not_223_out, F2, not_224_out, not_225_out);
  and and_31 (and_31_out, not_226_out, not_227_out, not_228_out, not_229_out, not_230_out, not_231_out, F5, not_232_out, not_233_out, F2, not_234_out, F0);
  and and_32 (and_32_out, not_235_out, not_236_out, not_237_out, not_238_out, not_239_out, not_240_out, F5, not_241_out, not_242_out, F2, F1, F0);
  and and_33 (and_33_out, not_243_out, not_244_out, not_245_out, not_246_out, not_247_out, not_248_out, F5, not_249_out, F3, not_250_out, F1, not_251_out);
  and and_34 (and_34_out, not_252_out, not_253_out, not_254_out, not_255_out, not_256_out, not_257_out, F5, not_258_out, F3, not_259_out, F1, F0);
  and and_35 (and_35_out, not_260_out, not_261_out, not_262_out, not_263_out, not_264_out, not_265_out, not_266_out, not_267_out, F3, F2, not_268_out, not_269_out);
  and and_36 (and_36_out, not_270_out, not_271_out, not_272_out, OP2, not_273_out, not_274_out);
  and and_37 (and_37_out, not_275_out, not_276_out, not_277_out, OP2, not_278_out, OP0);
  and and_38 (and_38_out, OP5, not_279_out, OP3, not_280_out, OP1, OP0);
  and and_39 (and_39_out, not_281_out, not_282_out, not_283_out, not_284_out, not_285_out, not_286_out, not_287_out, not_288_out, not_289_out, F2, F1, not_290_out);
  or or_1 (R1_Used, and_1_out, and_2_out, and_3_out, and_4_out, and_5_out, and_6_out, and_7_out, and_8_out, and_9_out, and_10_out, and_11_out, and_12_out, and_13_out, and_14_out, and_15_out, and_16_out, and_17_out, and_18_out, and_19_out, and_20_out, and_21_out, and_22_out, and_23_out);
  or or_2 (R2_Used, and_24_out, and_25_out, and_26_out, and_27_out, and_28_out, and_29_out, and_30_out, and_31_out, and_32_out, and_33_out, and_34_out, and_35_out, and_36_out, and_37_out, and_38_out, and_39_out);
endmodule
// 数据相关检测
module \数据相关检测  (
  input  [5:0] OP,
  input  [4:0] EX_WriteReg_num,
  input  EX_RegWrite,
  input  [5:0] Func,
  input  [4:0] MEM_WriteReg_num,
  input  MEM_RegWrite,
  input  [5:0] EX_OP,
  input  [5:0] MEM_OP,
  input  [4:0] ID_R1_num,
  input  [4:0] ID_R2_num,
  output \数据相关 ,
  output [1:0] R1_Forward,
  output Load_Use,
  output [1:0] R2_Forward
);

  wire and_1_out, and_2_out, and_3_out, and_4_out, and_5_out, and_6_out, and_7_out, and_8_out,
       comparator_1_eq, comparator_2_eq, comparator_3_eq, comparator_4_eq, comparator_5_eq, comparator_6_eq,
       comparator_7_eq, comparator_8_eq, comparator_9_eq, comparator_10_eq, comparator_11_eq,
       comparator_12_eq, not_1_out, not_2_out, not_3_out, not_4_out, or_1_out, or_2_out, or_3_out, or_5_out,
       or_6_out, \源寄存器使用情况_1_r1_used , \源寄存器使用情况_1_r2_used ;
  wire [1:0] priority_encoder_1_out, priority_encoder_2_out;

  \源寄存器使用情况  \u_源寄存器使用情况_1  (
    .OP0(OP[0]), .OP1(OP[1]), .OP2(OP[2]), .OP3(OP[3]), .OP4(OP[4]), .OP5(OP[5]), .F0(Func[0]), .F1(Func[1]),
    .F2(Func[2]), .F3(Func[3]), .F4(Func[4]), .F5(Func[5]), .R1_Used(\源寄存器使用情况_1_r1_used ),
    .R2_Used(\源寄存器使用情况_1_r2_used ));
  Comparator #(.width(5)) comparator_1 (.a(ID_R1_num), .b(EX_WriteReg_num), .eq(comparator_1_eq));  // open: gt, lt
  Comparator #(.width(5)) comparator_2 (.a(EX_WriteReg_num), .b({5{1'b0}}), .eq(comparator_2_eq));  // open: gt, lt
  Comparator #(.width(5)) comparator_3 (.a(ID_R2_num), .b(EX_WriteReg_num), .eq(comparator_3_eq));  // open: gt, lt
  Comparator #(.width(5)) comparator_4 (.a(EX_WriteReg_num), .b({5{1'b0}}), .eq(comparator_4_eq));  // open: gt, lt
  and and_1 (and_1_out, comparator_1_eq, EX_RegWrite, not_1_out);
  not not_1 (not_1_out, comparator_2_eq);
  and and_2 (and_2_out, comparator_3_eq, EX_RegWrite, not_2_out);
  not not_2 (not_2_out, comparator_4_eq);
  Comparator #(.width(5)) comparator_5 (.a(ID_R1_num), .b(MEM_WriteReg_num), .eq(comparator_5_eq));  // open: gt, lt
  not not_3 (not_3_out, comparator_6_eq);
  Comparator #(.width(5)) comparator_6 (.a(MEM_WriteReg_num), .b({5{1'b0}}), .eq(comparator_6_eq));  // open: gt, lt
  Comparator #(.width(5)) comparator_7 (.a(ID_R2_num), .b(MEM_WriteReg_num), .eq(comparator_7_eq));  // open: gt, lt
  not not_4 (not_4_out, comparator_8_eq);
  Comparator #(.width(5)) comparator_8 (.a(MEM_WriteReg_num), .b({5{1'b0}}), .eq(comparator_8_eq));  // open: gt, lt
  and and_3 (and_3_out, comparator_5_eq, MEM_RegWrite, not_3_out);
  and and_4 (and_4_out, comparator_7_eq, MEM_RegWrite, not_4_out);
  Comparator #(.width(6)) comparator_9 (.a(MEM_OP), .b(6'b100011), .eq(comparator_9_eq));  // open: gt, lt
  Comparator #(.width(6)) comparator_10 (.a(MEM_OP), .b(6'b100001), .eq(comparator_10_eq));  // open: gt, lt
  or or_1 (or_1_out, and_3_out, and_1_out);
  and and_5 (and_5_out, or_1_out, \源寄存器使用情况_1_r1_used );
  and and_6 (and_6_out, \源寄存器使用情况_1_r2_used , or_2_out);
  or or_2 (or_2_out, and_2_out, and_4_out);
  Comparator #(.width(6)) comparator_11 (.a(EX_OP), .b(6'b100011), .eq(comparator_11_eq));  // open: gt, lt
  Comparator #(.width(6)) comparator_12 (.a(EX_OP), .b(6'b100001), .eq(comparator_12_eq));  // open: gt, lt
  or or_3 (or_3_out, comparator_9_eq, comparator_10_eq);
  or or_4 (\数据相关 , and_5_out, and_6_out);
  or or_5 (or_5_out, and_1_out, and_2_out);
  or or_6 (or_6_out, comparator_11_eq, comparator_12_eq);
  and and_7 (and_7_out, or_3_out, and_3_out);
  and and_8 (and_8_out, or_3_out, and_4_out);
  Priority_Encoder #(.select(2)) priority_encoder_1 (
    .in0(1'b1), .in1(and_3_out), .in2(and_7_out), .in3(and_1_out), .out(priority_encoder_1_out));  // open: gs, en_out, en_in
  Priority_Encoder #(.select(2)) priority_encoder_2 (
    .in0(1'b1), .in1(and_4_out), .in2(and_8_out), .in3(and_2_out), .out(priority_encoder_2_out));  // open: gs, en_out, en_in
  and and_9 (Load_Use, or_6_out, or_5_out);
  Multiplexer #(.width(2), .enable("false")) multiplexer_1 (
    .in0(priority_encoder_1_out), .in1(2'b00), .out(R1_Forward), .sel(Load_Use));
  Multiplexer #(.width(2), .enable("false")) multiplexer_2 (
    .in0(priority_encoder_2_out), .in1(2'b00), .out(R2_Forward), .sel(Load_Use));

  // Other names for the same wires on the sheet: OP_CODE[5:0] = OP

  // Notes on the sheet:
  //   不管0号寄存器
  //   不管0号寄存器
  //   lw
  //   lh
  //   lw
  //   lh
endmodule

// IF/ID
module IF_ID (
  input  [31:0] PCr_in,
  input  [31:0] PC_in,
  input  [31:0] IR_in,
  input  [31:0] PC_G_in,
  input  [1:0] HG_in,
  input  Reset,
  input  CLK,
  input  Enable,
  output [31:0] PCr_out,
  output [31:0] PC_out,
  output [31:0] IR_out,
  output [31:0] PC_G_out,
  output [1:0] HG_out
);

  wire [1:0] multiplexer_5_out;
  wire [31:0] multiplexer_1_out, multiplexer_2_out, multiplexer_3_out, multiplexer_4_out;

  Multiplexer #(.width(32), .enable("false")) multiplexer_1 (
    .in0(PCr_in), .in1({32{1'b0}}), .out(multiplexer_1_out), .sel(Reset));
  Multiplexer #(.width(32), .enable("false")) multiplexer_2 (
    .in0(PC_in), .in1({32{1'b0}}), .out(multiplexer_2_out), .sel(Reset));
  Multiplexer #(.width(32), .enable("false")) multiplexer_3 (
    .in0(IR_in), .in1({32{1'b0}}), .out(multiplexer_3_out), .sel(Reset));
  Multiplexer #(.width(32), .enable("false")) multiplexer_4 (
    .in0(PC_G_in), .in1({32{1'b0}}), .out(multiplexer_4_out), .sel(Reset));
  Multiplexer #(.width(2), .enable("false")) multiplexer_5 (
    .in0(HG_in), .in1(2'b00), .out(multiplexer_5_out), .sel(Reset));
  Register #(.width(32)) register_1 (.D(multiplexer_1_out), .en(Enable), .Q(PCr_out), .clk(CLK));  // open: clr
  Register #(.width(32)) register_2 (.D(multiplexer_2_out), .en(Enable), .Q(PC_out), .clk(CLK));  // open: clr
  Register #(.width(32)) register_3 (.D(multiplexer_3_out), .en(Enable), .Q(IR_out), .clk(CLK));  // open: clr
  Register #(.width(32)) register_4 (.D(multiplexer_4_out), .en(Enable), .Q(PC_G_out), .clk(CLK));  // open: clr
  Register #(.width(2)) register_5 (.D(multiplexer_5_out), .en(Enable), .Q(HG_out), .clk(CLK));  // open: clr

  // Notes on the sheet:
  //   高电平有效
endmodule

// ID/EX
module ID_EX (
  input  BEQ_in,
  input  [31:0] IR_in,
  input  BNE_in,
  input  [31:0] PC_in,
  input  MemToReg_in,
  input  [31:0] R1_in,
  input  MemWrite_in,
  input  [31:0] R2_in,
  input  AluSrcB_in,
  input  RegWrite_in,
  input  [31:0] Imm_in,
  input  JAL_in,
  input  [31:0] Address_in,
  input  RegDst_in,
  input  [3:0] AluOP_in,
  input  Syscall_in,
  input  [4:0] Shamt_in,
  input  JMP_in,
  input  Halt_in,
  input  JR_in,
  input  LH_in,
  input  BLEZ_in,
  input  SRLV_in,
  input  [4:0] W__in,
  input  [31:0] PCr_in,
  input  [1:0] HG_in,
  input  [31:0] PCG_in,
  input  [2:0] Interrupt_in,
  input  Reset,
  input  Enable,
  input  CLK,
  output BEQ_out,
  output [31:0] IR_out,
  output BNE_out,
  output [31:0] PC_out,
  output MemToReg_out,
  output [31:0] R1_out,
  output MemWrite_out,
  output [31:0] R2_out,
  output AluSrcB_out,
  output RegWrite_out,
  output [31:0] Imm_out,
  output JAL_out,
  output [31:0] Address_out,
  output RegDst_out,
  output [3:0] AluOP_out,
  output Syscall_out,
  output [4:0] Shamt_out,
  output JMP_out,
  output Halt_out,
  output JR_out,
  output LH_out,
  output BLEZ_out,
  output SRLV_out,
  output [4:0] W__out,
  output [31:0] PCr_out,
  output [1:0] HG_out,
  output [31:0] PCG_out,
  output [2:0] Interrupt_out
);

  wire multiplexer_9_out, multiplexer_10_out, multiplexer_11_out, multiplexer_15_out, multiplexer_16_out,
       multiplexer_17_out, multiplexer_18_out, multiplexer_19_out, multiplexer_20_out, multiplexer_21_out,
       multiplexer_22_out, multiplexer_23_out, multiplexer_24_out, multiplexer_25_out, multiplexer_26_out;
  wire [1:0] multiplexer_13_out;
  wire [2:0] multiplexer_14_out;
  wire [3:0] multiplexer_7_out;
  wire [4:0] multiplexer_8_out, multiplexer_12_out;
  wire [31:0] multiplexer_1_out, multiplexer_2_out, multiplexer_3_out, multiplexer_4_out, multiplexer_5_out,
       multiplexer_6_out, multiplexer_27_out, multiplexer_28_out;

  Multiplexer #(.width(32), .enable("false")) multiplexer_1 (
    .in0(IR_in), .in1({32{1'b0}}), .out(multiplexer_1_out), .sel(Reset));
  Multiplexer #(.width(32), .enable("false")) multiplexer_2 (
    .in0(PC_in), .in1({32{1'b0}}), .out(multiplexer_2_out), .sel(Reset));
  Multiplexer #(.width(32), .enable("false")) multiplexer_3 (
    .in0(R1_in), .in1({32{1'b0}}), .out(multiplexer_3_out), .sel(Reset));
  Multiplexer #(.width(32), .enable("false")) multiplexer_4 (
    .in0(R2_in), .in1({32{1'b0}}), .out(multiplexer_4_out), .sel(Reset));
  Multiplexer #(.width(32), .enable("false")) multiplexer_5 (
    .in0(Imm_in), .in1({32{1'b0}}), .out(multiplexer_5_out), .sel(Reset));
  Multiplexer #(.width(32), .enable("false")) multiplexer_6 (
    .in0(Address_in), .in1({32{1'b0}}), .out(multiplexer_6_out), .sel(Reset));
  Multiplexer #(.width(4), .enable("false")) multiplexer_7 (
    .in0(AluOP_in), .in1(4'b0000), .out(multiplexer_7_out), .sel(Reset));
  Multiplexer #(.width(5), .enable("false")) multiplexer_8 (
    .in0(Shamt_in), .in1({5{1'b0}}), .out(multiplexer_8_out), .sel(Reset));
  Multiplexer #(.enable("false")) multiplexer_9 (.in0(Halt_in), .in1(1'b0), .out(multiplexer_9_out), .sel(Reset));
  Multiplexer #(.enable("false")) multiplexer_10 (.in0(LH_in), .in1(1'b0), .out(multiplexer_10_out), .sel(Reset));
  Multiplexer #(.enable("false")) multiplexer_11 (.in0(BLEZ_in), .in1(1'b0), .out(multiplexer_11_out), .sel(Reset));
  Multiplexer #(.width(5), .enable("false")) multiplexer_12 (
    .in0(W__in), .in1({5{1'b0}}), .out(multiplexer_12_out), .sel(Reset));
  Multiplexer #(.width(2), .enable("false")) multiplexer_13 (
    .in0(HG_in), .in1(2'b00), .out(multiplexer_13_out), .sel(Reset));
  Multiplexer #(.width(3), .enable("false")) multiplexer_14 (
    .in0(Interrupt_in), .in1(3'b000), .out(multiplexer_14_out), .sel(Reset));
  Register #(.width(32)) register_1 (.D(multiplexer_1_out), .en(Enable), .Q(IR_out), .clk(CLK));  // open: clr
  Register #(.width(32)) register_2 (.D(multiplexer_2_out), .en(Enable), .Q(PC_out), .clk(CLK));  // open: clr
  Register #(.width(32)) register_3 (.D(multiplexer_3_out), .en(Enable), .Q(R1_out), .clk(CLK));  // open: clr
  Register #(.width(32)) register_4 (.D(multiplexer_4_out), .en(Enable), .Q(R2_out), .clk(CLK));  // open: clr
  Register #(.width(32)) register_5 (.D(multiplexer_5_out), .en(Enable), .Q(Imm_out), .clk(CLK));  // open: clr
  Register #(.width(32)) register_6 (.D(multiplexer_6_out), .en(Enable), .Q(Address_out), .clk(CLK));  // open: clr
  Register #(.width(4)) register_7 (.D(multiplexer_7_out), .en(Enable), .Q(AluOP_out), .clk(CLK));  // open: clr
  Register #(.width(5)) register_8 (.D(multiplexer_8_out), .en(Enable), .Q(Shamt_out), .clk(CLK));  // open: clr
  Register #(.width(1)) register_9 (.D(multiplexer_9_out), .en(Enable), .Q(Halt_out), .clk(CLK));  // open: clr
  Register #(.width(1)) register_10 (.D(multiplexer_10_out), .en(Enable), .Q(LH_out), .clk(CLK));  // open: clr
  Register #(.width(1)) register_11 (.D(multiplexer_11_out), .en(Enable), .Q(BLEZ_out), .clk(CLK));  // open: clr
  Register #(.width(5)) register_12 (.D(multiplexer_12_out), .en(Enable), .Q(W__out), .clk(CLK));  // open: clr
  Register #(.width(2)) register_13 (.D(multiplexer_13_out), .en(Enable), .Q(HG_out), .clk(CLK));  // open: clr
  Register #(.width(3)) register_14 (.D(multiplexer_14_out), .en(Enable), .Q(Interrupt_out), .clk(CLK));  // open: clr
  Multiplexer #(.enable("false")) multiplexer_15 (.in0(BEQ_in), .in1(1'b0), .out(multiplexer_15_out), .sel(Reset));
  Multiplexer #(.enable("false")) multiplexer_16 (.in0(BNE_in), .in1(1'b0), .out(multiplexer_16_out), .sel(Reset));
  Multiplexer #(.enable("false")) multiplexer_17 (.in0(MemToReg_in), .in1(1'b0), .out(multiplexer_17_out), .sel(Reset));
  Multiplexer #(.enable("false")) multiplexer_18 (.in0(MemWrite_in), .in1(1'b0), .out(multiplexer_18_out), .sel(Reset));
  Multiplexer #(.enable("false")) multiplexer_19 (.in0(AluSrcB_in), .in1(1'b0), .out(multiplexer_19_out), .sel(Reset));
  Multiplexer #(.enable("false")) multiplexer_20 (.in0(RegWrite_in), .in1(1'b0), .out(multiplexer_20_out), .sel(Reset));
  Multiplexer #(.enable("false")) multiplexer_21 (.in0(JAL_in), .in1(1'b0), .out(multiplexer_21_out), .sel(Reset));
  Multiplexer #(.enable("false")) multiplexer_22 (.in0(RegDst_in), .in1(1'b0), .out(multiplexer_22_out), .sel(Reset));
  Multiplexer #(.enable("false")) multiplexer_23 (.in0(Syscall_in), .in1(1'b0), .out(multiplexer_23_out), .sel(Reset));
  Multiplexer #(.enable("false")) multiplexer_24 (.in0(JMP_in), .in1(1'b0), .out(multiplexer_24_out), .sel(Reset));
  Multiplexer #(.enable("false")) multiplexer_25 (.in0(JR_in), .in1(1'b0), .out(multiplexer_25_out), .sel(Reset));
  Multiplexer #(.enable("false")) multiplexer_26 (.in0(SRLV_in), .in1(1'b0), .out(multiplexer_26_out), .sel(Reset));
  Multiplexer #(.width(32), .enable("false")) multiplexer_27 (
    .in0(PCr_in), .in1({32{1'b0}}), .out(multiplexer_27_out), .sel(Reset));
  Multiplexer #(.width(32), .enable("false")) multiplexer_28 (
    .in0(PCG_in), .in1({32{1'b0}}), .out(multiplexer_28_out), .sel(Reset));
  Register #(.width(1)) register_15 (.D(multiplexer_15_out), .en(Enable), .Q(BEQ_out), .clk(CLK));  // open: clr
  Register #(.width(1)) register_16 (.D(multiplexer_16_out), .en(Enable), .Q(BNE_out), .clk(CLK));  // open: clr
  Register #(.width(1)) register_17 (.D(multiplexer_17_out), .en(Enable), .Q(MemToReg_out), .clk(CLK));  // open: clr
  Register #(.width(1)) register_18 (.D(multiplexer_18_out), .en(Enable), .Q(MemWrite_out), .clk(CLK));  // open: clr
  Register #(.width(1)) register_19 (.D(multiplexer_19_out), .en(Enable), .Q(AluSrcB_out), .clk(CLK));  // open: clr
  Register #(.width(1)) register_20 (.D(multiplexer_20_out), .en(Enable), .Q(RegWrite_out), .clk(CLK));  // open: clr
  Register #(.width(1)) register_21 (.D(multiplexer_21_out), .en(Enable), .Q(JAL_out), .clk(CLK));  // open: clr
  Register #(.width(1)) register_22 (.D(multiplexer_22_out), .en(Enable), .Q(RegDst_out), .clk(CLK));  // open: clr
  Register #(.width(1)) register_23 (.D(multiplexer_23_out), .en(Enable), .Q(Syscall_out), .clk(CLK));  // open: clr
  Register #(.width(1)) register_24 (.D(multiplexer_24_out), .en(Enable), .Q(JMP_out), .clk(CLK));  // open: clr
  Register #(.width(1)) register_25 (.D(multiplexer_25_out), .en(Enable), .Q(JR_out), .clk(CLK));  // open: clr
  Register #(.width(1)) register_26 (.D(multiplexer_26_out), .en(Enable), .Q(SRLV_out), .clk(CLK));  // open: clr
  Register #(.width(32)) register_27 (.D(multiplexer_27_out), .en(Enable), .Q(PCr_out), .clk(CLK));  // open: clr
  Register #(.width(32)) register_28 (.D(multiplexer_28_out), .en(Enable), .Q(PCG_out), .clk(CLK));  // open: clr
endmodule

// EX/MEM
module EX_MEM (
  input  MemToReg_in,
  input  [31:0] IR_in,
  input  MemWrite_in,
  input  [31:0] PC_in,
  input  RegWrite_in,
  input  [31:0] R2_in,
  input  JAL_in,
  input  [31:0] AluR_in,
  input  RegDst_in,
  input  Halt_in,
  input  Syscall_in,
  input  LH_in,
  input  [31:0] PCr_in,
  input  [4:0] W__in,
  input  [2:0] Interrupt_in,
  input  Reset,
  input  Enable,
  input  CLK,
  output MemToReg_out,
  output [31:0] IR_out,
  output MemWrite_out,
  output [31:0] PC_out,
  output RegWrite_out,
  output [31:0] R2_out,
  output JAL_out,
  output [31:0] AluR_out,
  output RegDst_out,
  output Halt_out,
  output Syscall_out,
  output LH_out,
  output [31:0] PCr_out,
  output [4:0] W__out,
  output [2:0] Interrupt_out
);

  wire multiplexer_5_out, multiplexer_6_out, multiplexer_9_out, multiplexer_10_out, multiplexer_11_out,
       multiplexer_12_out, multiplexer_13_out, multiplexer_14_out;
  wire [2:0] multiplexer_8_out;
  wire [4:0] multiplexer_7_out;
  wire [31:0] multiplexer_1_out, multiplexer_2_out, multiplexer_3_out, multiplexer_4_out, multiplexer_15_out;

  Multiplexer #(.width(32), .enable("false")) multiplexer_1 (
    .in0(IR_in), .in1({32{1'b0}}), .out(multiplexer_1_out), .sel(Reset));
  Multiplexer #(.width(32), .enable("false")) multiplexer_2 (
    .in0(PC_in), .in1({32{1'b0}}), .out(multiplexer_2_out), .sel(Reset));
  Multiplexer #(.width(32), .enable("false")) multiplexer_3 (
    .in0(R2_in), .in1({32{1'b0}}), .out(multiplexer_3_out), .sel(Reset));
  Multiplexer #(.width(32), .enable("false")) multiplexer_4 (
    .in0(AluR_in), .in1({32{1'b0}}), .out(multiplexer_4_out), .sel(Reset));
  Multiplexer #(.enable("false")) multiplexer_5 (.in0(Halt_in), .in1(1'b0), .out(multiplexer_5_out), .sel(Reset));
  Multiplexer #(.enable("false")) multiplexer_6 (.in0(LH_in), .in1(1'b0), .out(multiplexer_6_out), .sel(Reset));
  Multiplexer #(.width(5), .enable("false")) multiplexer_7 (
    .in0(W__in), .in1({5{1'b0}}), .out(multiplexer_7_out), .sel(Reset));
  Multiplexer #(.width(3), .enable("false")) multiplexer_8 (
    .in0(Interrupt_in), .in1(3'b000), .out(multiplexer_8_out), .sel(Reset));
  Register #(.width(32)) register_1 (.D(multiplexer_1_out), .en(Enable), .Q(IR_out), .clk(CLK));  // open: clr
  Register #(.width(32)) register_2 (.D(multiplexer_2_out), .en(Enable), .Q(PC_out), .clk(CLK));  // open: clr
  Register #(.width(32)) register_3 (.D(multiplexer_3_out), .en(Enable), .Q(R2_out), .clk(CLK));  // open: clr
  Register #(.width(32)) register_4 (.D(multiplexer_4_out), .en(Enable), .Q(AluR_out), .clk(CLK));  // open: clr
  Register #(.width(1)) register_5 (.D(multiplexer_5_out), .en(Enable), .Q(Halt_out), .clk(CLK));  // open: clr
  Register #(.width(1)) register_6 (.D(multiplexer_6_out), .en(Enable), .Q(LH_out), .clk(CLK));  // open: clr
  Register #(.width(5)) register_7 (.D(multiplexer_7_out), .en(Enable), .Q(W__out), .clk(CLK));  // open: clr
  Register #(.width(3)) register_8 (.D(multiplexer_8_out), .en(Enable), .Q(Interrupt_out), .clk(CLK));  // open: clr
  Multiplexer #(.enable("false")) multiplexer_9 (.in0(MemToReg_in), .in1(1'b0), .out(multiplexer_9_out), .sel(Reset));
  Multiplexer #(.enable("false")) multiplexer_10 (.in0(MemWrite_in), .in1(1'b0), .out(multiplexer_10_out), .sel(Reset));
  Multiplexer #(.enable("false")) multiplexer_11 (.in0(RegWrite_in), .in1(1'b0), .out(multiplexer_11_out), .sel(Reset));
  Multiplexer #(.enable("false")) multiplexer_12 (.in0(JAL_in), .in1(1'b0), .out(multiplexer_12_out), .sel(Reset));
  Multiplexer #(.enable("false")) multiplexer_13 (.in0(RegDst_in), .in1(1'b0), .out(multiplexer_13_out), .sel(Reset));
  Multiplexer #(.enable("false")) multiplexer_14 (.in0(Syscall_in), .in1(1'b0), .out(multiplexer_14_out), .sel(Reset));
  Multiplexer #(.width(32), .enable("false")) multiplexer_15 (
    .in0(PCr_in), .in1({32{1'b0}}), .out(multiplexer_15_out), .sel(Reset));
  Register #(.width(1)) register_9 (.D(multiplexer_9_out), .en(Enable), .Q(MemToReg_out), .clk(CLK));  // open: clr
  Register #(.width(1)) register_10 (.D(multiplexer_10_out), .en(Enable), .Q(MemWrite_out), .clk(CLK));  // open: clr
  Register #(.width(1)) register_11 (.D(multiplexer_11_out), .en(Enable), .Q(RegWrite_out), .clk(CLK));  // open: clr
  Register #(.width(1)) register_12 (.D(multiplexer_12_out), .en(Enable), .Q(JAL_out), .clk(CLK));  // open: clr
  Register #(.width(1)) register_13 (.D(multiplexer_13_out), .en(Enable), .Q(RegDst_out), .clk(CLK));  // open: clr
  Register #(.width(1)) register_14 (.D(multiplexer_14_out), .en(Enable), .Q(Syscall_out), .clk(CLK));  // open: clr
  Register #(.width(32)) register_15 (.D(multiplexer_15_out), .en(Enable), .Q(PCr_out), .clk(CLK));  // open: clr
endmodule

// MEM/WB
module MEM_WB (
  input  MemToReg_in,
  input  [31:0] IR_in,
  input  RegWrite_in,
  input  [31:0] PC_in,
  input  JAL_in,
  input  [31:0] MemD_in,
  input  RegDst_in,
  input  [31:0] AluR_in,
  input  Syscall_in,
  input  Halt_in,
  input  [4:0] W__in,
  input  [31:0] PCr_in,
  input  [2:0] Interrupt_in,
  input  [31:0] R2_in,
  input  Reset,
  input  Enable,
  input  CLK,
  output MemToReg_out,
  output [31:0] IR_out,
  output RegWrite_out,
  output [31:0] PC_out,
  output JAL_out,
  output [31:0] MemD_out,
  output RegDst_out,
  output [31:0] AluR_out,
  output Syscall_out,
  output Halt_out,
  output [4:0] W__out,
  output [31:0] PCr_out,
  output [2:0] Interrupt_out,
  output [31:0] R2_out
);

  wire multiplexer_5_out, multiplexer_8_out, multiplexer_9_out, multiplexer_10_out, multiplexer_11_out,
       multiplexer_12_out;
  wire [2:0] multiplexer_7_out;
  wire [4:0] multiplexer_6_out;
  wire [31:0] multiplexer_1_out, multiplexer_2_out, multiplexer_3_out, multiplexer_4_out, multiplexer_13_out,
       multiplexer_14_out;

  Multiplexer #(.width(32), .enable("false")) multiplexer_1 (
    .in0(IR_in), .in1({32{1'b0}}), .out(multiplexer_1_out), .sel(Reset));
  Multiplexer #(.width(32), .enable("false")) multiplexer_2 (
    .in0(PC_in), .in1({32{1'b0}}), .out(multiplexer_2_out), .sel(Reset));
  Multiplexer #(.width(32), .enable("false")) multiplexer_3 (
    .in0(MemD_in), .in1({32{1'b0}}), .out(multiplexer_3_out), .sel(Reset));
  Multiplexer #(.width(32), .enable("false")) multiplexer_4 (
    .in0(AluR_in), .in1({32{1'b0}}), .out(multiplexer_4_out), .sel(Reset));
  Multiplexer #(.enable("false")) multiplexer_5 (.in0(Halt_in), .in1(1'b0), .out(multiplexer_5_out), .sel(Reset));
  Multiplexer #(.width(5), .enable("false")) multiplexer_6 (
    .in0(W__in), .in1({5{1'b0}}), .out(multiplexer_6_out), .sel(Reset));
  Multiplexer #(.width(3), .enable("false")) multiplexer_7 (
    .in0(Interrupt_in), .in1(3'b000), .out(multiplexer_7_out), .sel(Reset));
  Register #(.width(32)) register_1 (.D(multiplexer_1_out), .en(Enable), .Q(IR_out), .clk(CLK));  // open: clr
  Register #(.width(32)) register_2 (.D(multiplexer_2_out), .en(Enable), .Q(PC_out), .clk(CLK));  // open: clr
  Register #(.width(32)) register_3 (.D(multiplexer_3_out), .en(Enable), .Q(MemD_out), .clk(CLK));  // open: clr
  Register #(.width(32)) register_4 (.D(multiplexer_4_out), .en(Enable), .Q(AluR_out), .clk(CLK));  // open: clr
  Register #(.width(1)) register_5 (.D(multiplexer_5_out), .en(Enable), .Q(Halt_out), .clk(CLK));  // open: clr
  Register #(.width(5)) register_6 (.D(multiplexer_6_out), .en(Enable), .Q(W__out), .clk(CLK));  // open: clr
  Register #(.width(3)) register_7 (.D(multiplexer_7_out), .en(Enable), .Q(Interrupt_out), .clk(CLK));  // open: clr
  Multiplexer #(.enable("false")) multiplexer_8 (.in0(MemToReg_in), .in1(1'b0), .out(multiplexer_8_out), .sel(Reset));
  Multiplexer #(.enable("false")) multiplexer_9 (.in0(RegWrite_in), .in1(1'b0), .out(multiplexer_9_out), .sel(Reset));
  Multiplexer #(.enable("false")) multiplexer_10 (.in0(JAL_in), .in1(1'b0), .out(multiplexer_10_out), .sel(Reset));
  Multiplexer #(.enable("false")) multiplexer_11 (.in0(RegDst_in), .in1(1'b0), .out(multiplexer_11_out), .sel(Reset));
  Multiplexer #(.enable("false")) multiplexer_12 (.in0(Syscall_in), .in1(1'b0), .out(multiplexer_12_out), .sel(Reset));
  Multiplexer #(.width(32), .enable("false")) multiplexer_13 (
    .in0(PCr_in), .in1({32{1'b0}}), .out(multiplexer_13_out), .sel(Reset));
  Multiplexer #(.width(32), .enable("false")) multiplexer_14 (
    .in0(R2_in), .in1({32{1'b0}}), .out(multiplexer_14_out), .sel(Reset));
  Register #(.width(1)) register_8 (.D(multiplexer_8_out), .en(Enable), .Q(MemToReg_out), .clk(CLK));  // open: clr
  Register #(.width(1)) register_9 (.D(multiplexer_9_out), .en(Enable), .Q(RegWrite_out), .clk(CLK));  // open: clr
  Register #(.width(1)) register_10 (.D(multiplexer_10_out), .en(Enable), .Q(JAL_out), .clk(CLK));  // open: clr
  Register #(.width(1)) register_11 (.D(multiplexer_11_out), .en(Enable), .Q(RegDst_out), .clk(CLK));  // open: clr
  Register #(.width(1)) register_12 (.D(multiplexer_12_out), .en(Enable), .Q(Syscall_out), .clk(CLK));  // open: clr
  Register #(.width(32)) register_13 (.D(multiplexer_13_out), .en(Enable), .Q(PCr_out), .clk(CLK));  // open: clr
  Register #(.width(32)) register_14 (.D(multiplexer_14_out), .en(Enable), .Q(R2_out), .clk(CLK));  // open: clr
endmodule

module \分支相关流水线  (
);

  wire and_1_out, and_2_out, and_3_out, and_4_out, and_5_out, BAC, CLK, comparator_1_eq, comparator_2_eq,
       comparator_2_lt, ex_mem_1_halt_out, ex_mem_1_jal_out, ex_mem_1_lh_out, ex_mem_1_memtoreg_out,
       ex_mem_1_memwrite_out, ex_mem_1_regdst_out, ex_mem_1_regwrite_out, ex_mem_1_syscall_out, Go, Halt,
       id_ex_1_alusrcb_out, id_ex_1_beq_out, id_ex_1_blez_out, id_ex_1_bne_out, id_ex_1_halt_out,
       id_ex_1_jal_out, id_ex_1_lh_out, id_ex_1_memtoreg_out, id_ex_1_memwrite_out, id_ex_1_regdst_out,
       id_ex_1_regwrite_out, id_ex_1_syscall_out, IR1, IR2, IR3, JMP, JR, mem_wb_1_halt_out,
       mem_wb_1_jal_out, mem_wb_1_memtoreg_out, mem_wb_1_regdst_out, mips_alu_1_equal, not_1_out, not_2_out,
       or_1_out, or_2_out, or_3_out, RegW, RST, SignedExt, SRLV, SysC, W1, W2, W3, \硬布线控制器_1_alu_src ,
       \硬布线控制器_1_beq , \硬布线控制器_1_blez , \硬布线控制器_1_bne , \硬布线控制器_1_jal , \硬布线控制器_1_jmp , \硬布线控制器_1_jr ,
       \硬布线控制器_1_lh , \硬布线控制器_1_memtoreg , \硬布线控制器_1_memwrite , \硬布线控制器_1_regdst , \硬布线控制器_1_regwrite ,
       \硬布线控制器_1_srlv , \硬布线控制器_1_syscall ;
  wire [3:0] id_ex_1_aluop_out, \硬布线控制器_1_alu_op ;
  wire [4:0] id_ex_1_shamt_out, multiplexer_5_out, multiplexer_6_out, multiplexer_8_out, multiplexer_12_out,
       multiplexer_14_out;
  wire [15:0] adder_3_out, \LoadUse次数 , mips_ram_1_p6, mips_ram_1_p6_2, multiplexer_9_out, \总周期数 , \插入气泡数 ,
       \无条件分支数 , \条件分支成功数 ;
  wire [31:0] adder_2_out, bit_extender_1_out, bit_extender_2_out, bit_extender_3_out, bit_extender_4_out,
       ex_mem_1_alur_out, ex_mem_1_ir_out, ex_mem_1_r2_out, EX_PC, id_ex_1_address_out, id_ex_1_imm_out,
       id_ex_1_ir_out, id_ex_1_r1_out, id_ex_1_r2_out, ID_PC, if_id_1_ir_out, IF_PC, LedData, MEM_PC,
       mem_wb_1_alur_out, mem_wb_1_ir_out, mem_wb_1_memd_out, mips_alu_1_result, mips_regifile_1_r1,
       mips_regifile_1_r2, multiplexer_1_out, multiplexer_2_out, multiplexer_3_out, multiplexer_4_out,
       multiplexer_7_out, multiplexer_10_out, multiplexer_11_out, multiplexer_13_out, PC_q, rom_1_data,
       shifter_1_out, shifter_2_out, WB_PC;

  Button \u_总复位  (.out(RST));
  Button _1 (.out(IR1));
  Button _2 (.out(IR2));
  Button _3 (.out(IR3));
  Button \u_继续运行  (.out(Go));
  LED led_1 (.in(W1));
  LED led_2 (.in(W2));
  LED led_3 (.in(W3));
  Multiplexer #(.width(32), .enable("false")) multiplexer_1 (
    .in0(IF_PC), .in1(adder_2_out), .out(multiplexer_1_out), .sel(BAC));
  Multiplexer #(.width(32), .enable("false")) multiplexer_2 (
    .in0(multiplexer_1_out), .in1(multiplexer_3_out), .out(multiplexer_2_out), .sel(JMP));
  Multiplexer #(.width(32), .enable("false")) multiplexer_3 (
    .in0(id_ex_1_address_out), .in1(id_ex_1_r1_out), .out(multiplexer_3_out), .sel(JR));
  Hex_Digit_Display hex_digit_display_1 (.value(LedData[31:28]));  // open: dp
  or or_1 (or_1_out, Halt, Go);
  Counter #(.width(16), .max('hffff)) counter_1 (
    .count(or_1_out), .Q(\总周期数 ), .clk(CLK), .clr(RST));  // open: load, D, carry
  Register #(.width(32)) PC (.D(multiplexer_2_out), .en(or_1_out), .Q(PC_q), .clk(CLK), .clr(RST));
  Hex_Digit_Display hex_digit_display_2 (.value(LedData[23:20]));  // open: dp
  Hex_Digit_Display hex_digit_display_3 (.value(LedData[27:24]));  // open: dp
  Hex_Digit_Display hex_digit_display_4 (.value(LedData[15:12]));  // open: dp
  Hex_Digit_Display hex_digit_display_5 (.value(LedData[19:16]));  // open: dp
  ROM #(.addrWidth(10), .dataWidth(32)) rom_1 (.addr(PC_q[11:2]), .data(rom_1_data));  // open: sel
  Adder #(.width(32)) adder_1 (.a(PC_q), .b(32'h4), .out(IF_PC));  // open: cin, cout
  Hex_Digit_Display hex_digit_display_6 (.value(LedData[7:4]));  // open: dp
  Hex_Digit_Display hex_digit_display_7 (.value(LedData[11:8]));  // open: dp
  Clock clock_1 (.out(CLK));
  IF_ID if_id_1 (
    .PC_in(IF_PC), .IR_in(rom_1_data), .PC_out(ID_PC), .IR_out(if_id_1_ir_out), .Reset(or_2_out), .CLK(CLK),
    .Enable(Halt));  // open: PCr_in, PCr_out, PC_G_in, PC_G_out, HG_in, HG_out
  Hex_Digit_Display hex_digit_display_8 (.value(LedData[3:0]));  // open: dp
  assign bit_extender_1_out = {{16{1'b0}}, if_id_1_ir_out[15:0]};  // Bit_Extender bit_extender_1
  Multiplexer #(.width(32), .enable("false")) multiplexer_4 (
    .in0(bit_extender_1_out), .in1(bit_extender_2_out), .out(multiplexer_4_out), .sel(SignedExt));
  assign bit_extender_2_out = {{16{if_id_1_ir_out[15]}}, if_id_1_ir_out[15:0]};  // Bit_Extender bit_extender_2
  assign bit_extender_3_out = {{6{if_id_1_ir_out[25]}}, if_id_1_ir_out[25:0]};  // Bit_Extender bit_extender_3
  // Probe on \总周期数 
  // Probe on \无条件分支数 
  // Probe on \条件分支成功数 
  // Probe on \插入气泡数 
  // Probe on \LoadUse次数 
  \硬布线控制器  \u_硬布线控制器_1  (
    .Func(if_id_1_ir_out[5:0]), .OP(if_id_1_ir_out[31:26]), .ALU_OP(\硬布线控制器_1_alu_op ),
    .MemToReg(\硬布线控制器_1_memtoreg ), .MemWrite(\硬布线控制器_1_memwrite ), .ALU_SRC(\硬布线控制器_1_alu_src ),
    .RegWrite(\硬布线控制器_1_regwrite ), .SysCALL(\硬布线控制器_1_syscall ), .SignedExt(SignedExt),
    .RegDst(\硬布线控制器_1_regdst ), .JR(\硬布线控制器_1_jr ), .JMP(\硬布线控制器_1_jmp ), .Beq(\硬布线控制器_1_beq ),
    .JAL(\硬布线控制器_1_jal ), .Bne(\硬布线控制器_1_bne ), .LH(\硬布线控制器_1_lh ), .BLEZ(\硬布线控制器_1_blez ),
    .SRLV(\硬布线控制器_1_srlv ));  // open: ERET, MFC0, MTC0, MF
  Multiplexer #(.width(5), .enable("false")) multiplexer_5 (
    .in0(if_id_1_ir_out[25:21]), .in1(5'b00100), .out(multiplexer_5_out), .sel(\硬布线控制器_1_syscall ));
  Multiplexer #(.width(5), .enable("false")) multiplexer_6 (
    .in0(if_id_1_ir_out[20:16]), .in1(5'b00010), .out(multiplexer_6_out), .sel(\硬布线控制器_1_syscall ));
  Shifter #(.width(32)) shifter_1 (.in(bit_extender_3_out), .\dist (5'b00010), .out(shifter_1_out));
  // Probe on IF_PC[11:0]
  and and_1 (and_1_out, comparator_1_eq, \硬布线控制器_1_syscall );
  not not_1 (not_1_out, comparator_1_eq);
  // Probe on ID_PC[11:0]
  MIPS_Regifile mips_regifile_1 (
    .Din(multiplexer_13_out), .Clk(CLK), .R1(mips_regifile_1_r1), .R2(mips_regifile_1_r2), .WE(RegW),
    .W_num(multiplexer_14_out), .R1_num(multiplexer_5_out), .R2_num(multiplexer_6_out));
  Register #(.width(32)) register_1 (.D(mips_regifile_1_r1), .en(and_1_out), .Q(LedData), .clk(CLK), .clr(RST));
  // Probe on MEM_PC[11:0]
  // Probe on EX_PC[11:0]
  or or_2 (or_2_out, JMP, RST, BAC);
  Comparator #(.width(32)) comparator_1 (.a(32'h22), .b(mips_regifile_1_r2), .eq(comparator_1_eq));  // open: gt, lt
  and and_2 (and_2_out, \硬布线控制器_1_syscall , not_1_out);
  // Probe on WB_PC[11:0]
  ID_EX id_ex_1 (
    .BNE_in(\硬布线控制器_1_bne ), .IR_in(if_id_1_ir_out), .MemToReg_in(\硬布线控制器_1_memtoreg ), .PC_in(ID_PC),
    .MemWrite_in(\硬布线控制器_1_memwrite ), .R1_in(mips_regifile_1_r1), .AluSrcB_in(\硬布线控制器_1_alu_src ),
    .R2_in(mips_regifile_1_r2), .RegWrite_in(\硬布线控制器_1_regwrite ), .Imm_in(multiplexer_4_out),
    .JAL_in(\硬布线控制器_1_jal ), .Address_in(shifter_1_out), .RegDst_in(\硬布线控制器_1_regdst ),
    .AluOP_in(\硬布线控制器_1_alu_op ), .Syscall_in(\硬布线控制器_1_syscall ), .Shamt_in(if_id_1_ir_out[10:6]),
    .JMP_in(\硬布线控制器_1_jmp ), .Halt_in(and_2_out), .JR_in(\硬布线控制器_1_jr ), .LH_in(\硬布线控制器_1_lh ),
    .SRLV_in(\硬布线控制器_1_srlv ), .BNE_out(id_ex_1_bne_out), .IR_out(id_ex_1_ir_out),
    .MemToReg_out(id_ex_1_memtoreg_out), .PC_out(EX_PC), .MemWrite_out(id_ex_1_memwrite_out),
    .R1_out(id_ex_1_r1_out), .AluSrcB_out(id_ex_1_alusrcb_out), .R2_out(id_ex_1_r2_out),
    .RegWrite_out(id_ex_1_regwrite_out), .Imm_out(id_ex_1_imm_out), .JAL_out(id_ex_1_jal_out),
    .Address_out(id_ex_1_address_out), .RegDst_out(id_ex_1_regdst_out), .AluOP_out(id_ex_1_aluop_out),
    .Syscall_out(id_ex_1_syscall_out), .Shamt_out(id_ex_1_shamt_out), .JMP_out(JMP),
    .Halt_out(id_ex_1_halt_out), .JR_out(JR), .LH_out(id_ex_1_lh_out), .SRLV_out(SRLV), .Reset(or_2_out),
    .Enable(Halt), .CLK(CLK), .BEQ_in(\硬布线控制器_1_beq ), .BEQ_out(id_ex_1_beq_out), .BLEZ_in(\硬布线控制器_1_blez ),
    .BLEZ_out(id_ex_1_blez_out));  // open: W__in, W__out, PCr_in, PCr_out, HG_in, HG_out, PCG_in, PCG_out, Interrupt_in, Interrupt_out
  Multiplexer #(.width(32), .enable("false")) multiplexer_7 (
    .in0(id_ex_1_r2_out), .in1(id_ex_1_imm_out), .out(multiplexer_7_out), .sel(id_ex_1_alusrcb_out));
  Multiplexer #(.width(5), .enable("false")) multiplexer_8 (
    .in0(id_ex_1_shamt_out), .in1(id_ex_1_r1_out[4:0]), .out(multiplexer_8_out), .sel(SRLV));
  Counter #(.width(16), .max('hffff)) counter_2 (
    .count(JMP), .Q(\无条件分支数 ), .clk(CLK), .clr(RST));  // open: load, D, carry
  Comparator #(.width(32)) comparator_2 (
    .a(id_ex_1_r1_out), .b({32{1'b0}}), .eq(comparator_2_eq), .lt(comparator_2_lt));  // open: gt
  or or_3 (or_3_out, comparator_2_eq, comparator_2_lt);
  not not_2 (not_2_out, mips_alu_1_equal);
  MIPS_ALU mips_alu_1 (
    .X(id_ex_1_r1_out), .Y(multiplexer_7_out), .AluOP(id_ex_1_aluop_out), .Equal(mips_alu_1_equal),
    .Result(mips_alu_1_result), .shamt(multiplexer_8_out));  // open: Result_2
  Shifter #(.width(32)) shifter_2 (.in(id_ex_1_imm_out), .\dist (5'b00010), .out(shifter_2_out));
  Adder #(.width(32)) adder_2 (.a(shifter_2_out), .b(EX_PC), .out(adder_2_out));  // open: cin, cout
  and and_3 (and_3_out, or_3_out, id_ex_1_blez_out);
  and and_4 (and_4_out, mips_alu_1_equal, id_ex_1_beq_out);
  and and_5 (and_5_out, not_2_out, id_ex_1_bne_out);
  or or_4 (BAC, and_4_out, and_3_out, and_5_out);
  EX_MEM ex_mem_1 (
    .MemToReg_in(id_ex_1_memtoreg_out), .IR_in(id_ex_1_ir_out), .MemWrite_in(id_ex_1_memwrite_out),
    .PC_in(EX_PC), .RegWrite_in(id_ex_1_regwrite_out), .R2_in(id_ex_1_r2_out), .JAL_in(id_ex_1_jal_out),
    .AluR_in(mips_alu_1_result), .RegDst_in(id_ex_1_regdst_out), .Halt_in(id_ex_1_halt_out),
    .Syscall_in(id_ex_1_syscall_out), .LH_in(id_ex_1_lh_out), .MemToReg_out(ex_mem_1_memtoreg_out),
    .IR_out(ex_mem_1_ir_out), .MemWrite_out(ex_mem_1_memwrite_out), .PC_out(MEM_PC),
    .RegWrite_out(ex_mem_1_regwrite_out), .R2_out(ex_mem_1_r2_out), .JAL_out(ex_mem_1_jal_out),
    .AluR_out(ex_mem_1_alur_out), .RegDst_out(ex_mem_1_regdst_out), .Halt_out(ex_mem_1_halt_out),
    .Syscall_out(ex_mem_1_syscall_out), .LH_out(ex_mem_1_lh_out), .Reset(RST), .Enable(Halt), .CLK(CLK));  // open: W__in, W__out, PCr_in, PCr_out, Interrupt_in, Interrupt_out
  Counter #(.width(16), .max('hffff)) counter_3 (
    .count(BAC), .Q(\条件分支成功数 ), .clk(CLK), .clr(RST));  // open: load, D, carry
  Multiplexer #(.width(16), .enable("false")) multiplexer_9 (
    .in0(mips_ram_1_p6), .in1(mips_ram_1_p6_2), .out(multiplexer_9_out), .sel(ex_mem_1_alur_out[1]));
  assign bit_extender_4_out = {{16{multiplexer_9_out[15]}}, multiplexer_9_out};  // Bit_Extender bit_extender_4
  // MIPS_RAM mips_ram_1: pin names not known; wires that end beside it: ex_mem_1_alur_out[11:2], ex_mem_1_r2_out, ex_mem_1_memwrite_out, CLK, RST, {mips_ram_1_p6_2, mips_ram_1_p6}, mem_wb_1_ir_out[15:11]
  Multiplexer #(.width(32), .enable("false")) multiplexer_10 (
    .in0({mips_ram_1_p6_2, mips_ram_1_p6}), .in1(bit_extender_4_out), .out(multiplexer_10_out),
    .sel(ex_mem_1_lh_out));
  Adder #(.width(16)) adder_3 (.a(\无条件分支数 ), .b(\条件分支成功数 ), .out(adder_3_out));  // open: cin, cout
  Multiplier #(.width(16)) multiplier_1 (.a(adder_3_out), .b(16'h2), .out(\插入气泡数 ));  // open: cin, cout
  MEM_WB mem_wb_1 (
    .MemToReg_in(ex_mem_1_memtoreg_out), .IR_in(ex_mem_1_ir_out), .RegWrite_in(ex_mem_1_regwrite_out),
    .PC_in(MEM_PC), .JAL_in(ex_mem_1_jal_out), .MemD_in(multiplexer_10_out), .RegDst_in(ex_mem_1_regdst_out),
    .AluR_in(ex_mem_1_alur_out), .Syscall_in(ex_mem_1_syscall_out), .Halt_in(ex_mem_1_halt_out),
    .MemToReg_out(mem_wb_1_memtoreg_out), .IR_out(mem_wb_1_ir_out), .RegWrite_out(RegW), .PC_out(WB_PC),
    .JAL_out(mem_wb_1_jal_out), .MemD_out(mem_wb_1_memd_out), .RegDst_out(mem_wb_1_regdst_out),
    .AluR_out(mem_wb_1_alur_out), .Syscall_out(SysC), .Halt_out(mem_wb_1_halt_out), .Reset(RST),
    .Enable(Halt), .CLK(CLK));  // open: W__in, W__out, PCr_in, PCr_out, Interrupt_in, Interrupt_out, R2_in, R2_out
  Multiplexer #(.width(32), .enable("false")) multiplexer_11 (
    .in0(mem_wb_1_alur_out), .in1(mem_wb_1_memd_out), .out(multiplexer_11_out), .sel(mem_wb_1_memtoreg_out));
  not not_3 (Halt, mem_wb_1_halt_out);
  Multiplexer #(.width(5), .enable("false")) multiplexer_12 (
    .in0(mem_wb_1_ir_out[20:16]), .in1(mem_wb_1_ir_out[15:11]), .out(multiplexer_12_out),
    .sel(mem_wb_1_regdst_out));
  Multiplexer #(.width(32), .enable("false")) multiplexer_13 (
    .in0(multiplexer_11_out), .in1(WB_PC), .out(multiplexer_13_out), .sel(mem_wb_1_jal_out));
  Multiplexer #(.width(5), .enable("false")) multiplexer_14 (
    .in0(multiplexer_12_out), .in1({5{1'b1}}), .out(multiplexer_14_out), .sel(mem_wb_1_jal_out));

  // Notes on the sheet:
  //   中断源
  //   中断等待指示
  //   数码管输出
  //   指令存储器
  //   contents of rom_1 (hex, n*v repeats v):
  //   20110020 20020022 8100006 20110004 20120005 20130006 10000003 20110007 20120008 20130009 14110003
  //   2011000a 2012000b 2013000c c100014 2002000a 0 0 0 c 2231ffff 0 0 0 112020 0 0 0 c 1620fff6 3e00008
  //   指令字
  //   OP
  //   Func
  //   rs
  //   rt
  //   rd
  //   Shamt
  //   JMP
  //   JR
  //   BLEZ
  //   Syscall
  //   $a0
  //   $v0
  //   Beq
  //   Bne
  //   MemToReg
  //   MemWrite
  //   AluOP
  //   AluSrcB
  //   RegWrite
  //   JAL
  //   RegDst
  //   流水调试日志用
  //   rt
  //   rd
  //   Din
  //   W#
endmodule

module \气泡流水线  (
);

  wire and_1_out, and_2_out, and_3_out, and_4_out, and_5_out, and_6_out, and_7_out, and_8_out, BAC, CLK,
       comparator_1_eq, comparator_2_eq, comparator_2_lt, ex_mem_1_halt_out, ex_mem_1_jal_out,
       ex_mem_1_lh_out, ex_mem_1_memtoreg_out, ex_mem_1_memwrite_out, ex_mem_1_regdst_out,
       ex_mem_1_syscall_out, EX_RegWrite, Go, Halt, id_ex_1_alusrcb_out, id_ex_1_beq_out, id_ex_1_blez_out,
       id_ex_1_bne_out, id_ex_1_halt_out, id_ex_1_jal_out, id_ex_1_lh_out, id_ex_1_memtoreg_out,
       id_ex_1_memwrite_out, id_ex_1_regdst_out, id_ex_1_syscall_out, IR1, IR2, IR3, JMP, JR, MEM_RegWrite,
       mem_wb_1_halt_out, mem_wb_1_jal_out, mem_wb_1_memtoreg_out, mem_wb_1_regdst_out, mips_alu_1_equal,
       not_1_out, not_2_out, not_3_out, not_4_out, not_5_out, or_1_out, or_2_out, or_3_out, RegW, RST,
       SignedExt, SRLV, SysC, W1, W2, W3, \数据相关 , \硬布线控制器_1_alu_src , \硬布线控制器_1_beq , \硬布线控制器_1_blez ,
       \硬布线控制器_1_bne , \硬布线控制器_1_jal , \硬布线控制器_1_jmp , \硬布线控制器_1_jr , \硬布线控制器_1_lh , \硬布线控制器_1_memtoreg ,
       \硬布线控制器_1_memwrite , \硬布线控制器_1_regdst , \硬布线控制器_1_regwrite , \硬布线控制器_1_srlv , \硬布线控制器_1_syscall ;
  wire [3:0] id_ex_1_aluop_out, \硬布线控制器_1_alu_op ;
  wire [4:0] EX_WriteReg_num, id_ex_1_shamt_out, ID_R1_num, ID_R2_num, MEM_WriteReg_num, multiplexer_4_out,
       multiplexer_8_out, multiplexer_10_out, multiplexer_14_out, multiplexer_16_out;
  wire [5:0] Func, OP;
  wire [15:0] \LoadUse次数 , mips_ram_1_p6, mips_ram_1_p6_2, multiplexer_11_out, \总周期数 , \插入气泡数 , \无条件分支数 ,
       \条件分支成功数 ;
  wire [25:6] if_id_1_ir_out;
  wire [31:0] adder_1_out, adder_2_out, bit_extender_1_out, bit_extender_2_out, bit_extender_3_out,
       bit_extender_4_out, ex_mem_1_alur_out, ex_mem_1_ir_out, ex_mem_1_pc_out, ex_mem_1_r2_out, EX_PC,
       id_ex_1_address_out, id_ex_1_imm_out, id_ex_1_ir_out, id_ex_1_pc_out, id_ex_1_r1_out, id_ex_1_r2_out,
       ID_PC, if_id_1_pc_out, IF_PC, LedData, MEM_PC, mem_wb_1_alur_out, mem_wb_1_ir_out, mem_wb_1_memd_out,
       mem_wb_1_pc_out, mips_alu_1_result, mips_regifile_1_r1, mips_regifile_1_r2, multiplexer_1_out,
       multiplexer_2_out, multiplexer_3_out, multiplexer_5_out, multiplexer_9_out, multiplexer_12_out,
       multiplexer_13_out, multiplexer_15_out, rom_1_data, shifter_1_out, shifter_2_out, WB_PC;

  Button \u_总复位  (.out(RST));
  Button _1 (.out(IR1));
  Button _2 (.out(IR2));
  Button _3 (.out(IR3));
  Button \u_继续运行  (.out(Go));
  LED led_1 (.in(W1));
  LED led_2 (.in(W2));
  LED led_3 (.in(W3));
  not not_1 (not_1_out, \数据相关 );
  and and_1 (and_1_out, not_1_out, Halt);
  Multiplexer #(.width(32), .enable("false")) multiplexer_1 (
    .in0(adder_1_out), .in1(adder_2_out), .out(multiplexer_1_out), .sel(BAC));
  Multiplexer #(.width(32), .enable("false")) multiplexer_2 (
    .in0(multiplexer_1_out), .in1(multiplexer_3_out), .out(multiplexer_2_out), .sel(JMP));
  Multiplexer #(.width(32), .enable("false")) multiplexer_3 (
    .in0(id_ex_1_address_out), .in1(id_ex_1_r1_out), .out(multiplexer_3_out), .sel(JR));
  Hex_Digit_Display hex_digit_display_1 (.value(LedData[31:28]));  // open: dp
  Counter #(.width(16), .max('hffff)) counter_1 (
    .count(Halt), .Q(\总周期数 ), .clk(CLK), .clr(RST));  // open: load, D, carry
  Register #(.width(32)) PC (.D(multiplexer_2_out), .en(and_1_out), .Q(IF_PC), .clk(CLK), .clr(RST));
  Hex_Digit_Display hex_digit_display_2 (.value(LedData[23:20]));  // open: dp
  Hex_Digit_Display hex_digit_display_3 (.value(LedData[27:24]));  // open: dp
  Hex_Digit_Display hex_digit_display_4 (.value(LedData[15:12]));  // open: dp
  Hex_Digit_Display hex_digit_display_5 (.value(LedData[19:16]));  // open: dp
  ROM #(.addrWidth(10), .dataWidth(32)) rom_1 (.addr(IF_PC[11:2]), .data(rom_1_data));  // open: sel
  Adder #(.width(32)) adder_1 (.a(IF_PC), .b(32'h4), .out(adder_1_out));  // open: cin, cout
  not not_2 (not_2_out, \数据相关 );
  and and_2 (and_2_out, not_2_out, Halt);
  Hex_Digit_Display hex_digit_display_6 (.value(LedData[11:8]));  // open: dp
  Hex_Digit_Display hex_digit_display_7 (.value(LedData[7:4]));  // open: dp
  Clock clock_1 (.out(CLK));
  IF_ID if_id_1 (
    .PC_in(adder_1_out), .IR_in(rom_1_data), .PC_out(if_id_1_pc_out), .IR_out({OP, if_id_1_ir_out, Func}),
    .Reset(or_1_out), .CLK(CLK), .Enable(and_2_out), .PCr_in(IF_PC), .PCr_out(ID_PC));  // open: PC_G_in, PC_G_out, HG_in, HG_out
  Hex_Digit_Display hex_digit_display_8 (.value(LedData[3:0]));  // open: dp
  Multiplexer #(.width(5), .enable("false")) multiplexer_4 (
    .in0(if_id_1_ir_out[20:16]), .in1(if_id_1_ir_out[15:11]), .out(multiplexer_4_out), .sel(\硬布线控制器_1_regdst ));
  assign bit_extender_1_out = {{16{1'b0}}, {if_id_1_ir_out[15:6], Func}};  // Bit_Extender bit_extender_1
  Multiplexer #(.width(32), .enable("false")) multiplexer_5 (
    .in0(bit_extender_1_out), .in1(bit_extender_2_out), .out(multiplexer_5_out), .sel(SignedExt));
  assign bit_extender_2_out = {{16{if_id_1_ir_out[15]}}, {if_id_1_ir_out[15:6], Func}};  // Bit_Extender bit_extender_2
  assign bit_extender_3_out = {{6{if_id_1_ir_out[25]}}, {if_id_1_ir_out, Func}};  // Bit_Extender bit_extender_3
  // Probe on \总周期数 
  // Probe on \无条件分支数 
  // Probe on \条件分支成功数 
  // Probe on \插入气泡数 
  // Probe on \LoadUse次数 
  \硬布线控制器  \u_硬布线控制器_1  (
    .Func(Func), .OP(OP), .ALU_OP(\硬布线控制器_1_alu_op ), .MemToReg(\硬布线控制器_1_memtoreg ),
    .MemWrite(\硬布线控制器_1_memwrite ), .ALU_SRC(\硬布线控制器_1_alu_src ), .RegWrite(\硬布线控制器_1_regwrite ),
    .SysCALL(\硬布线控制器_1_syscall ), .SignedExt(SignedExt), .RegDst(\硬布线控制器_1_regdst ), .JR(\硬布线控制器_1_jr ),
    .JMP(\硬布线控制器_1_jmp ), .Beq(\硬布线控制器_1_beq ), .JAL(\硬布线控制器_1_jal ), .Bne(\硬布线控制器_1_bne ),
    .LH(\硬布线控制器_1_lh ), .BLEZ(\硬布线控制器_1_blez ), .SRLV(\硬布线控制器_1_srlv ));  // open: ERET, MFC0, MTC0, MF
  Multiplexer #(.width(5), .enable("false")) multiplexer_6 (
    .in0(if_id_1_ir_out[25:21]), .in1(5'b00100), .out(ID_R1_num), .sel(\硬布线控制器_1_syscall ));
  Multiplexer #(.width(5), .enable("false")) multiplexer_7 (
    .in0(if_id_1_ir_out[20:16]), .in1(5'b00010), .out(ID_R2_num), .sel(\硬布线控制器_1_syscall ));
  Multiplexer #(.width(5), .enable("false")) multiplexer_8 (
    .in0(multiplexer_4_out), .in1({5{1'b1}}), .out(multiplexer_8_out), .sel(\硬布线控制器_1_jal ));
  Shifter #(.width(32)) shifter_1 (.in(bit_extender_3_out), .\dist (5'b00010), .out(shifter_1_out));
  // Probe on IF_PC[11:0]
  and and_3 (and_3_out, comparator_1_eq, \硬布线控制器_1_syscall );
  not not_3 (not_3_out, comparator_1_eq);
  // Probe on ID_PC[11:0]
  MIPS_Regifile mips_regifile_1 (
    .Din(multiplexer_15_out), .Clk(CLK), .R1(mips_regifile_1_r1), .R2(mips_regifile_1_r2), .WE(RegW),
    .W_num(multiplexer_16_out), .R1_num(ID_R1_num), .R2_num(ID_R2_num));
  Register #(.width(32)) register_1 (.D(mips_regifile_1_r1), .en(and_3_out), .Q(LedData), .clk(CLK), .clr(RST));
  // Probe on EX_PC[11:0]
  // Probe on MEM_PC[11:0]
  or or_1 (or_1_out, JMP, RST, BAC);
  Comparator #(.width(32)) comparator_1 (.a(32'h22), .b(mips_regifile_1_r2), .eq(comparator_1_eq));  // open: gt, lt
  and and_4 (and_4_out, \硬布线控制器_1_syscall , not_3_out);
  // Probe on WB_PC[11:0]
  or or_2 (or_2_out, or_1_out, \数据相关 );
  ID_EX id_ex_1 (
    .BNE_in(\硬布线控制器_1_bne ), .IR_in({OP, if_id_1_ir_out, Func}), .MemToReg_in(\硬布线控制器_1_memtoreg ),
    .PC_in(if_id_1_pc_out), .MemWrite_in(\硬布线控制器_1_memwrite ), .R1_in(mips_regifile_1_r1),
    .AluSrcB_in(\硬布线控制器_1_alu_src ), .R2_in(mips_regifile_1_r2), .RegWrite_in(\硬布线控制器_1_regwrite ),
    .Imm_in(multiplexer_5_out), .JAL_in(\硬布线控制器_1_jal ), .Address_in(shifter_1_out),
    .RegDst_in(\硬布线控制器_1_regdst ), .AluOP_in(\硬布线控制器_1_alu_op ), .Syscall_in(\硬布线控制器_1_syscall ),
    .Shamt_in(if_id_1_ir_out[10:6]), .JMP_in(\硬布线控制器_1_jmp ), .Halt_in(and_4_out), .JR_in(\硬布线控制器_1_jr ),
    .LH_in(\硬布线控制器_1_lh ), .SRLV_in(\硬布线控制器_1_srlv ), .BNE_out(id_ex_1_bne_out), .IR_out(id_ex_1_ir_out),
    .MemToReg_out(id_ex_1_memtoreg_out), .PC_out(id_ex_1_pc_out), .MemWrite_out(id_ex_1_memwrite_out),
    .R1_out(id_ex_1_r1_out), .AluSrcB_out(id_ex_1_alusrcb_out), .R2_out(id_ex_1_r2_out),
    .RegWrite_out(EX_RegWrite), .Imm_out(id_ex_1_imm_out), .JAL_out(id_ex_1_jal_out),
    .Address_out(id_ex_1_address_out), .RegDst_out(id_ex_1_regdst_out), .AluOP_out(id_ex_1_aluop_out),
    .Syscall_out(id_ex_1_syscall_out), .Shamt_out(id_ex_1_shamt_out), .JMP_out(JMP),
    .Halt_out(id_ex_1_halt_out), .JR_out(JR), .LH_out(id_ex_1_lh_out), .SRLV_out(SRLV), .Reset(or_2_out),
    .Enable(Halt), .CLK(CLK), .BEQ_in(\硬布线控制器_1_beq ), .BEQ_out(id_ex_1_beq_out), .BLEZ_in(\硬布线控制器_1_blez ),
    .BLEZ_out(id_ex_1_blez_out), .W__in(multiplexer_8_out), .W__out(EX_WriteReg_num), .PCr_in(ID_PC),
    .PCr_out(EX_PC));  // open: HG_in, HG_out, PCG_in, PCG_out, Interrupt_in, Interrupt_out
  Multiplexer #(.width(32), .enable("false")) multiplexer_9 (
    .in0(id_ex_1_r2_out), .in1(id_ex_1_imm_out), .out(multiplexer_9_out), .sel(id_ex_1_alusrcb_out));
  Multiplexer #(.width(5), .enable("false")) multiplexer_10 (
    .in0(id_ex_1_shamt_out), .in1(id_ex_1_r1_out[4:0]), .out(multiplexer_10_out), .sel(SRLV));
  Counter #(.width(16), .max('hffff)) counter_2 (
    .count(JMP), .Q(\无条件分支数 ), .clk(CLK), .clr(RST));  // open: load, D, carry
  Comparator #(.width(32)) comparator_2 (
    .a(id_ex_1_r1_out), .b({32{1'b0}}), .eq(comparator_2_eq), .lt(comparator_2_lt));  // open: gt
  or or_3 (or_3_out, comparator_2_eq, comparator_2_lt);
  not not_4 (not_4_out, mips_alu_1_equal);
  MIPS_ALU mips_alu_1 (
    .X(id_ex_1_r1_out), .Y(multiplexer_9_out), .AluOP(id_ex_1_aluop_out), .Equal(mips_alu_1_equal),
    .Result(mips_alu_1_result), .shamt(multiplexer_10_out));  // open: Result_2
  Shifter #(.width(32)) shifter_2 (.in(id_ex_1_imm_out), .\dist (5'b00010), .out(shifter_2_out));
  Adder #(.width(32)) adder_2 (.a(shifter_2_out), .b(id_ex_1_pc_out), .out(adder_2_out));  // open: cin, cout
  and and_5 (and_5_out, or_3_out, id_ex_1_blez_out);
  and and_6 (and_6_out, mips_alu_1_equal, id_ex_1_beq_out);
  and and_7 (and_7_out, not_4_out, id_ex_1_bne_out);
  or or_4 (BAC, and_6_out, and_5_out, and_7_out);
  EX_MEM ex_mem_1 (
    .MemToReg_in(id_ex_1_memtoreg_out), .IR_in(id_ex_1_ir_out), .MemWrite_in(id_ex_1_memwrite_out),
    .PC_in(id_ex_1_pc_out), .RegWrite_in(EX_RegWrite), .R2_in(id_ex_1_r2_out), .JAL_in(id_ex_1_jal_out),
    .AluR_in(mips_alu_1_result), .RegDst_in(id_ex_1_regdst_out), .Halt_in(id_ex_1_halt_out),
    .Syscall_in(id_ex_1_syscall_out), .LH_in(id_ex_1_lh_out), .MemToReg_out(ex_mem_1_memtoreg_out),
    .IR_out(ex_mem_1_ir_out), .MemWrite_out(ex_mem_1_memwrite_out), .PC_out(ex_mem_1_pc_out),
    .RegWrite_out(MEM_RegWrite), .R2_out(ex_mem_1_r2_out), .JAL_out(ex_mem_1_jal_out),
    .AluR_out(ex_mem_1_alur_out), .RegDst_out(ex_mem_1_regdst_out), .Halt_out(ex_mem_1_halt_out),
    .Syscall_out(ex_mem_1_syscall_out), .LH_out(ex_mem_1_lh_out), .Reset(RST), .Enable(Halt), .CLK(CLK),
    .W__in(EX_WriteReg_num), .W__out(MEM_WriteReg_num), .PCr_in(EX_PC), .PCr_out(MEM_PC));  // open: Interrupt_in, Interrupt_out
  Counter #(.width(16), .max('hffff)) counter_3 (
    .count(BAC), .Q(\条件分支成功数 ), .clk(CLK), .clr(RST));  // open: load, D, carry
  \数据相关检测  \u_数据相关检测_1  (
    .OP(OP), .EX_WriteReg_num(EX_WriteReg_num), .EX_RegWrite(EX_RegWrite), .\数据相关 (\数据相关 ),
    .MEM_WriteReg_num(MEM_WriteReg_num), .MEM_RegWrite(MEM_RegWrite), .Func(Func), .ID_R1_num(ID_R1_num),
    .ID_R2_num(ID_R2_num));  // open: Load_Use, R1_Forward, R2_Forward, EX_OP, MEM_OP
  Multiplexer #(.width(16), .enable("false")) multiplexer_11 (
    .in0(mips_ram_1_p6), .in1(mips_ram_1_p6_2), .out(multiplexer_11_out), .sel(ex_mem_1_alur_out[1]));
  assign bit_extender_4_out = {{16{multiplexer_11_out[15]}}, multiplexer_11_out};  // Bit_Extender bit_extender_4
  Counter #(.width(16), .max('hffff)) counter_4 (
    .count(and_8_out), .Q(\插入气泡数 ), .clk(CLK), .clr(RST));  // open: load, D, carry
  and and_8 (and_8_out, Halt, \数据相关 );
  // MIPS_RAM mips_ram_1: pin names not known; wires that end beside it: ex_mem_1_alur_out[11:2], ex_mem_1_r2_out, ex_mem_1_memwrite_out, CLK, RST, {mips_ram_1_p6_2, mips_ram_1_p6}, mem_wb_1_ir_out[15:11]
  Multiplexer #(.width(32), .enable("false")) multiplexer_12 (
    .in0({mips_ram_1_p6_2, mips_ram_1_p6}), .in1(bit_extender_4_out), .out(multiplexer_12_out),
    .sel(ex_mem_1_lh_out));
  MEM_WB mem_wb_1 (
    .MemToReg_in(ex_mem_1_memtoreg_out), .IR_in(ex_mem_1_ir_out), .RegWrite_in(MEM_RegWrite),
    .PC_in(ex_mem_1_pc_out), .JAL_in(ex_mem_1_jal_out), .MemD_in(multiplexer_12_out),
    .RegDst_in(ex_mem_1_regdst_out), .AluR_in(ex_mem_1_alur_out), .Syscall_in(ex_mem_1_syscall_out),
    .Halt_in(ex_mem_1_halt_out), .MemToReg_out(mem_wb_1_memtoreg_out), .IR_out(mem_wb_1_ir_out),
    .RegWrite_out(RegW), .PC_out(mem_wb_1_pc_out), .JAL_out(mem_wb_1_jal_out), .MemD_out(mem_wb_1_memd_out),
    .RegDst_out(mem_wb_1_regdst_out), .AluR_out(mem_wb_1_alur_out), .Syscall_out(SysC),
    .Halt_out(mem_wb_1_halt_out), .Reset(RST), .Enable(Halt), .CLK(CLK), .W__in(MEM_WriteReg_num),
    .PCr_in(MEM_PC), .PCr_out(WB_PC));  // open: W__out, Interrupt_in, Interrupt_out, R2_in, R2_out
  Multiplexer #(.width(32), .enable("false")) multiplexer_13 (
    .in0(mem_wb_1_alur_out), .in1(mem_wb_1_memd_out), .out(multiplexer_13_out), .sel(mem_wb_1_memtoreg_out));
  not not_5 (not_5_out, mem_wb_1_halt_out);
  Multiplexer #(.width(5), .enable("false")) multiplexer_14 (
    .in0(mem_wb_1_ir_out[20:16]), .in1(mem_wb_1_ir_out[15:11]), .out(multiplexer_14_out),
    .sel(mem_wb_1_regdst_out));
  or or_5 (Halt, Go, RST, not_5_out);
  Multiplexer #(.width(32), .enable("false")) multiplexer_15 (
    .in0(multiplexer_13_out), .in1(mem_wb_1_pc_out), .out(multiplexer_15_out), .sel(mem_wb_1_jal_out));
  Multiplexer #(.width(5), .enable("false")) multiplexer_16 (
    .in0(multiplexer_14_out), .in1({5{1'b1}}), .out(multiplexer_16_out), .sel(mem_wb_1_jal_out));

  // Notes on the sheet:
  //   中断源
  //   中断等待指示
  //   数码管输出
  //   指令存储器
  //   contents of rom_1 (hex, n*v repeats v):
  //   20110001 8100005 20110001 20120002 20130003 8100009 20110001 20120002 20130003 810000d 20110001
  //   20120002 20130003 8100011 20110001 20120002 20130003 c1000f6 20100001 20110001 118fc0 112020
  //   20020022 c 118882 12200001 8100015 112020 20020022 c 20110001 118880 112020 20020022 c 12200001
  //   810001f 20110001 118fc0 112020 20020022 c 1188c3 112020 20020022 c 118903 112020 20020022 c 118903
  //   112020 20020022 c 118903 112020 20020022 c 118903 112020 20020022 c 118903 112020 20020022 c 118903
  //   112020 20020022 c 118903 112020 20020022 c 20100001 109fc0 139fc3 8021 2012000c 24160003 26100001
  //   3210000f 20080008 20090001 139900 2709825 132020 20020022 c 1094022 1500fff9 22100001 2018000f
  //   2188024 108700 20080008 20090001 139902 2709825 132021 20020022 c 1094022 1500fff9 108702 2c9b022
  //   12c00001 8100050 4020 1084027 84400 3508ffff 82021 20020022 c 2010ffff 20110000 ae300000 22100001
  //   22310004 ae300000 22100001 22310004 ae300000 22100001 22310004 ae300000 22100001 22310004 ae300000
  //   22100001 22310004 ae300000 22100001 22310004 ae300000 22100001 22310004 ae300000 22100001 22310004
  //   ae300000 22100001 22310004 ae300000 22100001 22310004 ae300000 22100001 22310004 ae300000 22100001
  //   22310004 ae300000 22100001 22310004 ae300000 22100001 22310004 ae300000 22100001 22310004 ae300000
  //   22100001 22310004 22100001 8020 2011003c 8e130000 8e340000 274402a 11000002 ae330000 ae140000
  //   2231fffc 1611fff8 102020 20020022 c 22100004 2011003c 1611fff2 20020032 c 20080001 20090003 20110876
  //   118d00 112020 20020022 c 200b0008 1118806 1318806 112020 20020022 c 216bffff 1560fff9 2002000a c
  //   2008ffff 20090000 20111997 112020 20020022 c 2288820 2e291949 1120fffa 2002000a c 20090000 200b0010
  //   34118483 20120404 118c00 129400 36318281 22520404 ad310000 2328820 21290004 216bffff 1560fffb
  //   200b0020 20090000 85310000 112020 20020022 c 21290002 216bffff 1560fff9 2002000a c 2011fff1 112020
  //   20020022 c 22310001 1a20fffb 2002000a c 2002000a c 20100000 22100001 102020 20020022 c 22100002
  //   102020 20020022 c 22100003 102020 20020022 c 22100004 102020 20020022 c 22100005 102020 20020022 c
  //   22100006 102020 20020022 c 22100007 102020 20020022 c 22100008 102020 20020022 20020022 c 3e00008
  //   指令字
  //   OP
  //   Func
  //   rs
  //   rt
  //   rd
  //   Shamt
  //   JMP
  //   JR
  //   BLEZ
  //   Syscall
  //   $a0
  //   $v0
  //   Beq
  //   Bne
  //   MemToReg
  //   MemWrite
  //   AluOP
  //   AluSrcB
  //   RegWrite
  //   JAL
  //   RegDst
  //   流水调试日志用
  //   rt
  //   rd
  //   Din
  //   W#
endmodule

module \重定向流水线  (
);

  wire and_1_out, and_2_out, and_3_out, and_4_out, and_5_out, and_6_out, and_7_out, and_8_out, BAC, CLK,
       comparator_1_eq, comparator_2_eq, comparator_2_lt, ex_mem_1_halt_out, ex_mem_1_jal_out,
       ex_mem_1_lh_out, ex_mem_1_memtoreg_out, ex_mem_1_memwrite_out, ex_mem_1_regdst_out,
       ex_mem_1_syscall_out, EX_RegWrite, Go, Halt, id_ex_1_alusrcb_out, id_ex_1_beq_out, id_ex_1_blez_out,
       id_ex_1_bne_out, id_ex_1_jal_out, id_ex_1_lh_out, id_ex_1_memtoreg_out, id_ex_1_memwrite_out,
       id_ex_1_regdst_out, id_ex_1_syscall_out, IR1, IR2, IR3, JMP, JR, LoadUse, MEM_RegWrite,
       mem_wb_1_halt_out, mem_wb_1_jal_out, mem_wb_1_memtoreg_out, mem_wb_1_regdst_out, mips_alu_1_equal,
       not_1_out, not_2_out, not_3_out, not_4_out, not_5_out, or_1_out, or_2_out, or_3_out, RegW, RST,
       SignedExt, SRLV, SysC, W1, W2, W3, \数据相关 , \硬布线控制器_1_alu_src , \硬布线控制器_1_beq , \硬布线控制器_1_blez ,
       \硬布线控制器_1_bne , \硬布线控制器_1_jal , \硬布线控制器_1_jmp , \硬布线控制器_1_jr , \硬布线控制器_1_lh , \硬布线控制器_1_memtoreg ,
       \硬布线控制器_1_memwrite , \硬布线控制器_1_regdst , \硬布线控制器_1_regwrite , \硬布线控制器_1_srlv , \硬布线控制器_1_syscall ;
  wire [1:0] R1_Forward, R2_Forward, \数据相关检测_1_r1_forward , \数据相关检测_1_r2_forward ;
  wire [3:0] id_ex_1_aluop_out, \硬布线控制器_1_alu_op ;
  wire [4:0] EX_WriteReg_num, id_ex_1_shamt_out, ID_R1_num, ID_R2_num, MEM_WriteReg_num, multiplexer_4_out,
       multiplexer_8_out, multiplexer_12_out, multiplexer_16_out, multiplexer_18_out;
  wire [5:0] EX_OP, Func, MEM_OP, OP;
  wire [15:0] adder_3_out, \LoadUse次数 , mips_ram_1_p6, mips_ram_1_p6_2, multiplexer_13_out, multiplier_1_out,
       \总周期数 , \插入气泡数 , \无条件分支数 , \条件分支成功数 ;
  wire [25:0] ex_mem_1_ir_out, id_ex_1_ir_out;
  wire [25:6] if_id_1_ir_out;
  wire [31:0] adder_1_out, adder_2_out, bit_extender_1_out, bit_extender_2_out, bit_extender_3_out,
       bit_extender_4_out, ex_mem_1_alur_out, ex_mem_1_pc_out, ex_mem_1_r2_out, EX_PC, id_ex_1_address_out,
       id_ex_1_imm_out, id_ex_1_pc_out, id_ex_1_r1_out, id_ex_1_r2_out, ID_PC, if_id_1_pc_out, IF_PC,
       LedData, MEM_PC, mem_wb_1_alur_out, mem_wb_1_ir_out, mem_wb_1_memd_out, mem_wb_1_pc_out,
       mips_alu_1_result, mips_regifile_1_r1, mips_regifile_1_r2, multiplexer_1_out, multiplexer_2_out,
       multiplexer_3_out, multiplexer_5_out, multiplexer_9_out, multiplexer_10_out, multiplexer_11_out,
       multiplexer_14_out, multiplexer_15_out, multiplexer_17_out, rom_1_data, shifter_1_out, shifter_2_out,
       WB_PC;

  Button \u_总复位  (.out(RST));
  Button _1 (.out(IR1));
  Button _2 (.out(IR2));
  Button _3 (.out(IR3));
  Button \u_继续运行  (.out(Go));
  LED led_1 (.in(W1));
  LED led_2 (.in(W2));
  LED led_3 (.in(W3));
  not not_1 (not_1_out, LoadUse);
  and and_1 (and_1_out, not_1_out, Halt);
  Multiplexer #(.width(32), .enable("false")) multiplexer_1 (
    .in0(adder_1_out), .in1(adder_2_out), .out(multiplexer_1_out), .sel(BAC));
  Multiplexer #(.width(32), .enable("false")) multiplexer_2 (
    .in0(multiplexer_1_out), .in1(multiplexer_3_out), .out(multiplexer_2_out), .sel(JMP));
  // Probe on multiplexer_2_out[11:0]
  Multiplexer #(.width(32), .enable("false")) multiplexer_3 (
    .in0(id_ex_1_address_out), .in1(multiplexer_9_out), .out(multiplexer_3_out), .sel(JR));
  Hex_Digit_Display hex_digit_display_1 (.value(LedData[31:28]));  // open: dp
  Counter #(.width(16), .max('hffff)) counter_1 (
    .count(Halt), .Q(\总周期数 ), .clk(CLK), .clr(RST));  // open: load, D, carry
  Register #(.width(32)) PC_2 (.D(multiplexer_2_out), .en(and_1_out), .Q(IF_PC), .clk(CLK), .clr(RST));
  Hex_Digit_Display hex_digit_display_2 (.value(LedData[27:24]));  // open: dp
  Hex_Digit_Display hex_digit_display_3 (.value(LedData[23:20]));  // open: dp
  Hex_Digit_Display hex_digit_display_4 (.value(LedData[15:12]));  // open: dp
  Hex_Digit_Display hex_digit_display_5 (.value(LedData[19:16]));  // open: dp
  ROM #(.addrWidth(10), .dataWidth(32)) rom_1 (.addr(IF_PC[11:2]), .data(rom_1_data));  // open: sel
  Adder #(.width(32)) adder_1 (.a(IF_PC), .b(32'h4), .out(adder_1_out));  // open: cin, cout
  not not_2 (not_2_out, LoadUse);
  and and_2 (and_2_out, not_2_out, Halt);
  Hex_Digit_Display hex_digit_display_6 (.value(LedData[7:4]));  // open: dp
  Hex_Digit_Display hex_digit_display_7 (.value(LedData[11:8]));  // open: dp
  Clock clock_1 (.out(CLK));
  IF_ID if_id_1 (
    .PC_in(adder_1_out), .IR_in(rom_1_data), .PC_out(if_id_1_pc_out), .IR_out({OP, if_id_1_ir_out, Func}),
    .Reset(or_1_out), .CLK(CLK), .Enable(and_2_out), .PCr_in(IF_PC), .PCr_out(ID_PC));  // open: PC_G_in, PC_G_out, HG_in, HG_out
  Hex_Digit_Display hex_digit_display_8 (.value(LedData[3:0]));  // open: dp
  Multiplexer #(.width(5), .enable("false")) multiplexer_4 (
    .in0(if_id_1_ir_out[20:16]), .in1(if_id_1_ir_out[15:11]), .out(multiplexer_4_out), .sel(\硬布线控制器_1_regdst ));
  assign bit_extender_1_out = {{16{1'b0}}, {if_id_1_ir_out[15:6], Func}};  // Bit_Extender bit_extender_1
  Multiplexer #(.width(32), .enable("false")) multiplexer_5 (
    .in0(bit_extender_1_out), .in1(bit_extender_2_out), .out(multiplexer_5_out), .sel(SignedExt));
  assign bit_extender_2_out = {{16{if_id_1_ir_out[15]}}, {if_id_1_ir_out[15:6], Func}};  // Bit_Extender bit_extender_2
  assign bit_extender_3_out = {{6{if_id_1_ir_out[25]}}, {if_id_1_ir_out, Func}};  // Bit_Extender bit_extender_3
  // Probe on \总周期数 
  // Probe on \无条件分支数 
  // Probe on \条件分支成功数 
  // Probe on \插入气泡数 
  // Probe on \LoadUse次数 
  \硬布线控制器  \u_硬布线控制器_1  (
    .Func(Func), .OP(OP), .ALU_OP(\硬布线控制器_1_alu_op ), .MemToReg(\硬布线控制器_1_memtoreg ),
    .MemWrite(\硬布线控制器_1_memwrite ), .ALU_SRC(\硬布线控制器_1_alu_src ), .RegWrite(\硬布线控制器_1_regwrite ),
    .SysCALL(\硬布线控制器_1_syscall ), .SignedExt(SignedExt), .RegDst(\硬布线控制器_1_regdst ), .JR(\硬布线控制器_1_jr ),
    .JMP(\硬布线控制器_1_jmp ), .Beq(\硬布线控制器_1_beq ), .JAL(\硬布线控制器_1_jal ), .Bne(\硬布线控制器_1_bne ),
    .LH(\硬布线控制器_1_lh ), .BLEZ(\硬布线控制器_1_blez ), .SRLV(\硬布线控制器_1_srlv ));  // open: ERET, MFC0, MTC0, MF
  Multiplexer #(.width(5), .enable("false")) multiplexer_6 (
    .in0(if_id_1_ir_out[25:21]), .in1(5'b00100), .out(ID_R1_num), .sel(\硬布线控制器_1_syscall ));
  Multiplexer #(.width(5), .enable("false")) multiplexer_7 (
    .in0(if_id_1_ir_out[20:16]), .in1(5'b00010), .out(ID_R2_num), .sel(\硬布线控制器_1_syscall ));
  Multiplexer #(.width(5), .enable("false")) multiplexer_8 (
    .in0(multiplexer_4_out), .in1({5{1'b1}}), .out(multiplexer_8_out), .sel(\硬布线控制器_1_jal ));
  Shifter #(.width(32)) shifter_1 (.in(bit_extender_3_out), .\dist (5'b00010), .out(shifter_1_out));
  // Probe on IF_PC[11:0]
  // Probe on ID_PC[11:0]
  MIPS_Regifile mips_regifile_1 (
    .Din(multiplexer_17_out), .Clk(CLK), .R1(mips_regifile_1_r1), .R2(mips_regifile_1_r2), .WE(RegW),
    .W_num(multiplexer_18_out), .R1_num(ID_R1_num), .R2_num(ID_R2_num));
  // Probe on EX_PC[11:0]
  // Probe on MEM_PC[11:0]
  or or_1 (or_1_out, JMP, RST, BAC);
  // Probe on WB_PC[11:0]
  or or_2 (or_2_out, or_1_out, LoadUse);
  ID_EX id_ex_1 (
    .BNE_in(\硬布线控制器_1_bne ), .IR_in({OP, if_id_1_ir_out, Func}), .MemToReg_in(\硬布线控制器_1_memtoreg ),
    .PC_in(if_id_1_pc_out), .MemWrite_in(\硬布线控制器_1_memwrite ), .R1_in(mips_regifile_1_r1),
    .AluSrcB_in(\硬布线控制器_1_alu_src ), .R2_in(mips_regifile_1_r2), .RegWrite_in(\硬布线控制器_1_regwrite ),
    .Imm_in(multiplexer_5_out), .JAL_in(\硬布线控制器_1_jal ), .Address_in(shifter_1_out),
    .RegDst_in(\硬布线控制器_1_regdst ), .AluOP_in(\硬布线控制器_1_alu_op ), .Syscall_in(\硬布线控制器_1_syscall ),
    .Shamt_in(if_id_1_ir_out[10:6]), .JMP_in(\硬布线控制器_1_jmp ), .JR_in(\硬布线控制器_1_jr ), .LH_in(\硬布线控制器_1_lh ),
    .SRLV_in(\硬布线控制器_1_srlv ), .BNE_out(id_ex_1_bne_out), .IR_out({EX_OP, id_ex_1_ir_out}),
    .MemToReg_out(id_ex_1_memtoreg_out), .PC_out(id_ex_1_pc_out), .MemWrite_out(id_ex_1_memwrite_out),
    .R1_out(id_ex_1_r1_out), .AluSrcB_out(id_ex_1_alusrcb_out), .R2_out(id_ex_1_r2_out),
    .RegWrite_out(EX_RegWrite), .Imm_out(id_ex_1_imm_out), .JAL_out(id_ex_1_jal_out),
    .Address_out(id_ex_1_address_out), .RegDst_out(id_ex_1_regdst_out), .AluOP_out(id_ex_1_aluop_out),
    .Syscall_out(id_ex_1_syscall_out), .Shamt_out(id_ex_1_shamt_out), .JMP_out(JMP), .JR_out(JR),
    .LH_out(id_ex_1_lh_out), .SRLV_out(SRLV), .Reset(or_2_out), .Enable(Halt), .CLK(CLK),
    .BEQ_in(\硬布线控制器_1_beq ), .BEQ_out(id_ex_1_beq_out), .BLEZ_in(\硬布线控制器_1_blez ),
    .BLEZ_out(id_ex_1_blez_out), .W__in(multiplexer_8_out), .W__out(EX_WriteReg_num), .PCr_in(ID_PC),
    .PCr_out(EX_PC));  // open: Halt_in, Halt_out, HG_in, HG_out, PCG_in, PCG_out, Interrupt_in, Interrupt_out
  Multiplexer #(.select(2), .width(32), .enable("false")) multiplexer_9 (
    .in0(id_ex_1_r1_out), .in1(mem_wb_1_alur_out), .in2(mem_wb_1_memd_out), .in3(ex_mem_1_alur_out),
    .out(multiplexer_9_out), .sel(R1_Forward));
  Multiplexer #(.select(2), .width(32), .enable("false")) multiplexer_10 (
    .in0(id_ex_1_r2_out), .in1(mem_wb_1_alur_out), .in2(mem_wb_1_memd_out), .in3(ex_mem_1_alur_out),
    .out(multiplexer_10_out), .sel(R2_Forward));
  Counter #(.width(16), .max('hffff)) counter_2 (
    .count(JMP), .Q(\无条件分支数 ), .clk(CLK), .clr(RST));  // open: load, D, carry
  Multiplexer #(.width(32), .enable("false")) multiplexer_11 (
    .in0(multiplexer_10_out), .in1(id_ex_1_imm_out), .out(multiplexer_11_out), .sel(id_ex_1_alusrcb_out));
  and and_3 (and_3_out, id_ex_1_syscall_out, comparator_1_eq);
  Comparator #(.width(32)) comparator_1 (.a(32'h22), .b(multiplexer_11_out), .eq(comparator_1_eq));  // open: gt, lt
  not not_3 (not_3_out, comparator_1_eq);
  Register #(.width(32)) register_1 (.D(multiplexer_9_out), .en(and_3_out), .Q(LedData), .clk(CLK), .clr(RST));
  and and_4 (and_4_out, not_3_out, id_ex_1_syscall_out);
  Counter #(.width(16), .max('hffff)) counter_3 (
    .count(BAC), .Q(\条件分支成功数 ), .clk(CLK), .clr(RST));  // open: load, D, carry
  Comparator #(.width(32)) comparator_2 (
    .a(multiplexer_9_out), .b({32{1'b0}}), .eq(comparator_2_eq), .lt(comparator_2_lt));  // open: gt
  MIPS_ALU mips_alu_1 (
    .X(multiplexer_9_out), .Y(multiplexer_11_out), .AluOP(id_ex_1_aluop_out), .Equal(mips_alu_1_equal),
    .Result(mips_alu_1_result), .shamt(multiplexer_12_out));  // open: Result_2
  Multiplexer #(.width(5), .enable("false")) multiplexer_12 (
    .in0(id_ex_1_shamt_out), .in1(multiplexer_9_out[4:0]), .out(multiplexer_12_out), .sel(SRLV));
  Shifter #(.width(32)) shifter_2 (.in(id_ex_1_imm_out), .\dist (5'b00010), .out(shifter_2_out));
  or or_3 (or_3_out, comparator_2_eq, comparator_2_lt);
  and and_5 (and_5_out, or_3_out, id_ex_1_blez_out);
  and and_6 (and_6_out, mips_alu_1_equal, id_ex_1_beq_out);
  not not_4 (not_4_out, mips_alu_1_equal);
  and and_7 (and_7_out, not_4_out, id_ex_1_bne_out);
  Adder #(.width(32)) adder_2 (.a(shifter_2_out), .b(id_ex_1_pc_out), .out(adder_2_out));  // open: cin, cout
  or or_4 (BAC, and_6_out, and_5_out, and_7_out);
  EX_MEM ex_mem_1 (
    .MemToReg_in(id_ex_1_memtoreg_out), .IR_in({EX_OP, id_ex_1_ir_out}), .MemWrite_in(id_ex_1_memwrite_out),
    .PC_in(id_ex_1_pc_out), .RegWrite_in(EX_RegWrite), .R2_in(multiplexer_10_out), .JAL_in(id_ex_1_jal_out),
    .AluR_in(mips_alu_1_result), .RegDst_in(id_ex_1_regdst_out), .Halt_in(and_4_out),
    .Syscall_in(id_ex_1_syscall_out), .LH_in(id_ex_1_lh_out), .MemToReg_out(ex_mem_1_memtoreg_out),
    .IR_out({MEM_OP, ex_mem_1_ir_out}), .MemWrite_out(ex_mem_1_memwrite_out), .PC_out(ex_mem_1_pc_out),
    .RegWrite_out(MEM_RegWrite), .R2_out(ex_mem_1_r2_out), .JAL_out(ex_mem_1_jal_out),
    .AluR_out(ex_mem_1_alur_out), .RegDst_out(ex_mem_1_regdst_out), .Halt_out(ex_mem_1_halt_out),
    .Syscall_out(ex_mem_1_syscall_out), .LH_out(ex_mem_1_lh_out), .Reset(RST), .Enable(Halt), .CLK(CLK),
    .W__in(EX_WriteReg_num), .W__out(MEM_WriteReg_num), .PCr_in(EX_PC), .PCr_out(MEM_PC));  // open: Interrupt_in, Interrupt_out
  Adder #(.width(16)) adder_3 (.a(\无条件分支数 ), .b(\条件分支成功数 ), .out(adder_3_out));  // open: cin, cout
  Multiplier #(.width(16)) multiplier_1 (.a(adder_3_out), .b(16'h2), .out(multiplier_1_out));  // open: cin, cout
  Adder #(.width(16)) adder_4 (.a(multiplier_1_out), .b(\LoadUse次数 ), .out(\插入气泡数 ));  // open: cin, cout
  Multiplexer #(.width(16), .enable("false")) multiplexer_13 (
    .in0(mips_ram_1_p6), .in1(mips_ram_1_p6_2), .out(multiplexer_13_out), .sel(ex_mem_1_alur_out[1]));
  // MIPS_RAM mips_ram_1: pin names not known; wires that end beside it: ex_mem_1_alur_out[11:2], ex_mem_1_r2_out, ex_mem_1_memwrite_out, CLK, RST, {mips_ram_1_p6_2, mips_ram_1_p6}
  assign bit_extender_4_out = {{16{multiplexer_13_out[15]}}, multiplexer_13_out};  // Bit_Extender bit_extender_4
  \数据相关检测  \u_数据相关检测_1  (
    .OP(OP), .EX_WriteReg_num(EX_WriteReg_num), .EX_RegWrite(EX_RegWrite), .\数据相关 (\数据相关 ),
    .MEM_WriteReg_num(MEM_WriteReg_num), .MEM_RegWrite(MEM_RegWrite), .Func(Func), .Load_Use(LoadUse),
    .ID_R1_num(ID_R1_num), .ID_R2_num(ID_R2_num), .R1_Forward(\数据相关检测_1_r1_forward ),
    .R2_Forward(\数据相关检测_1_r2_forward ), .EX_OP(EX_OP), .MEM_OP(MEM_OP));
  Multiplexer #(.width(32), .enable("false")) multiplexer_14 (
    .in0({mips_ram_1_p6_2, mips_ram_1_p6}), .in1(bit_extender_4_out), .out(multiplexer_14_out),
    .sel(ex_mem_1_lh_out));
  and and_8 (and_8_out, Halt, LoadUse);
  MEM_WB mem_wb_1 (
    .MemToReg_in(ex_mem_1_memtoreg_out), .IR_in({MEM_OP, ex_mem_1_ir_out}), .RegWrite_in(MEM_RegWrite),
    .PC_in(ex_mem_1_pc_out), .JAL_in(ex_mem_1_jal_out), .MemD_in(multiplexer_14_out),
    .RegDst_in(ex_mem_1_regdst_out), .AluR_in(ex_mem_1_alur_out), .Syscall_in(ex_mem_1_syscall_out),
    .Halt_in(ex_mem_1_halt_out), .MemToReg_out(mem_wb_1_memtoreg_out), .IR_out(mem_wb_1_ir_out),
    .RegWrite_out(RegW), .PC_out(mem_wb_1_pc_out), .JAL_out(mem_wb_1_jal_out), .MemD_out(mem_wb_1_memd_out),
    .RegDst_out(mem_wb_1_regdst_out), .AluR_out(mem_wb_1_alur_out), .Syscall_out(SysC),
    .Halt_out(mem_wb_1_halt_out), .Reset(RST), .Enable(Halt), .CLK(CLK), .W__in(MEM_WriteReg_num),
    .PCr_in(MEM_PC), .PCr_out(WB_PC));  // open: W__out, Interrupt_in, Interrupt_out, R2_in, R2_out
  Counter #(.width(16), .max('hffff)) counter_4 (
    .count(and_8_out), .Q(\LoadUse次数 ), .clk(CLK), .clr(RST));  // open: load, D, carry
  Register #(.width(4)) register_2 (
    .D({\数据相关检测_1_r2_forward , \数据相关检测_1_r1_forward }), .Q({R2_Forward, R1_Forward}), .clk(CLK), .clr(RST));  // open: en
  not not_5 (not_5_out, mem_wb_1_halt_out);
  Multiplexer #(.width(32), .enable("false")) multiplexer_15 (
    .in0(mem_wb_1_alur_out), .in1(mem_wb_1_memd_out), .out(multiplexer_15_out), .sel(mem_wb_1_memtoreg_out));
  Multiplexer #(.width(5), .enable("false")) multiplexer_16 (
    .in0(mem_wb_1_ir_out[20:16]), .in1(mem_wb_1_ir_out[15:11]), .out(multiplexer_16_out),
    .sel(mem_wb_1_regdst_out));
  or or_5 (Halt, Go, RST, not_5_out);
  Multiplexer #(.width(32), .enable("false")) multiplexer_17 (
    .in0(multiplexer_15_out), .in1(mem_wb_1_pc_out), .out(multiplexer_17_out), .sel(mem_wb_1_jal_out));
  Multiplexer #(.width(5), .enable("false")) multiplexer_18 (
    .in0(multiplexer_16_out), .in1({5{1'b1}}), .out(multiplexer_18_out), .sel(mem_wb_1_jal_out));

  // Notes on the sheet:
  //   中断源
  //   中断等待指示
  //   数码管输出
  //   指令存储器
  //   contents of rom_1 (hex, n*v repeats v):
  //   20110001 8100005 20110001 20120002 20130003 8100009 20110001 20120002 20130003 810000d 20110001
  //   20120002 20130003 8100011 20110001 20120002 20130003 c1000f6 20100001 20110001 118fc0 112020
  //   20020022 c 118882 12200001 8100015 112020 20020022 c 20110001 118880 112020 20020022 c 12200001
  //   810001f 20110001 118fc0 112020 20020022 c 1188c3 112020 20020022 c 118903 112020 20020022 c 118903
  //   112020 20020022 c 118903 112020 20020022 c 118903 112020 20020022 c 118903 112020 20020022 c 118903
  //   112020 20020022 c 118903 112020 20020022 c 20100001 109fc0 139fc3 8021 2012000c 24160003 26100001
  //   3210000f 20080008 20090001 139900 2709825 132020 20020022 c 1094022 1500fff9 22100001 2018000f
  //   2188024 108700 20080008 20090001 139902 2709825 132021 20020022 c 1094022 1500fff9 108702 2c9b022
  //   12c00001 8100050 4020 1084027 84400 3508ffff 82021 20020022 c 2010ffff 20110000 ae300000 22100001
  //   22310004 ae300000 22100001 22310004 ae300000 22100001 22310004 ae300000 22100001 22310004 ae300000
  //   22100001 22310004 ae300000 22100001 22310004 ae300000 22100001 22310004 ae300000 22100001 22310004
  //   ae300000 22100001 22310004 ae300000 22100001 22310004 ae300000 22100001 22310004 ae300000 22100001
  //   22310004 ae300000 22100001 22310004 ae300000 22100001 22310004 ae300000 22100001 22310004 ae300000
  //   22100001 22310004 22100001 8020 2011003c 8e130000 8e340000 274402a 11000002 ae330000 ae140000
  //   2231fffc 1611fff8 102020 20020022 c 22100004 2011003c 1611fff2 20020032 c 20080001 20090003 20110876
  //   118d00 112020 20020022 c 200b0008 1118806 1318806 112020 20020022 c 216bffff 1560fff9 2002000a c
  //   2008ffff 20090000 20111997 112020 20020022 c 2288820 2e291949 1120fffa 2002000a c 20090000 200b0010
  //   34118483 20120404 118c00 129400 36318281 22520404 ad310000 2328820 21290004 216bffff 1560fffb
  //   200b0020 20090000 85310000 112020 20020022 c 21290002 216bffff 1560fff9 2002000a c 2011fff1 112020
  //   20020022 c 22310001 1a20fffb 2002000a c 2002000a c 20100000 22100001 102020 20020022 c 22100002
  //   102020 20020022 c 22100003 102020 20020022 c 22100004 102020 20020022 c 22100005 102020 20020022 c
  //   22100006 102020 20020022 c 22100007 102020 20020022 c 22100008 102020 20020022 20020022 c 3e00008
  //   指令字
  //   OP
  //   Func
  //   rs
  //   rt
  //   rd
  //   Shamt
  //   JMP
  //   JR
  //   BLEZ
  //   Syscall
  //   $a0
  //   $v0
  //   Beq
  //   Bne
  //   MemToReg
  //   MemWrite
  //   AluOP
  //   AluSrcB
  //   RegWrite
  //   JAL
  //   RegDst
  //   流水调试日志用
  //   rt
  //   rd
  //   W#
  //   Din
endmodule

// 信号生成2
module \信号生成2  (
  input  OP0,
  input  OP1,
  input  OP2,
  input  OP3,
  input  OP4,
  input  OP5,
  input  F0,
  input  F1,
  input  F2,
  input  F3,
  input  F4,
  input  F5,
  output LH,
  output BLEZ,
  output SRLV,
  output ERET
);

  wire not_1_out, not_2_out, not_3_out, not_4_out, not_5_out, not_6_out, not_7_out, not_8_out, not_9_out,
       not_10_out, not_11_out, not_12_out, not_13_out, not_14_out, not_15_out, not_16_out, not_17_out,
       not_18_out, not_19_out, not_20_out, not_21_out, not_22_out, not_23_out, not_24_out, not_25_out,
       not_26_out, not_27_out;

  not not_1 (not_1_out, OP4);
  not not_2 (not_2_out, OP3);
  not not_3 (not_3_out, OP2);
  not not_4 (not_4_out, OP1);
  not not_5 (not_5_out, OP5);
  not not_6 (not_6_out, OP4);
  not not_7 (not_7_out, OP3);
  not not_8 (not_8_out, OP0);
  not not_9 (not_9_out, OP5);
  not not_10 (not_10_out, OP4);
  not not_11 (not_11_out, OP3);
  not not_12 (not_12_out, OP2);
  not not_13 (not_13_out, OP1);
  not not_14 (not_14_out, OP0);
  not not_15 (not_15_out, F5);
  not not_16 (not_16_out, F4);
  not not_17 (not_17_out, F3);
  not not_18 (not_18_out, F0);
  not not_19 (not_19_out, OP5);
  not not_20 (not_20_out, OP3);
  not not_21 (not_21_out, OP2);
  not not_22 (not_22_out, OP1);
  not not_23 (not_23_out, OP0);
  not not_24 (not_24_out, F5);
  not not_25 (not_25_out, F2);
  not not_26 (not_26_out, F1);
  not not_27 (not_27_out, F0);
  and and_1 (LH, OP5, not_1_out, not_2_out, not_3_out, not_4_out, OP0);
  and and_2 (BLEZ, not_5_out, not_6_out, not_7_out, OP2, OP1, not_8_out);
  and and_3 (SRLV, not_9_out, not_10_out, not_11_out, not_12_out, not_13_out, not_14_out, not_15_out, not_16_out, not_17_out, F2, F1, not_18_out);
  and and_4 (ERET, not_19_out, OP4, not_20_out, not_21_out, not_22_out, not_23_out, not_24_out, F4, F3, not_25_out, not_26_out, not_27_out);
endmodule

// BHT
module BHT (
  input  [31:0] PC,
  input  [1:0] NewStatusIn,
  input  Enable,
  input  [31:0] EX_PC,
  input  PCReady,
  input  StatusReady,
  input  CLK,
  input  [1:0] StatusIn,
  input  [31:0] TorgetAddrIn,
  input  RST,
  output Hit,
  output [31:0] AddrOut,
  output Miss,
  output [1:0] StatusOut,
  output StatusHit,
  output [1:0] IDStatusOut
);

  wire and_1_out, and_2_out, and_3_out, and_4_out, and_5_out, and_6_out, and_7_out, and_8_out, and_25_out,
       and_26_out, and_27_out, and_28_out, and_29_out, and_30_out, and_31_out, and_32_out, and_33_out,
       and_34_out, and_35_out, and_36_out, and_37_out, and_38_out, and_39_out, and_40_out, and_41_out,
       and_42_out, and_43_out, and_44_out, and_45_out, and_46_out, and_47_out, and_48_out, and_49_out,
       and_50_out, comparator_1_eq, comparator_2_eq, comparator_3_eq, comparator_4_eq, comparator_5_eq,
       comparator_6_eq, comparator_7_eq, comparator_8_eq, comparator_9_eq, comparator_10_eq,
       comparator_11_eq, comparator_12_eq, comparator_13_eq, comparator_14_eq, comparator_15_eq,
       comparator_16_eq, F0, F1, F2, F3, F4, F5, F6, F7, L0, L1, L2, L3, L4, L5, L6, L7, not_1_out,
       not_2_out, not_3_out, not_4_out, not_5_out, not_6_out, not_7_out, not_8_out, not_9_out, or_1_out,
       or_2_out, or_3_out, or_4_out, or_5_out, or_6_out, or_7_out, or_8_out, or_9_out, or_10_out, or_11_out,
       or_12_out, or_13_out, or_14_out, or_15_out, or_16_out, priority_encoder_1_en_out, R0, R1, R2, R3, R4,
       R5, R6, R7, S0, S1, S2, S3, S4, S5, S6, S7, V0, V1, V2, V3, V4, V5, V6, V7, valid_2_q, valid_3_q,
       valid_4_q, valid_5_q, valid_6_q, valid_7_q, valid_8_q, valid_q;
  wire [1:0] NewStatusIn0, NewStatusIn1, NewStatusIn2, NewStatusIn3, NewStatusIn4, NewStatusIn5,
       NewStatusIn6, NewStatusIn7, \分支预测历史_2_q , \分支预测历史_3_q , \分支预测历史_4_q , \分支预测历史_5_q , \分支预测历史_6_q ,
       \分支预测历史_7_q , \分支预测历史_8_q , \分支预测历史_q ;
  wire [2:0] max3_1_max_num, max3_2_max_num, max3_3_max_num, max3_4_max_num, max3_5_max_num, max3_6_max_num,
       max3_7_max_num, priority_encoder_1_out;
  wire [15:0] C0, C1, C2, C3, C4, C5, C6, C7, max3_1_max, max3_2_max, max3_3_max, max3_4_max, max3_5_max,
       max3_6_max, \淘汰标志位_2_q , \淘汰标志位_3_q , \淘汰标志位_4_q , \淘汰标志位_5_q , \淘汰标志位_6_q , \淘汰标志位_7_q , \淘汰标志位_8_q ,
       \淘汰标志位_q ;
  wire [31:0] Tag0, Tag1, Tag2, Tag3, Tag4, Tag5, Tag6, Tag7, \分支目标地址_2_q , \分支目标地址_3_q , \分支目标地址_4_q ,
       \分支目标地址_5_q , \分支目标地址_6_q , \分支目标地址_7_q , \分支目标地址_8_q , \分支目标地址_q , \标记位_2_q , \标记位_3_q , \标记位_4_q ,
       \标记位_5_q , \标记位_6_q , \标记位_7_q , \标记位_8_q , \标记位_q ;

  // Probe on EX_PC[11:0]
  Register #(.width(1)) valid (.D(1'b1), .en(and_1_out), .Q(valid_q), .clk(CLK), .clr(RST));
  Register #(.width(1)) valid_2 (.D(1'b1), .en(and_2_out), .Q(valid_2_q), .clk(CLK), .clr(RST));
  Register #(.width(1)) valid_3 (.D(1'b1), .en(and_3_out), .Q(valid_3_q), .clk(CLK), .clr(RST));
  Register #(.width(1)) valid_4 (.D(1'b1), .en(and_4_out), .Q(valid_4_q), .clk(CLK), .clr(RST));
  Register #(.width(1)) valid_5 (.D(1'b1), .en(and_5_out), .Q(valid_5_q), .clk(CLK), .clr(RST));
  Register #(.width(1)) valid_6 (.D(1'b1), .en(and_6_out), .Q(valid_6_q), .clk(CLK), .clr(RST));
  assign V0 = Enable ? valid_q : 1'bz;  // Controlled_Buffer controlled_buffer_1
  and and_1 (and_1_out, Enable, R0);
  assign V1 = Enable ? valid_2_q : 1'bz;  // Controlled_Buffer controlled_buffer_2
  and and_2 (and_2_out, Enable, R1);
  assign V2 = Enable ? valid_3_q : 1'bz;  // Controlled_Buffer controlled_buffer_3
  and and_3 (and_3_out, Enable, R2);
  assign V3 = Enable ? valid_4_q : 1'bz;  // Controlled_Buffer controlled_buffer_4
  and and_4 (and_4_out, Enable, R3);
  assign V4 = Enable ? valid_5_q : 1'bz;  // Controlled_Buffer controlled_buffer_5
  and and_5 (and_5_out, Enable, R4);
  assign V5 = Enable ? valid_6_q : 1'bz;  // Controlled_Buffer controlled_buffer_6
  and and_6 (and_6_out, Enable, R5);
  assign V6 = Enable ? valid_7_q : 1'bz;  // Controlled_Buffer controlled_buffer_7
  Register #(.width(1)) valid_7 (.D(1'b1), .en(and_7_out), .Q(valid_7_q), .clk(CLK), .clr(RST));
  assign V7 = Enable ? valid_8_q : 1'bz;  // Controlled_Buffer controlled_buffer_8
  Register #(.width(1)) valid_8 (.D(1'b1), .en(and_8_out), .Q(valid_8_q), .clk(CLK), .clr(RST));
  // Probe on PC[11:0]
  Register #(.width(32)) \u_标记位  (.D(PC), .en(and_1_out), .Q(\标记位_q ), .clk(CLK), .clr(RST));
  Register #(.width(32)) \u_标记位_2  (.D(PC), .en(and_2_out), .Q(\标记位_2_q ), .clk(CLK), .clr(RST));
  and and_7 (and_7_out, Enable, R6);
  and and_8 (and_8_out, Enable, R7);
  Comparator #(.width(32)) comparator_1 (.a(PC), .b(Tag0), .eq(comparator_1_eq));  // open: gt, lt
  Comparator #(.width(32)) comparator_2 (.a(PC), .b(Tag1), .eq(comparator_2_eq));  // open: gt, lt
  Comparator #(.width(32)) comparator_3 (.a(PC), .b(Tag2), .eq(comparator_3_eq));  // open: gt, lt
  Comparator #(.width(32)) comparator_4 (.a(PC), .b(Tag3), .eq(comparator_4_eq));  // open: gt, lt
  Comparator #(.width(32)) comparator_5 (.a(PC), .b(Tag4), .eq(comparator_5_eq));  // open: gt, lt
  Comparator #(.width(32)) comparator_6 (.a(PC), .b(Tag5), .eq(comparator_6_eq));  // open: gt, lt
  Comparator #(.width(32)) comparator_7 (.a(PC), .b(Tag6), .eq(comparator_7_eq));  // open: gt, lt
  Comparator #(.width(32)) comparator_8 (.a(PC), .b(Tag7), .eq(comparator_8_eq));  // open: gt, lt
  Comparator #(.width(32)) comparator_9 (.a(EX_PC), .b(Tag0), .eq(comparator_9_eq));  // open: gt, lt
  Comparator #(.width(32)) comparator_10 (.a(EX_PC), .b(Tag1), .eq(comparator_10_eq));  // open: gt, lt
  Comparator #(.width(32)) comparator_11 (.a(EX_PC), .b(Tag2), .eq(comparator_11_eq));  // open: gt, lt
  Comparator #(.width(32)) comparator_12 (.a(EX_PC), .b(Tag3), .eq(comparator_12_eq));  // open: gt, lt
  Comparator #(.width(32)) comparator_13 (.a(EX_PC), .b(Tag4), .eq(comparator_13_eq));  // open: gt, lt
  Comparator #(.width(32)) comparator_14 (.a(EX_PC), .b(Tag5), .eq(comparator_14_eq));  // open: gt, lt
  Comparator #(.width(32)) comparator_15 (.a(EX_PC), .b(Tag6), .eq(comparator_15_eq));  // open: gt, lt
  Comparator #(.width(32)) comparator_16 (.a(EX_PC), .b(Tag7), .eq(comparator_16_eq));  // open: gt, lt
  assign Tag0 = Enable ? \标记位_q  : 32'bz;  // Controlled_Buffer controlled_buffer_9
  assign Tag1 = Enable ? \标记位_2_q  : 32'bz;  // Controlled_Buffer controlled_buffer_10
  assign Tag2 = Enable ? \标记位_3_q  : 32'bz;  // Controlled_Buffer controlled_buffer_11
  Register #(.width(32)) \u_标记位_3  (.D(PC), .en(and_3_out), .Q(\标记位_3_q ), .clk(CLK), .clr(RST));
  Register #(.width(32)) \u_标记位_4  (.D(PC), .en(and_4_out), .Q(\标记位_4_q ), .clk(CLK), .clr(RST));
  assign Tag3 = Enable ? \标记位_4_q  : 32'bz;  // Controlled_Buffer controlled_buffer_12
  assign Tag4 = Enable ? \标记位_5_q  : 32'bz;  // Controlled_Buffer controlled_buffer_13
  Register #(.width(32)) \u_标记位_5  (.D(PC), .en(and_5_out), .Q(\标记位_5_q ), .clk(CLK), .clr(RST));
  assign Tag5 = Enable ? \标记位_6_q  : 32'bz;  // Controlled_Buffer controlled_buffer_14
  Register #(.width(32)) \u_标记位_6  (.D(PC), .en(and_6_out), .Q(\标记位_6_q ), .clk(CLK), .clr(RST));
  Register #(.width(32)) \u_标记位_7  (.D(PC), .en(and_7_out), .Q(\标记位_7_q ), .clk(CLK), .clr(RST));
  Register #(.width(32)) \u_标记位_8  (.D(PC), .en(and_8_out), .Q(\标记位_8_q ), .clk(CLK), .clr(RST));
  and and_9 (L0, comparator_1_eq, V0);
  and and_10 (L1, comparator_2_eq, V1);
  and and_11 (L2, comparator_3_eq, V2);
  and and_12 (L3, comparator_4_eq, V3);
  and and_13 (L4, comparator_5_eq, V4);
  and and_14 (L5, comparator_6_eq, V5);
  and and_15 (L6, comparator_7_eq, V6);
  and and_16 (L7, comparator_8_eq, V7);
  and and_17 (F0, comparator_9_eq, V0);
  and and_18 (F1, comparator_10_eq, V1);
  and and_19 (F2, comparator_11_eq, V2);
  and and_20 (F3, comparator_12_eq, V3);
  and and_21 (F4, comparator_13_eq, V4);
  and and_22 (F5, comparator_14_eq, V5);
  and and_23 (F6, comparator_15_eq, V6);
  and and_24 (F7, comparator_16_eq, V7);
  not not_1 (not_1_out, V0);
  not not_2 (not_2_out, V1);
  not not_3 (not_3_out, V2);
  not not_4 (not_4_out, V3);
  assign Tag6 = Enable ? \标记位_7_q  : 32'bz;  // Controlled_Buffer controlled_buffer_15
  assign Tag7 = Enable ? \标记位_8_q  : 32'bz;  // Controlled_Buffer controlled_buffer_16
  Counter #(.width(16), .max('hffff), .trigger("falling")) \u_淘汰标志位  (
    .count(or_1_out), .Q(\淘汰标志位_q ), .clk(CLK), .clr(and_34_out));  // open: load, D, carry
  or or_1 (or_1_out, Hit, not_1_out);
  Counter #(.width(16), .max('hffff), .trigger("falling")) \u_淘汰标志位_2  (
    .count(or_2_out), .Q(\淘汰标志位_2_q ), .clk(CLK), .clr(and_36_out));  // open: load, D, carry
  or or_2 (or_2_out, Hit, not_2_out);
  or or_3 (or_3_out, Hit, not_3_out);
  or or_4 (or_4_out, Hit, not_4_out);
  not not_5 (not_5_out, V4);
  or or_5 (or_5_out, Hit, not_5_out);
  not not_6 (not_6_out, V5);
  or or_6 (or_6_out, Hit, not_6_out);
  not not_7 (not_7_out, V6);
  or or_7 (or_7_out, Hit, not_7_out);
  not not_8 (not_8_out, V7);
  or or_8 (or_8_out, Hit, not_8_out);
  Priority_Encoder #(.disabled(0)) priority_encoder_1 (
    .in0(F0), .in1(F1), .in2(F2), .in3(F3), .in4(F4), .in5(F5), .in6(F6), .in7(F7),
    .out(priority_encoder_1_out), .en_out(priority_encoder_1_en_out));  // open: en_in, gs
  assign C0 = Enable ? \淘汰标志位_q  : 16'bz;  // Controlled_Buffer controlled_buffer_17
  and and_25 (and_25_out, Enable, S0);
  assign C1 = Enable ? \淘汰标志位_2_q  : 16'bz;  // Controlled_Buffer controlled_buffer_18
  and and_26 (and_26_out, Enable, S1);
  assign C2 = Enable ? \淘汰标志位_3_q  : 16'bz;  // Controlled_Buffer controlled_buffer_19
  Counter #(.width(16), .max('hffff), .trigger("falling")) \u_淘汰标志位_3  (
    .count(or_3_out), .Q(\淘汰标志位_3_q ), .clk(CLK), .clr(and_38_out));  // open: load, D, carry
  and and_27 (and_27_out, Enable, S2);
  assign C3 = Enable ? \淘汰标志位_4_q  : 16'bz;  // Controlled_Buffer controlled_buffer_20
  Counter #(.width(16), .max('hffff), .trigger("falling")) \u_淘汰标志位_4  (
    .count(or_4_out), .Q(\淘汰标志位_4_q ), .clk(CLK), .clr(and_40_out));  // open: load, D, carry
  and and_28 (and_28_out, Enable, S3);
  assign C4 = Enable ? \淘汰标志位_5_q  : 16'bz;  // Controlled_Buffer controlled_buffer_21
  Counter #(.width(16), .max('hffff), .trigger("falling")) \u_淘汰标志位_5  (
    .count(or_5_out), .Q(\淘汰标志位_5_q ), .clk(CLK), .clr(and_42_out));  // open: load, D, carry
  and and_29 (and_29_out, Enable, S4);
  assign C5 = Enable ? \淘汰标志位_6_q  : 16'bz;  // Controlled_Buffer controlled_buffer_22
  Counter #(.width(16), .max('hffff), .trigger("falling")) \u_淘汰标志位_6  (
    .count(or_6_out), .Q(\淘汰标志位_6_q ), .clk(CLK), .clr(and_44_out));  // open: load, D, carry
  and and_30 (and_30_out, Enable, S5);
  Counter #(.width(16), .max('hffff), .trigger("falling")) \u_淘汰标志位_7  (
    .count(or_7_out), .Q(\淘汰标志位_7_q ), .clk(CLK), .clr(and_46_out));  // open: load, D, carry
  Counter #(.width(16), .max('hffff), .trigger("falling")) \u_淘汰标志位_8  (
    .count(or_8_out), .Q(\淘汰标志位_8_q ), .clk(CLK), .clr(and_48_out));  // open: load, D, carry
  not not_9 (not_9_out, priority_encoder_1_en_out);
  or or_9 (or_9_out, and_1_out, and_25_out);
  or or_10 (or_10_out, and_2_out, and_26_out);
  or or_11 (or_11_out, and_3_out, and_27_out);
  or or_12 (or_12_out, and_4_out, and_28_out);
  or or_13 (or_13_out, and_5_out, and_29_out);
  or or_14 (or_14_out, and_6_out, and_30_out);
  assign C6 = Enable ? \淘汰标志位_7_q  : 16'bz;  // Controlled_Buffer controlled_buffer_23
  or or_15 (or_15_out, and_7_out, and_31_out);
  and and_31 (and_31_out, Enable, S6);
  assign C7 = Enable ? \淘汰标志位_8_q  : 16'bz;  // Controlled_Buffer controlled_buffer_24
  or or_16 (or_16_out, and_8_out, and_32_out);
  and and_32 (and_32_out, Enable, S7);
  Max3 max3_1 (.Y(C1), .X(C0), .Y_num(3'b001), .X_num(3'b000), .MAX(max3_1_max), .Max_num(max3_1_max_num));
  Max3 max3_2 (.Y(C3), .X(C2), .Y_num(3'b011), .X_num(3'b010), .MAX(max3_2_max), .Max_num(max3_2_max_num));
  Max3 max3_3 (.Y(C5), .X(C4), .Y_num(3'b101), .X_num(3'b100), .MAX(max3_3_max), .Max_num(max3_3_max_num));
  Max3 max3_4 (.Y(C7), .X(C6), .Y_num(3'b111), .X_num(3'b110), .MAX(max3_4_max), .Max_num(max3_4_max_num));
  and and_33 (and_33_out, Enable, StatusHit, StatusReady);
  Register #(.width(2)) \u_分支预测历史  (.D(NewStatusIn0), .en(or_9_out), .Q(\分支预测历史_q ), .clk(CLK), .clr(RST));
  Register #(.width(32)) \u_分支目标地址  (.D(TorgetAddrIn), .en(and_1_out), .Q(\分支目标地址_q ), .clk(CLK), .clr(RST));
  Register #(.width(2)) \u_分支预测历史_2  (.D(NewStatusIn1), .en(or_10_out), .Q(\分支预测历史_2_q ), .clk(CLK), .clr(RST));
  Register #(.width(32)) \u_分支目标地址_2  (.D(TorgetAddrIn), .en(and_2_out), .Q(\分支目标地址_2_q ), .clk(CLK), .clr(RST));
  Demultiplexer #(.select(3), .disabled(0)) demultiplexer_1 (
    .out0(S0), .out1(S1), .out2(S2), .out3(S3), .out4(S4), .out5(S5), .out6(S6), .out7(S7), .in(and_33_out),
    .sel(priority_encoder_1_out), .en(not_9_out));
  assign IDStatusOut = and_34_out ? \分支预测历史_q  : 2'bz;  // Controlled_Buffer controlled_buffer_25
  assign StatusOut = and_35_out ? \分支预测历史_q  : 2'bz;  // Controlled_Buffer controlled_buffer_26
  assign AddrOut = and_34_out ? \分支目标地址_q  : 32'bz;  // Controlled_Buffer controlled_buffer_27
  and and_34 (and_34_out, L0, Enable);
  and and_35 (and_35_out, Enable, F0);
  assign IDStatusOut = and_36_out ? \分支预测历史_2_q  : 2'bz;  // Controlled_Buffer controlled_buffer_28
  assign StatusOut = and_37_out ? \分支预测历史_2_q  : 2'bz;  // Controlled_Buffer controlled_buffer_29
  assign AddrOut = and_36_out ? \分支目标地址_2_q  : 32'bz;  // Controlled_Buffer controlled_buffer_30
  and and_36 (and_36_out, L1, Enable);
  and and_37 (and_37_out, Enable, F1);
  assign IDStatusOut = and_38_out ? \分支预测历史_3_q  : 2'bz;  // Controlled_Buffer controlled_buffer_31
  Register #(.width(2)) \u_分支预测历史_3  (.D(NewStatusIn2), .en(or_11_out), .Q(\分支预测历史_3_q ), .clk(CLK), .clr(RST));
  Register #(.width(32)) \u_分支目标地址_3  (.D(TorgetAddrIn), .en(and_3_out), .Q(\分支目标地址_3_q ), .clk(CLK), .clr(RST));
  assign AddrOut = and_38_out ? \分支目标地址_3_q  : 32'bz;  // Controlled_Buffer controlled_buffer_32
  assign IDStatusOut = and_40_out ? \分支预测历史_4_q  : 2'bz;  // Controlled_Buffer controlled_buffer_33
  Register #(.width(2)) \u_分支预测历史_4  (.D(NewStatusIn3), .en(or_12_out), .Q(\分支预测历史_4_q ), .clk(CLK), .clr(RST));
  Register #(.width(32)) \u_分支目标地址_4  (.D(TorgetAddrIn), .en(and_4_out), .Q(\分支目标地址_4_q ), .clk(CLK), .clr(RST));
  assign AddrOut = and_40_out ? \分支目标地址_4_q  : 32'bz;  // Controlled_Buffer controlled_buffer_34
  assign IDStatusOut = and_42_out ? \分支预测历史_5_q  : 2'bz;  // Controlled_Buffer controlled_buffer_35
  Register #(.width(2)) \u_分支预测历史_5  (.D(NewStatusIn4), .en(or_13_out), .Q(\分支预测历史_5_q ), .clk(CLK), .clr(RST));
  Register #(.width(32)) \u_分支目标地址_5  (.D(TorgetAddrIn), .en(and_5_out), .Q(\分支目标地址_5_q ), .clk(CLK), .clr(RST));
  assign AddrOut = and_42_out ? \分支目标地址_5_q  : 32'bz;  // Controlled_Buffer controlled_buffer_36
  assign IDStatusOut = and_44_out ? \分支预测历史_6_q  : 2'bz;  // Controlled_Buffer controlled_buffer_37
  Register #(.width(2)) \u_分支预测历史_6  (.D(NewStatusIn5), .en(or_14_out), .Q(\分支预测历史_6_q ), .clk(CLK), .clr(RST));
  Register #(.width(32)) \u_分支目标地址_6  (.D(TorgetAddrIn), .en(and_6_out), .Q(\分支目标地址_6_q ), .clk(CLK), .clr(RST));
  assign AddrOut = and_44_out ? \分支目标地址_6_q  : 32'bz;  // Controlled_Buffer controlled_buffer_38
  Register #(.width(2)) \u_分支预测历史_7  (.D(NewStatusIn6), .en(or_15_out), .Q(\分支预测历史_7_q ), .clk(CLK), .clr(RST));
  Register #(.width(32)) \u_分支目标地址_7  (.D(TorgetAddrIn), .en(and_7_out), .Q(\分支目标地址_7_q ), .clk(CLK), .clr(RST));
  assign AddrOut = and_46_out ? \分支目标地址_7_q  : 32'bz;  // Controlled_Buffer controlled_buffer_39
  Register #(.width(2)) \u_分支预测历史_8  (.D(NewStatusIn7), .en(or_16_out), .Q(\分支预测历史_8_q ), .clk(CLK), .clr(RST));
  assign AddrOut = and_48_out ? \分支目标地址_8_q  : 32'bz;  // Controlled_Buffer controlled_buffer_40
  Register #(.width(32)) \u_分支目标地址_8  (.D(TorgetAddrIn), .en(and_8_out), .Q(\分支目标地址_8_q ), .clk(CLK), .clr(RST));
  or or_17 (Hit, L0, L1, L2, L3, L4, L5, L6, L7);
  not not_10 (Miss, Hit);
  or or_18 (StatusHit, F0, F1, F2, F3, F4, F5, F6, F7);
  Max3 max3_5 (
    .Y(max3_2_max), .X(max3_1_max), .Y_num(max3_2_max_num), .X_num(max3_1_max_num), .MAX(max3_5_max),
    .Max_num(max3_5_max_num));
  Max3 max3_6 (
    .Y(max3_4_max), .X(max3_3_max), .Y_num(max3_4_max_num), .X_num(max3_3_max_num), .MAX(max3_6_max),
    .Max_num(max3_6_max_num));
  assign StatusOut = and_39_out ? \分支预测历史_3_q  : 2'bz;  // Controlled_Buffer controlled_buffer_41
  and and_38 (and_38_out, L2, Enable);
  and and_39 (and_39_out, Enable, F2);
  assign StatusOut = and_41_out ? \分支预测历史_4_q  : 2'bz;  // Controlled_Buffer controlled_buffer_42
  and and_40 (and_40_out, L3, Enable);
  and and_41 (and_41_out, Enable, F3);
  assign StatusOut = and_43_out ? \分支预测历史_5_q  : 2'bz;  // Controlled_Buffer controlled_buffer_43
  and and_42 (and_42_out, L4, Enable);
  and and_43 (and_43_out, Enable, F4);
  assign StatusOut = and_45_out ? \分支预测历史_6_q  : 2'bz;  // Controlled_Buffer controlled_buffer_44
  and and_44 (and_44_out, L5, Enable);
  and and_45 (and_45_out, Enable, F5);
  assign IDStatusOut = and_46_out ? \分支预测历史_7_q  : 2'bz;  // Controlled_Buffer controlled_buffer_45
  assign StatusOut = and_47_out ? \分支预测历史_7_q  : 2'bz;  // Controlled_Buffer controlled_buffer_46
  and and_46 (and_46_out, L6, Enable);
  and and_47 (and_47_out, Enable, F6);
  assign IDStatusOut = and_48_out ? \分支预测历史_8_q  : 2'bz;  // Controlled_Buffer controlled_buffer_47
  assign StatusOut = and_49_out ? \分支预测历史_8_q  : 2'bz;  // Controlled_Buffer controlled_buffer_48
  and and_48 (and_48_out, L7, Enable);
  and and_49 (and_49_out, Enable, F7);
  Max3 max3_7 (
    .Y(max3_6_max), .X(max3_5_max), .Y_num(max3_6_max_num), .X_num(max3_5_max_num), .Max_num(max3_7_max_num));  // open: MAX
  Demultiplexer #(.select(3), .enable("false")) demultiplexer_2 (
    .out0(R0), .out1(R1), .out2(R2), .out3(R3), .out4(R4), .out5(R5), .out6(R6), .out7(R7), .in(and_50_out),
    .sel(max3_7_max_num));
  and and_50 (and_50_out, Enable, Miss, PCReady);
  Demultiplexer #(.select(3), .width(2), .tristate("true")) demultiplexer_3 (
    .out0(NewStatusIn0), .out1(NewStatusIn1), .out2(NewStatusIn2), .out3(NewStatusIn3), .out4(NewStatusIn4),
    .out5(NewStatusIn5), .out6(NewStatusIn6), .out7(NewStatusIn7), .in(StatusIn),
    .sel(priority_encoder_1_out), .en(not_9_out));
  Demultiplexer #(.select(3), .width(2), .tristate("true"), .enable("false")) demultiplexer_4 (
    .out0(NewStatusIn0), .out1(NewStatusIn1), .out2(NewStatusIn2), .out3(NewStatusIn3), .out4(NewStatusIn4),
    .out5(NewStatusIn5), .out6(NewStatusIn6), .out7(NewStatusIn7), .in(NewStatusIn), .sel(max3_7_max_num));

  // Other names for the same wires on the sheet: En = Enable; StatusIn0[1:0] = NewStatusIn0;
  //   StatusIn1[1:0] = NewStatusIn1; StatusIn2[1:0] = NewStatusIn2; StatusIn3[1:0] = NewStatusIn3;
  //   StatusIn4[1:0] = NewStatusIn4; StatusIn5[1:0] = NewStatusIn5; StatusIn6[1:0] = NewStatusIn6;
  //   StatusIn7[1:0] = NewStatusIn7; Torget[31:0] = TorgetAddrIn

  // Notes on the sheet:
  //   输入引脚区
  //   并行比较
  //   找PC
  //   找状态
  //   输出引脚区
  //   命中和缺失判断
  //   选择写入
  //   LRU 淘汰计数值最大的
endmodule

// Max3
module Max3 (
  input  [15:0] Y,
  input  [15:0] X,
  input  [2:0] Y_num,
  input  [2:0] X_num,
  output [15:0] MAX,
  output [2:0] Max_num
);

  wire comparator_1_eq, comparator_1_gt, or_1_out;

  Multiplexer #(.width(16), .enable("false")) multiplexer_1 (.in0(Y), .in1(X), .out(MAX), .sel(or_1_out));
  Comparator #(.width(16), .mode("unsigned")) comparator_1 (
    .a(X), .b(Y), .gt(comparator_1_gt), .eq(comparator_1_eq));  // open: lt
  or or_1 (or_1_out, comparator_1_gt, comparator_1_eq);
  Multiplexer #(.width(3), .enable("false")) multiplexer_2 (.in0(Y_num), .in1(X_num), .out(Max_num), .sel(or_1_out));

  // Notes on the sheet:
  //   输出两个输入中的较大值，并输出较大值的3位编号
endmodule
module \分支预测流水线  (
);

  wire and_1_out, and_2_out, and_3_out, and_4_out, and_5_out, and_6_out, and_7_out, and_8_out, and_9_out,
       and_10_out, BAC, CLK, comparator_1_eq, comparator_2_eq, comparator_2_lt, ex_mem_1_halt_out,
       ex_mem_1_jal_out, ex_mem_1_lh_out, ex_mem_1_memtoreg_out, ex_mem_1_memwrite_out, ex_mem_1_regdst_out,
       ex_mem_1_syscall_out, EX_RegWrite, Go, GuessFail, GuessSucc, Halt, id_ex_1_alusrcb_out,
       id_ex_1_beq_out, id_ex_1_blez_out, id_ex_1_bne_out, id_ex_1_jal_out, id_ex_1_lh_out,
       id_ex_1_memtoreg_out, id_ex_1_memwrite_out, id_ex_1_regdst_out, id_ex_1_syscall_out, IR1, IR2, IR3,
       JMP, JR, LoadUse, MEM_RegWrite, mem_wb_1_halt_out, mem_wb_1_jal_out, mem_wb_1_memtoreg_out,
       mem_wb_1_regdst_out, mips_alu_1_equal, not_1_out, not_2_out, not_3_out, not_4_out, not_5_out,
       not_6_out, or_1_out, or_2_out, or_3_out, or_5_out, RegW, RST, SignedExt, SRLV, SysC, W1, W2, W3,
       \数据相关 , \是跳 , \硬布线控制器_1_alu_src , \硬布线控制器_1_beq , \硬布线控制器_1_blez , \硬布线控制器_1_bne , \硬布线控制器_1_jal ,
       \硬布线控制器_1_jmp , \硬布线控制器_1_jr , \硬布线控制器_1_lh , \硬布线控制器_1_memtoreg , \硬布线控制器_1_memwrite ,
       \硬布线控制器_1_regdst , \硬布线控制器_1_regwrite , \硬布线控制器_1_srlv , \硬布线控制器_1_syscall ;
  wire [1:0] HG, if_id_1_hg_out, npc_1_guessj, R1_Forward, R2_Forward, \数据相关检测_1_r1_forward ,
       \数据相关检测_1_r2_forward ;
  wire [3:0] id_ex_1_aluop_out, \硬布线控制器_1_alu_op ;
  wire [4:0] EX_WriteReg_num, id_ex_1_shamt_out, ID_R1_num, ID_R2_num, MEM_WriteReg_num, multiplexer_4_out,
       multiplexer_8_out, multiplexer_12_out, multiplexer_16_out, multiplexer_18_out;
  wire [5:0] EX_OP, Func, MEM_OP, OP;
  wire [15:0] \LoadUse次数 , mips_ram_1_p6, mips_ram_1_p6_2, multiplexer_13_out, \总周期数 , \无条件分支数 , \条件分支成功数 ,
       \预测失败数 , \预测成功数 ;
  wire [25:0] ex_mem_1_ir_out, id_ex_1_ir_out;
  wire [25:6] if_id_1_ir_out;
  wire [31:0] adder_1_out, adder_2_out, bit_extender_1_out, bit_extender_2_out, bit_extender_3_out,
       bit_extender_4_out, ex_mem_1_alur_out, ex_mem_1_pc_out, ex_mem_1_r2_out, EX_PC, id_ex_1_address_out,
       id_ex_1_imm_out, id_ex_1_pc_out, id_ex_1_r1_out, id_ex_1_r2_out, ID_PC, if_id_1_pc_g_out,
       if_id_1_pc_out, IF_PC, LedData, MEM_PC, mem_wb_1_alur_out, mem_wb_1_ir_out, mem_wb_1_memd_out,
       mem_wb_1_pc_out, mips_alu_1_result, mips_regifile_1_r1, mips_regifile_1_r2, multiplexer_1_out,
       multiplexer_2_out, multiplexer_3_out, multiplexer_5_out, multiplexer_9_out, multiplexer_10_out,
       multiplexer_11_out, multiplexer_14_out, multiplexer_15_out, multiplexer_17_out, npc_1_pcout,
       rom_1_data, shifter_1_out, shifter_2_out, WB_PC;

  Button \u_总复位  (.out(RST));
  Button _1 (.out(IR1));
  Button _2 (.out(IR2));
  Button _3 (.out(IR3));
  // Probe on npc_1_pcout[11:0]
  Button \u_继续运行  (.out(Go));
  LED led_1 (.in(W1));
  LED led_2 (.in(W2));
  LED led_3 (.in(W3));
  not not_1 (not_1_out, LoadUse);
  and and_1 (and_1_out, not_1_out, Halt);
  NPC npc_1 (
    .CLK(CLK), .EX_Hit(HG[1]), .EX_PC(EX_PC), .IR(rom_1_data), .RST(RST), .EX_JR(JR), .PC_4(adder_1_out),
    .Enable(Halt), .EX_isJump(\是跳 ), .EX_GuessJ(HG[0]), .EX_REG(multiplexer_9_out),
    .EX_Addr(multiplexer_2_out), .EX_JumpSucc(or_1_out), .GuessSucc(GuessSucc), .PCOut(npc_1_pcout),
    .GuessFail(GuessFail), .GuessJ(npc_1_guessj[0]), .Hit(npc_1_guessj[1]), .PC(IF_PC),
    .EX_PC_4(id_ex_1_pc_out));
  Hex_Digit_Display hex_digit_display_1 (.value(LedData[31:28]));  // open: dp
  Counter #(.width(16), .max('hffff)) counter_1 (
    .count(Halt), .Q(\总周期数 ), .clk(CLK), .clr(RST));  // open: load, D, carry
  Register #(.width(32)) PC_2 (.D(npc_1_pcout), .en(and_1_out), .Q(IF_PC), .clk(CLK), .clr(RST));
  or or_1 (or_1_out, and_2_out, BAC);
  Counter #(.width(16), .max('hffff)) counter_2 (
    .count(GuessSucc), .Q(\预测成功数 ), .clk(CLK), .clr(RST));  // open: load, D, carry
  Hex_Digit_Display hex_digit_display_2 (.value(LedData[23:20]));  // open: dp
  Hex_Digit_Display hex_digit_display_3 (.value(LedData[27:24]));  // open: dp
  and and_2 (and_2_out, JMP, not_2_out);
  not not_2 (not_2_out, JR);
  Hex_Digit_Display hex_digit_display_4 (.value(LedData[15:12]));  // open: dp
  Hex_Digit_Display hex_digit_display_5 (.value(LedData[19:16]));  // open: dp
  ROM #(.addrWidth(10), .dataWidth(32)) rom_1 (.addr(IF_PC[11:2]), .data(rom_1_data));  // open: sel
  Adder #(.width(32)) adder_1 (.a(IF_PC), .b(32'h4), .out(adder_1_out));  // open: cin, cout
  not not_3 (not_3_out, LoadUse);
  and and_3 (and_3_out, not_3_out, Halt);
  Multiplexer #(.width(32), .enable("false")) multiplexer_1 (
    .in0({32{1'b0}}), .in1(adder_2_out), .out(multiplexer_1_out), .sel(BAC));
  Multiplexer #(.width(32), .enable("false")) multiplexer_2 (
    .in0(multiplexer_1_out), .in1(multiplexer_3_out), .out(multiplexer_2_out), .sel(JMP));
  Counter #(.width(16), .max('hffff)) counter_3 (
    .count(GuessFail), .Q(\预测失败数 ), .clk(CLK), .clr(RST));  // open: load, D, carry
  Hex_Digit_Display hex_digit_display_6 (.value(LedData[7:4]));  // open: dp
  Hex_Digit_Display hex_digit_display_7 (.value(LedData[11:8]));  // open: dp
  Clock clock_1 (.out(CLK));
  IF_ID if_id_1 (
    .PC_in(adder_1_out), .IR_in(rom_1_data), .PC_out(if_id_1_pc_out), .IR_out({OP, if_id_1_ir_out, Func}),
    .Reset(or_2_out), .CLK(CLK), .Enable(and_3_out), .PCr_in(IF_PC), .PCr_out(ID_PC), .PC_G_in(npc_1_pcout),
    .PC_G_out(if_id_1_pc_g_out), .HG_in(npc_1_guessj), .HG_out(if_id_1_hg_out));
  Multiplexer #(.width(32), .enable("false")) multiplexer_3 (
    .in0(id_ex_1_address_out), .in1(multiplexer_9_out), .out(multiplexer_3_out), .sel(JR));
  Hex_Digit_Display hex_digit_display_8 (.value(LedData[3:0]));  // open: dp
  Multiplexer #(.width(5), .enable("false")) multiplexer_4 (
    .in0(if_id_1_ir_out[20:16]), .in1(if_id_1_ir_out[15:11]), .out(multiplexer_4_out), .sel(\硬布线控制器_1_regdst ));
  assign bit_extender_1_out = {{16{1'b0}}, {if_id_1_ir_out[15:6], Func}};  // Bit_Extender bit_extender_1
  Multiplexer #(.width(32), .enable("false")) multiplexer_5 (
    .in0(bit_extender_1_out), .in1(bit_extender_2_out), .out(multiplexer_5_out), .sel(SignedExt));
  assign bit_extender_2_out = {{16{if_id_1_ir_out[15]}}, {if_id_1_ir_out[15:6], Func}};  // Bit_Extender bit_extender_2
  assign bit_extender_3_out = {{6{if_id_1_ir_out[25]}}, {if_id_1_ir_out, Func}};  // Bit_Extender bit_extender_3
  // Probe on \总周期数 
  // Probe on \无条件分支数 
  // Probe on \条件分支成功数 
  // Probe on \LoadUse次数 
  // Probe on \预测成功数 
  // Probe on \预测失败数 
  // Probe on \LoadUse次数 
  \硬布线控制器  \u_硬布线控制器_1  (
    .Func(Func), .OP(OP), .ALU_OP(\硬布线控制器_1_alu_op ), .MemToReg(\硬布线控制器_1_memtoreg ),
    .MemWrite(\硬布线控制器_1_memwrite ), .ALU_SRC(\硬布线控制器_1_alu_src ), .RegWrite(\硬布线控制器_1_regwrite ),
    .SysCALL(\硬布线控制器_1_syscall ), .SignedExt(SignedExt), .RegDst(\硬布线控制器_1_regdst ), .JR(\硬布线控制器_1_jr ),
    .JMP(\硬布线控制器_1_jmp ), .Beq(\硬布线控制器_1_beq ), .JAL(\硬布线控制器_1_jal ), .Bne(\硬布线控制器_1_bne ),
    .LH(\硬布线控制器_1_lh ), .BLEZ(\硬布线控制器_1_blez ), .SRLV(\硬布线控制器_1_srlv ));  // open: ERET, MFC0, MTC0, MF
  Multiplexer #(.width(5), .enable("false")) multiplexer_6 (
    .in0(if_id_1_ir_out[25:21]), .in1(5'b00100), .out(ID_R1_num), .sel(\硬布线控制器_1_syscall ));
  Multiplexer #(.width(5), .enable("false")) multiplexer_7 (
    .in0(if_id_1_ir_out[20:16]), .in1(5'b00010), .out(ID_R2_num), .sel(\硬布线控制器_1_syscall ));
  Multiplexer #(.width(5), .enable("false")) multiplexer_8 (
    .in0(multiplexer_4_out), .in1({5{1'b1}}), .out(multiplexer_8_out), .sel(\硬布线控制器_1_jal ));
  Shifter #(.width(32)) shifter_1 (.in(bit_extender_3_out), .\dist (5'b00010), .out(shifter_1_out));
  // Probe on IF_PC[11:0]
  // Probe on ID_PC[11:0]
  or or_2 (or_2_out, JR, RST, GuessFail);
  MIPS_Regifile mips_regifile_1 (
    .Din(multiplexer_17_out), .Clk(CLK), .R1(mips_regifile_1_r1), .R2(mips_regifile_1_r2), .WE(RegW),
    .W_num(multiplexer_18_out), .R1_num(ID_R1_num), .R2_num(ID_R2_num));
  // Probe on EX_PC[11:0]
  // Probe on MEM_PC[11:0]
  or or_3 (or_3_out, or_2_out, LoadUse);
  ID_EX id_ex_1 (
    .BNE_in(\硬布线控制器_1_bne ), .IR_in({OP, if_id_1_ir_out, Func}), .MemToReg_in(\硬布线控制器_1_memtoreg ),
    .PC_in(if_id_1_pc_out), .MemWrite_in(\硬布线控制器_1_memwrite ), .R1_in(mips_regifile_1_r1),
    .AluSrcB_in(\硬布线控制器_1_alu_src ), .R2_in(mips_regifile_1_r2), .RegWrite_in(\硬布线控制器_1_regwrite ),
    .Imm_in(multiplexer_5_out), .JAL_in(\硬布线控制器_1_jal ), .Address_in(shifter_1_out),
    .RegDst_in(\硬布线控制器_1_regdst ), .AluOP_in(\硬布线控制器_1_alu_op ), .Syscall_in(\硬布线控制器_1_syscall ),
    .Shamt_in(if_id_1_ir_out[10:6]), .JMP_in(\硬布线控制器_1_jmp ), .JR_in(\硬布线控制器_1_jr ), .LH_in(\硬布线控制器_1_lh ),
    .SRLV_in(\硬布线控制器_1_srlv ), .BNE_out(id_ex_1_bne_out), .IR_out({EX_OP, id_ex_1_ir_out}),
    .MemToReg_out(id_ex_1_memtoreg_out), .PC_out(id_ex_1_pc_out), .MemWrite_out(id_ex_1_memwrite_out),
    .R1_out(id_ex_1_r1_out), .AluSrcB_out(id_ex_1_alusrcb_out), .R2_out(id_ex_1_r2_out),
    .RegWrite_out(EX_RegWrite), .Imm_out(id_ex_1_imm_out), .JAL_out(id_ex_1_jal_out),
    .Address_out(id_ex_1_address_out), .RegDst_out(id_ex_1_regdst_out), .AluOP_out(id_ex_1_aluop_out),
    .Syscall_out(id_ex_1_syscall_out), .Shamt_out(id_ex_1_shamt_out), .JMP_out(JMP), .JR_out(JR),
    .LH_out(id_ex_1_lh_out), .SRLV_out(SRLV), .Reset(or_3_out), .Enable(Halt), .CLK(CLK),
    .BEQ_in(\硬布线控制器_1_beq ), .BEQ_out(id_ex_1_beq_out), .BLEZ_in(\硬布线控制器_1_blez ),
    .BLEZ_out(id_ex_1_blez_out), .W__in(multiplexer_8_out), .W__out(EX_WriteReg_num), .PCr_in(ID_PC),
    .PCr_out(EX_PC), .HG_in(if_id_1_hg_out), .HG_out(HG), .PCG_in(if_id_1_pc_g_out));  // open: Halt_in, Halt_out, PCG_out, Interrupt_in, Interrupt_out
  // Probe on WB_PC[11:0]
  or or_4 (\是跳 , id_ex_1_blez_out, id_ex_1_beq_out, id_ex_1_bne_out, and_4_out);
  Multiplexer #(.select(2), .width(32), .enable("false")) multiplexer_9 (
    .in0(id_ex_1_r1_out), .in1(mem_wb_1_alur_out), .in2(mem_wb_1_memd_out), .in3(ex_mem_1_alur_out),
    .out(multiplexer_9_out), .sel(R1_Forward));
  Multiplexer #(.select(2), .width(32), .enable("false")) multiplexer_10 (
    .in0(id_ex_1_r2_out), .in1(mem_wb_1_alur_out), .in2(mem_wb_1_memd_out), .in3(ex_mem_1_alur_out),
    .out(multiplexer_10_out), .sel(R2_Forward));
  Counter #(.width(16), .max('hffff)) counter_4 (
    .count(JMP), .Q(\无条件分支数 ), .clk(CLK), .clr(RST));  // open: load, D, carry
  and and_4 (and_4_out, JMP, ~JR);  // AND_Gate
  Multiplexer #(.width(32), .enable("false")) multiplexer_11 (
    .in0(multiplexer_10_out), .in1(id_ex_1_imm_out), .out(multiplexer_11_out), .sel(id_ex_1_alusrcb_out));
  and and_5 (and_5_out, id_ex_1_syscall_out, comparator_1_eq);
  Comparator #(.width(32)) comparator_1 (.a(32'h22), .b(multiplexer_11_out), .eq(comparator_1_eq));  // open: gt, lt
  not not_4 (not_4_out, comparator_1_eq);
  Register #(.width(32)) register_1 (.D(multiplexer_9_out), .en(and_5_out), .Q(LedData), .clk(CLK), .clr(RST));
  and and_6 (and_6_out, not_4_out, id_ex_1_syscall_out);
  Counter #(.width(16), .max('hffff)) counter_5 (
    .count(BAC), .Q(\条件分支成功数 ), .clk(CLK), .clr(RST));  // open: load, D, carry
  Comparator #(.width(32)) comparator_2 (
    .a(multiplexer_9_out), .b({32{1'b0}}), .eq(comparator_2_eq), .lt(comparator_2_lt));  // open: gt
  MIPS_ALU mips_alu_1 (
    .X(multiplexer_9_out), .Y(multiplexer_11_out), .AluOP(id_ex_1_aluop_out), .Equal(mips_alu_1_equal),
    .Result(mips_alu_1_result), .shamt(multiplexer_12_out));  // open: Result_2
  Multiplexer #(.width(5), .enable("false")) multiplexer_12 (
    .in0(id_ex_1_shamt_out), .in1(multiplexer_9_out[4:0]), .out(multiplexer_12_out), .sel(SRLV));
  Shifter #(.width(32)) shifter_2 (.in(id_ex_1_imm_out), .\dist (5'b00010), .out(shifter_2_out));
  or or_5 (or_5_out, comparator_2_eq, comparator_2_lt);
  and and_7 (and_7_out, or_5_out, id_ex_1_blez_out);
  and and_8 (and_8_out, mips_alu_1_equal, id_ex_1_beq_out);
  not not_5 (not_5_out, mips_alu_1_equal);
  and and_9 (and_9_out, not_5_out, id_ex_1_bne_out);
  Adder #(.width(32)) adder_2 (.a(shifter_2_out), .b(id_ex_1_pc_out), .out(adder_2_out));  // open: cin, cout
  or or_6 (BAC, and_8_out, and_7_out, and_9_out);
  EX_MEM ex_mem_1 (
    .MemToReg_in(id_ex_1_memtoreg_out), .IR_in({EX_OP, id_ex_1_ir_out}), .MemWrite_in(id_ex_1_memwrite_out),
    .PC_in(id_ex_1_pc_out), .RegWrite_in(EX_RegWrite), .R2_in(multiplexer_10_out), .JAL_in(id_ex_1_jal_out),
    .AluR_in(mips_alu_1_result), .RegDst_in(id_ex_1_regdst_out), .Halt_in(and_6_out),
    .Syscall_in(id_ex_1_syscall_out), .LH_in(id_ex_1_lh_out), .MemToReg_out(ex_mem_1_memtoreg_out),
    .IR_out({MEM_OP, ex_mem_1_ir_out}), .MemWrite_out(ex_mem_1_memwrite_out), .PC_out(ex_mem_1_pc_out),
    .RegWrite_out(MEM_RegWrite), .R2_out(ex_mem_1_r2_out), .JAL_out(ex_mem_1_jal_out),
    .AluR_out(ex_mem_1_alur_out), .RegDst_out(ex_mem_1_regdst_out), .Halt_out(ex_mem_1_halt_out),
    .Syscall_out(ex_mem_1_syscall_out), .LH_out(ex_mem_1_lh_out), .Reset(RST), .Enable(Halt), .CLK(CLK),
    .W__in(EX_WriteReg_num), .W__out(MEM_WriteReg_num), .PCr_in(EX_PC), .PCr_out(MEM_PC));  // open: Interrupt_in, Interrupt_out
  Multiplexer #(.width(16), .enable("false")) multiplexer_13 (
    .in0(mips_ram_1_p6), .in1(mips_ram_1_p6_2), .out(multiplexer_13_out), .sel(ex_mem_1_alur_out[1]));
  // MIPS_RAM mips_ram_1: pin names not known; wires that end beside it: ex_mem_1_alur_out[11:2], ex_mem_1_r2_out, ex_mem_1_memwrite_out, CLK, RST, {mips_ram_1_p6_2, mips_ram_1_p6}
  assign bit_extender_4_out = {{16{multiplexer_13_out[15]}}, multiplexer_13_out};  // Bit_Extender bit_extender_4
  \数据相关检测  \u_数据相关检测_1  (
    .OP(OP), .EX_WriteReg_num(EX_WriteReg_num), .EX_RegWrite(EX_RegWrite), .\数据相关 (\数据相关 ),
    .MEM_WriteReg_num(MEM_WriteReg_num), .MEM_RegWrite(MEM_RegWrite), .Func(Func), .Load_Use(LoadUse),
    .ID_R1_num(ID_R1_num), .ID_R2_num(ID_R2_num), .R1_Forward(\数据相关检测_1_r1_forward ),
    .R2_Forward(\数据相关检测_1_r2_forward ), .EX_OP(EX_OP), .MEM_OP(MEM_OP));
  Multiplexer #(.width(32), .enable("false")) multiplexer_14 (
    .in0({mips_ram_1_p6_2, mips_ram_1_p6}), .in1(bit_extender_4_out), .out(multiplexer_14_out),
    .sel(ex_mem_1_lh_out));
  and and_10 (and_10_out, Halt, LoadUse);
  MEM_WB mem_wb_1 (
    .MemToReg_in(ex_mem_1_memtoreg_out), .IR_in({MEM_OP, ex_mem_1_ir_out}), .RegWrite_in(MEM_RegWrite),
    .PC_in(ex_mem_1_pc_out), .JAL_in(ex_mem_1_jal_out), .MemD_in(multiplexer_14_out),
    .RegDst_in(ex_mem_1_regdst_out), .AluR_in(ex_mem_1_alur_out), .Syscall_in(ex_mem_1_syscall_out),
    .Halt_in(ex_mem_1_halt_out), .MemToReg_out(mem_wb_1_memtoreg_out), .IR_out(mem_wb_1_ir_out),
    .RegWrite_out(RegW), .PC_out(mem_wb_1_pc_out), .JAL_out(mem_wb_1_jal_out), .MemD_out(mem_wb_1_memd_out),
    .RegDst_out(mem_wb_1_regdst_out), .AluR_out(mem_wb_1_alur_out), .Syscall_out(SysC),
    .Halt_out(mem_wb_1_halt_out), .Reset(RST), .Enable(Halt), .CLK(CLK), .W__in(MEM_WriteReg_num),
    .PCr_in(MEM_PC), .PCr_out(WB_PC));  // open: W__out, Interrupt_in, Interrupt_out, R2_in, R2_out
  Counter #(.width(16), .max('hffff)) counter_6 (
    .count(and_10_out), .Q(\LoadUse次数 ), .clk(CLK), .clr(RST));  // open: load, D, carry
  Register #(.width(4)) register_2 (
    .D({\数据相关检测_1_r2_forward , \数据相关检测_1_r1_forward }), .Q({R2_Forward, R1_Forward}), .clk(CLK), .clr(RST));  // open: en
  not not_6 (not_6_out, mem_wb_1_halt_out);
  Multiplexer #(.width(32), .enable("false")) multiplexer_15 (
    .in0(mem_wb_1_alur_out), .in1(mem_wb_1_memd_out), .out(multiplexer_15_out), .sel(mem_wb_1_memtoreg_out));
  Multiplexer #(.width(5), .enable("false")) multiplexer_16 (
    .in0(mem_wb_1_ir_out[20:16]), .in1(mem_wb_1_ir_out[15:11]), .out(multiplexer_16_out),
    .sel(mem_wb_1_regdst_out));
  or or_7 (Halt, Go, RST, not_6_out);
  Multiplexer #(.width(32), .enable("false")) multiplexer_17 (
    .in0(multiplexer_15_out), .in1(mem_wb_1_pc_out), .out(multiplexer_17_out), .sel(mem_wb_1_jal_out));
  Multiplexer #(.width(5), .enable("false")) multiplexer_18 (
    .in0(multiplexer_16_out), .in1({5{1'b1}}), .out(multiplexer_18_out), .sel(mem_wb_1_jal_out));

  // Other names for the same wires on the sheet: 插入气泡数[15:0] = \LoadUse次数 

  // Notes on the sheet:
  //   中断源
  //   中断等待指示
  //   数码管输出
  //   指令存储器
  //   contents of rom_1 (hex, n*v repeats v):
  //   20110001 8000c05 20110001 20120002 20130003 8000c09 20110001 20120002 20130003 8000c0d 20110001
  //   20120002 20130003 8000c11 20110001 20120002 20130003 c000cb8 20100001 20110001 118fc0 112020
  //   20020022 c 118882 12200001 8000c15 112020 20020022 c 20110001 118880 112020 20020022 c 12200001
  //   8000c1f 20110001 118fc0 112020 20020022 c 1188c3 112020 20020022 c 118903 112020 20020022 c 118903
  //   112020 20020022 c 118903 112020 20020022 c 118903 112020 20020022 c 118903 112020 20020022 c 118903
  //   112020 20020022 c 118903 112020 20020022 c 20100001 109fc0 139fc3 8021 2012000c 24160003 26100001
  //   3210000f 20080008 20090001 139900 2709825 132020 20020022 c 1094022 1500fff9 22100001 2018000f
  //   2188024 108700 20080008 20090001 139902 2709825 132021 20020022 c 1094022 1500fff9 108702 2c9b022
  //   12c00001 8000c50 4020 1084027 84400 3508ffff 82021 20020022 c 2010ffff 20110000 ae300000 22100001
  //   22310004 ae300000 22100001 22310004 ae300000 22100001 22310004 ae300000 22100001 22310004 ae300000
  //   22100001 22310004 ae300000 22100001 22310004 ae300000 22100001 22310004 ae300000 22100001 22310004
  //   ae300000 22100001 22310004 ae300000 22100001 22310004 ae300000 22100001 22310004 ae300000 22100001
  //   22310004 ae300000 22100001 22310004 ae300000 22100001 22310004 ae300000 22100001 22310004 ae300000
  //   22100001 22310004 22100001 8020 2011003c 8e130000 8e340000 274402a 11000002 ae330000 ae140000
  //   2231fffc 1611fff8 102020 20020022 c 22100004 2011003c 1611fff2 20020032 c 20100000 22100001 102020
  //   20020022 c 22100002 102020 20020022 c 22100003 102020 20020022 c 22100004 102020 20020022 c 22100005
  //   102020 20020022 c 22100006 102020 20020022 c 22100007 102020 20020022 c 22100008 102020 20020022
  //   20020022 c 3e00008
  //   指令字
  //   OP
  //   Func
  //   rs
  //   rt
  //   rd
  //   Shamt
  //   JMP
  //   JR
  //   BLEZ
  //   Syscall
  //   $a0
  //   $v0
  //   Beq
  //   Bne
  //   MemToReg
  //   MemWrite
  //   AluOP
  //   AluSrcB
  //   RegWrite
  //   JAL
  //   RegDst
  //   流水调试日志用
  //   rt
  //   rd
  //   W#
  //   Din
endmodule

module \分支状态  (
  input  X1,
  input  X0,
  input  JumpSces,
  output Y1,
  output Y0
);

  wire and_1_out, and_2_out, and_3_out, and_4_out, not_1_out, not_2_out, not_3_out, not_4_out, not_5_out;

  not not_1 (not_1_out, X0);
  not not_2 (not_2_out, X1);
  not not_3 (not_3_out, X0);
  not not_4 (not_4_out, X0);
  not not_5 (not_5_out, JumpSces);
  and and_1 (and_1_out, X0, JumpSces);
  and and_2 (and_2_out, X1, not_1_out);
  and and_3 (and_3_out, not_2_out, not_3_out, JumpSces);
  and and_4 (and_4_out, X1, not_4_out, not_5_out);
  or or_1 (Y1, and_1_out, and_2_out);
  or or_2 (Y0, and_3_out, and_4_out);
endmodule

// 分支预测
module NPC (
  input  CLK,
  input  EX_Hit,
  input  [31:0] EX_PC,
  input  [31:0] IR,
  input  [31:0] EX_PC_4,
  input  RST,
  input  [31:0] PC_4,
  input  EX_JR,
  input  Enable,
  input  EX_isJump,
  input  EX_GuessJ,
  input  [31:0] EX_REG,
  input  [31:0] EX_Addr,
  input  [31:0] PC,
  input  EX_JumpSucc,
  output GuessSucc,
  output [31:0] PCOut,
  output GuessFail,
  output GuessJ,
  output Hit
);

  wire and_1_out, and_6_out, and_7_out, and_9_out, and_10_out, and_11_out, and_12_out, and_13_out, B, isJump,
       J, Miss, multiplexer_8_out, not_1_out, or_2_out, StatusHit;
  wire [1:0] and_4_out, bht_1_idstatusout, bht_1_statusout, \分支状态_1_y0 ;
  wire [31:0] GuessAddr, multiplexer_1_out, multiplexer_3_out, multiplexer_4_out, multiplexer_5_out,
       multiplexer_6_out, PC_Guess, \分支超前生成_1_baddr , \分支超前生成_1_jaddr ;

  \分支超前生成  \u_分支超前生成_1  (.IR(IR), .PC(PC_4), .JAddr(\分支超前生成_1_jaddr ), .BAddr(\分支超前生成_1_baddr ), .B(B), .J(J));
  or or_1 (isJump, J, B);
  and and_1 (and_1_out, EX_GuessJ, EX_JumpSucc);
  not not_1 (not_1_out, and_1_out);
  Multiplexer #(.width(32), .enable("false")) multiplexer_1 (
    .in0(PC_4), .in1(\分支超前生成_1_baddr ), .out(multiplexer_1_out), .sel(B));
  Multiplexer #(.width(32), .enable("false")) multiplexer_2 (
    .in0(multiplexer_1_out), .in1(\分支超前生成_1_jaddr ), .out(GuessAddr), .sel(J));
  or or_2 (or_2_out, J, B);
  // AND_Gate and_2 has open pins: in0=EX_Hit, in1=not_1_out, out=open
  // AND_Gate and_3 has open pins: in0=and_1_out, in1=EX_Hit, out=open
  and and_4 (and_4_out[0], B, Miss);
  and and_5 (and_4_out[1], Miss, or_2_out);
  and and_6 (and_6_out, EX_JumpSucc, ~EX_GuessJ);  // AND_Gate
  and and_7 (and_7_out, EX_GuessJ, ~EX_JumpSucc);  // AND_Gate
  and and_8 (GuessSucc, EX_GuessJ, EX_JumpSucc);
  and and_9 (and_9_out, isJump, ~Hit);  // AND_Gate
  Multiplexer #(.width(32), .enable("false")) multiplexer_3 (
    .in0(PC_4), .in1(GuessAddr), .out(multiplexer_3_out), .sel(and_9_out));
  or or_3 (GuessFail, and_6_out, and_7_out);
  and and_10 (and_10_out, Hit, GuessJ);
  Multiplexer #(.width(32), .enable("false")) multiplexer_4 (
    .in0(EX_Addr), .in1(EX_PC_4), .out(multiplexer_4_out), .sel(and_11_out));
  and and_11 (and_11_out, EX_GuessJ, ~EX_JumpSucc);  // AND_Gate
  and and_12 (and_12_out, Miss, isJump);
  \分支状态  \u_分支状态_1  (
    .X1(bht_1_statusout[1]), .X0(bht_1_statusout[0]), .JumpSces(EX_JumpSucc), .Y1(\分支状态_1_y0 [1]),
    .Y0(\分支状态_1_y0 [0]));
  Multiplexer #(.width(32), .enable("false")) multiplexer_5 (
    .in0(multiplexer_3_out), .in1(PC_Guess), .out(multiplexer_5_out), .sel(and_10_out));
  Multiplexer #(.width(32), .disabled(0), .enable("false")) multiplexer_6 (
    .in0(multiplexer_5_out), .in1(multiplexer_4_out), .out(multiplexer_6_out), .sel(GuessFail));
  BHT bht_1 (
    .TorgetAddrIn(GuessAddr), .PC(PC), .PCReady(and_12_out), .CLK(CLK), .Enable(Enable), .Miss(Miss),
    .AddrOut(PC_Guess), .RST(RST), .EX_PC(EX_PC), .StatusOut(bht_1_statusout), .StatusReady(EX_isJump),
    .NewStatusIn(and_4_out), .Hit(Hit), .StatusHit(StatusHit), .StatusIn(\分支状态_1_y0 ),
    .IDStatusOut(bht_1_idstatusout));
  Multiplexer #(.width(32), .enable("false")) multiplexer_7 (
    .in0(multiplexer_6_out), .in1(EX_REG), .out(PCOut), .sel(EX_JR));
  Multiplexer #(.enable("false")) multiplexer_8 (
    .in0(1'b0), .in1(bht_1_idstatusout[1]), .out(multiplexer_8_out), .sel(Hit));
  and and_13 (and_13_out, isJump, ~Hit);  // AND_Gate
  or or_4 (GuessJ, multiplexer_8_out, and_13_out);

  // Notes on the sheet:
  //   输入引脚区
  //   J、B指令更新BHT
  //   成功失败
  //   B指令初始状态为11
  //   J指令初始状态为10
  //   输出引脚区
endmodule

// 超前
module \分支超前生成  (
  input  [31:0] IR,
  input  [31:0] PC,
  output [31:0] JAddr,
  output [31:0] BAddr,
  output B,
  output J
);

  wire not_1_out, \硬布线控制器_1_beq , \硬布线控制器_1_blez , \硬布线控制器_1_bne , \硬布线控制器_1_jmp , \硬布线控制器_1_jr ;
  wire [31:0] bit_extender_1_out, bit_extender_2_out, shifter_1_out;

  and and_1 (J, \硬布线控制器_1_jmp , not_1_out);
  not not_1 (not_1_out, \硬布线控制器_1_jr );
  \硬布线控制器  \u_硬布线控制器_1  (
    .Func(IR[5:0]), .OP(IR[31:26]), .JR(\硬布线控制器_1_jr ), .JMP(\硬布线控制器_1_jmp ), .Beq(\硬布线控制器_1_beq ),
    .Bne(\硬布线控制器_1_bne ), .BLEZ(\硬布线控制器_1_blez ));  // open: ALU_OP, MemToReg, MemWrite, ALU_SRC, RegWrite, SysCALL, SignedExt, RegDst, JAL, LH, SRLV, ERET, MFC0, MTC0, MF
  assign bit_extender_1_out = {{16{IR[15]}}, IR[15:0]};  // Bit_Extender bit_extender_1
  assign bit_extender_2_out = {{6{IR[25]}}, IR[25:0]};  // Bit_Extender bit_extender_2
  or or_1 (B, \硬布线控制器_1_beq , \硬布线控制器_1_blez , \硬布线控制器_1_bne );
  Shifter #(.width(32)) shifter_1 (.in(bit_extender_1_out), .\dist (5'b00010), .out(shifter_1_out));
  Shifter #(.width(32)) shifter_2 (.in(bit_extender_2_out), .\dist (5'b00010), .out(JAddr));
  Adder #(.width(32)) adder_1 (.a(shifter_1_out), .b(PC), .out(BAddr));  // open: cin, cout

  // Notes on the sheet:
  //   输入引脚区
  //   OP
  //   Func
  //   输出引脚区
endmodule

module \单级中断  (
);

  wire and_1_out, and_2_out, and_3_out, and_4_out, and_5_out, and_7_out, and_8_out, and_9_out, BAC, CLK,
       comparator_1_eq, comparator_2_eq, comparator_2_lt, counter_1_q, d_ff_1_q, d_ff_2_q, d_ff_3_q,
       decoder_1_out1, decoder_1_out2, decoder_1_out3, Enable, ERET, Go, IE_q, Interr, Interr1, Interr2,
       Interr3, IR, IR1, IR2, IR3, JMP, LH, mips_alu_1_equal, not_3_out, not_4_out, or_4_out, or_5_out,
       or_6_out, or_7_out, or_8_out, or_9_out, RST, Rst1, Rst2, Rst3, SignedExt, SRLV, Stop, W1, W2, W3,
       \硬布线控制器_1_alu_src , \硬布线控制器_1_beq , \硬布线控制器_1_blez , \硬布线控制器_1_bne , \硬布线控制器_1_jal , \硬布线控制器_1_jr ,
       \硬布线控制器_1_memtoreg , \硬布线控制器_1_memwrite , \硬布线控制器_1_regdst , \硬布线控制器_1_regwrite , \硬布线控制器_1_syscall ;
  wire [1:0] priority_encoder_1_out, \中断号_q ;
  wire [3:0] \硬布线控制器_1_alu_op ;
  wire [4:0] mips_regifile_1_r1, multiplexer_6_out, multiplexer_7_out, multiplexer_8_out, multiplexer_9_out,
       multiplexer_14_out, rom_1_data_2;
  wire [15:0] mips_ram_1_p6, mips_ram_1_p6_2, multiplexer_15_out, \总周期数 , \无条件分支数 , \条件分支成功数 ;
  wire [31:0] adder_1_out, adder_2_out, bit_extender_1_out, bit_extender_2_out, bit_extender_3_out,
       bit_extender_4_out, EPC, InterruptAddr, LedData, mips_alu_1_result, mips_regifile_1_r2,
       multiplexer_1_out, multiplexer_2_out, multiplexer_3_out, multiplexer_4_out, multiplexer_5_out,
       multiplexer_10_out, multiplexer_11_out, multiplexer_12_out, multiplexer_16_out, multiplexer_17_out,
       PC, rom_1_data, shifter_1_out, shifter_2_out;
  wire [31:5] mips_regifile_1_r1_2;

  Button \u_总复位  (.out(RST));
  Button \u_继续运行  (.out(Go));
  Clock clock_1 (.out(CLK));
  Button _1 (.out(IR1));
  Button _2 (.out(IR2));
  Button _3 (.out(IR3));
  LED led_1 (.in(W1));
  LED led_2 (.in(W2));
  LED led_3 (.in(W3));
  Multiplexer #(.width(32), .enable("false")) multiplexer_1 (
    .in0(adder_1_out), .in1(adder_2_out), .out(multiplexer_1_out), .sel(BAC));
  // Probe on multiplexer_2_out[11:0]
  Multiplexer #(.width(32), .enable("false")) multiplexer_2 (
    .in0(shifter_1_out), .in1({mips_regifile_1_r1_2, mips_regifile_1_r1}), .out(multiplexer_2_out),
    .sel(\硬布线控制器_1_jr ));
  Hex_Digit_Display hex_digit_display_1 (.value(LedData[31:28]));  // open: dp
  Hex_Digit_Display hex_digit_display_2 (.value(LedData[27:24]));  // open: dp
  Multiplexer #(.width(32), .enable("false")) multiplexer_3 (
    .in0(multiplexer_1_out), .in1(multiplexer_2_out), .out(multiplexer_3_out), .sel(JMP));
  or or_1 (W1, Interr1, d_ff_1_q);
  or or_2 (W2, Interr2, d_ff_2_q);
  or or_3 (W3, Interr3, d_ff_3_q);
  Hex_Digit_Display hex_digit_display_3 (.value(LedData[19:16]));  // open: dp
  Hex_Digit_Display hex_digit_display_4 (.value(LedData[23:20]));  // open: dp
  Multiplexer #(.width(32), .enable("false")) multiplexer_4 (
    .in0(multiplexer_3_out), .in1(InterruptAddr), .out(multiplexer_4_out), .sel(IR));
  Multiplexer #(.width(32), .enable("false")) multiplexer_5 (
    .in0(multiplexer_4_out), .in1(EPC), .out(multiplexer_5_out), .sel(ERET));
  D_Flip_Flop d_ff_1 (.clk(IR1), .D(1'b1), .Q(d_ff_1_q), .reset(Interr1));  // open: Qn, preset, en
  D_Flip_Flop d_ff_2 (.clk(IR2), .D(1'b1), .Q(d_ff_2_q), .reset(Interr2));  // open: Qn, preset, en
  D_Flip_Flop d_ff_3 (.clk(IR3), .D(1'b1), .Q(d_ff_3_q), .reset(Interr3));  // open: Qn, preset, en
  Hex_Digit_Display hex_digit_display_5 (.value(LedData[15:12]));  // open: dp
  Hex_Digit_Display hex_digit_display_6 (.value(LedData[11:8]));  // open: dp
  Register #(.width(32)) u_PC (.D(multiplexer_5_out), .en(Enable), .Q(PC), .clk(CLK), .clr(RST));
  or or_4 (or_4_out, d_ff_1_q, Interr1);
  or or_5 (or_5_out, d_ff_2_q, Interr2);
  or or_6 (or_6_out, d_ff_3_q, Interr3);
  Hex_Digit_Display hex_digit_display_7 (.value(LedData[3:0]));  // open: dp
  Hex_Digit_Display hex_digit_display_8 (.value(LedData[7:4]));  // open: dp
  Counter #(.width(1), .max('h1)) counter_1 (
    .D(\硬布线控制器_1_syscall ), .count(and_1_out), .Q(counter_1_q), .clk(CLK), .clr(or_7_out));  // open: load, carry
  and and_1 (and_1_out, Stop, \硬布线控制器_1_syscall );
  and and_2 (and_2_out, or_4_out, ~Rst1);  // AND_Gate
  and and_3 (and_3_out, or_5_out, ~Rst2);  // AND_Gate
  and and_4 (and_4_out, or_6_out, ~Rst3);  // AND_Gate
  not not_1 (Enable, counter_1_q);
  or or_7 (or_7_out, RST, Go);
  ROM #(.addrWidth(10), .dataWidth(32)) rom_1 (
    .addr(PC[11:2]), .data({rom_1_data[31:11], rom_1_data_2, rom_1_data[5:0]}));  // open: sel
  Adder #(.width(32)) adder_1 (.a(PC), .b(32'h4), .out(adder_1_out));  // open: cin, cout
  D_Flip_Flop u_IR1 (.clk(CLK), .D(and_2_out), .Q(Interr1));  // open: Qn, preset, en, reset
  D_Flip_Flop u_IR2 (.clk(CLK), .D(and_3_out), .Q(Interr2));  // open: Qn, preset, en, reset
  D_Flip_Flop u_IR3 (.clk(CLK), .D(and_4_out), .Q(Interr3));  // open: Qn, preset, en, reset
  // Probe on \总周期数 
  // Probe on \无条件分支数 
  // Probe on \条件分支成功数 
  \硬布线控制器  \u_硬布线控制器_1  (
    .Func(rom_1_data[5:0]), .OP(rom_1_data[31:26]), .ALU_OP(\硬布线控制器_1_alu_op ),
    .MemToReg(\硬布线控制器_1_memtoreg ), .MemWrite(\硬布线控制器_1_memwrite ), .ALU_SRC(\硬布线控制器_1_alu_src ),
    .RegWrite(\硬布线控制器_1_regwrite ), .SysCALL(\硬布线控制器_1_syscall ), .SignedExt(SignedExt),
    .RegDst(\硬布线控制器_1_regdst ), .JR(\硬布线控制器_1_jr ), .JMP(JMP), .Beq(\硬布线控制器_1_beq ), .JAL(\硬布线控制器_1_jal ),
    .Bne(\硬布线控制器_1_bne ), .LH(LH), .BLEZ(\硬布线控制器_1_blez ), .SRLV(SRLV), .ERET(ERET));  // open: MFC0, MTC0, MF
  Multiplexer #(.width(5), .enable("false")) multiplexer_6 (
    .in0(rom_1_data[20:16]), .in1(rom_1_data[15:11]), .out(multiplexer_6_out), .sel(\硬布线控制器_1_regdst ));
  assign bit_extender_1_out = {{16{1'b0}}, {rom_1_data[15:11], rom_1_data_2, rom_1_data[5:0]}};  // Bit_Extender bit_extender_1
  assign bit_extender_2_out = {{16{rom_1_data[15]}}, {rom_1_data[15:11], rom_1_data_2, rom_1_data[5:0]}};  // Bit_Extender bit_extender_2
  assign bit_extender_3_out = {{6{rom_1_data[25]}}, {rom_1_data[25:11], rom_1_data_2, rom_1_data[5:0]}};  // Bit_Extender bit_extender_3
  Multiplexer #(.width(5), .enable("false")) multiplexer_7 (
    .in0(rom_1_data[25:21]), .in1(5'b00100), .out(multiplexer_7_out), .sel(\硬布线控制器_1_syscall ));
  Multiplexer #(.width(5), .enable("false")) multiplexer_8 (
    .in0(rom_1_data[20:16]), .in1(5'b00010), .out(multiplexer_8_out), .sel(\硬布线控制器_1_syscall ));
  Multiplexer #(.width(5), .enable("false")) multiplexer_9 (
    .in0(multiplexer_6_out), .in1({5{1'b1}}), .out(multiplexer_9_out), .sel(\硬布线控制器_1_jal ));
  Multiplexer #(.width(32), .enable("false")) multiplexer_10 (
    .in0(bit_extender_1_out), .in1(bit_extender_2_out), .out(multiplexer_10_out), .sel(SignedExt));
  Multiplexer #(.width(32), .enable("false")) multiplexer_11 (
    .in0(multiplexer_17_out), .in1(adder_1_out), .out(multiplexer_11_out), .sel(\硬布线控制器_1_jal ));
  Shifter #(.width(32)) shifter_1 (.in(bit_extender_3_out), .\dist (5'b00010), .out(shifter_1_out));
  Priority_Encoder #(.select(2)) priority_encoder_1 (
    .in0(1'b0), .in1(Interr1), .in2(Interr2), .in3(Interr3), .out(priority_encoder_1_out), .gs(Interr));  // open: en_out, en_in
  Counter #(.width(16), .max('hffff)) counter_2 (
    .count(Enable), .Q(\总周期数 ), .clk(CLK), .clr(RST));  // open: load, D, carry
  not not_2 (Stop, comparator_1_eq);
  and and_5 (and_5_out, comparator_1_eq, \硬布线控制器_1_syscall );
  MIPS_Regifile mips_regifile_1 (
    .Din(multiplexer_11_out), .Clk(CLK), .R1({mips_regifile_1_r1_2, mips_regifile_1_r1}),
    .R2(mips_regifile_1_r2), .WE(\硬布线控制器_1_regwrite ), .W_num(multiplexer_9_out), .R1_num(multiplexer_7_out),
    .R2_num(multiplexer_8_out));
  Shifter #(.width(32)) shifter_2 (.in(multiplexer_10_out), .\dist (5'b00010), .out(shifter_2_out));
  or or_8 (or_8_out, ERET, IR);
  Register #(.width(32)) register_1 (
    .D({mips_regifile_1_r1_2, mips_regifile_1_r1}), .en(and_5_out), .Q(LedData), .clk(CLK), .clr(RST));
  Comparator #(.width(32)) comparator_1 (.a(32'h22), .b(mips_regifile_1_r2), .eq(comparator_1_eq));  // open: gt, lt
  Multiplexer #(.width(32), .enable("false")) multiplexer_12 (
    .in0(mips_regifile_1_r2), .in1(multiplexer_10_out), .out(multiplexer_12_out), .sel(\硬布线控制器_1_alu_src ));
  Adder #(.width(32)) adder_2 (.a(shifter_2_out), .b(adder_1_out), .out(adder_2_out));  // open: cin, cout
  Register #(.width(32)) u_EPC (.D(PC), .en(IR), .Q(EPC), .clk(CLK));  // open: clr
  not not_3 (not_3_out, IE_q);
  Register #(.width(1)) IE (.D(IR), .en(or_8_out), .Q(IE_q), .clk(CLK));  // open: clr
  Multiplexer #(.select(2), .width(32), .enable("false")) multiplexer_13 (
    .in1(32'h4), .in2(32'h1c8), .in3(32'h38c), .out(InterruptAddr), .sel(priority_encoder_1_out));  // open: in0
  Multiplexer #(.width(5), .enable("false")) multiplexer_14 (
    .in0(rom_1_data_2), .in1(mips_regifile_1_r1), .out(multiplexer_14_out), .sel(SRLV));
  and and_6 (IR, not_3_out, Interr);
  Counter #(.width(16), .max('hffff)) counter_3 (
    .count(JMP), .Q(\无条件分支数 ), .clk(CLK), .clr(RST));  // open: load, D, carry
  Comparator #(.width(32)) comparator_2 (
    .a({mips_regifile_1_r1_2, mips_regifile_1_r1}), .b({32{1'b0}}), .eq(comparator_2_eq), .lt(comparator_2_lt));  // open: gt
  or or_9 (or_9_out, comparator_2_eq, comparator_2_lt);
  not not_4 (not_4_out, mips_alu_1_equal);
  MIPS_ALU mips_alu_1 (
    .X({mips_regifile_1_r1_2, mips_regifile_1_r1}), .Y(multiplexer_12_out), .AluOP(\硬布线控制器_1_alu_op ),
    .Equal(mips_alu_1_equal), .Result(mips_alu_1_result), .shamt(multiplexer_14_out));  // open: Result_2
  Register #(.width(2)) \u_中断号  (.D(priority_encoder_1_out), .en(IR), .Q(\中断号_q ), .clk(CLK));  // open: clr
  and and_7 (and_7_out, or_9_out, \硬布线控制器_1_blez );
  and and_8 (and_8_out, mips_alu_1_equal, \硬布线控制器_1_beq );
  and and_9 (and_9_out, not_4_out, \硬布线控制器_1_bne );
  Multiplexer #(.width(16), .enable("false")) multiplexer_15 (
    .in0(mips_ram_1_p6), .in1(mips_ram_1_p6_2), .out(multiplexer_15_out), .sel(mips_alu_1_result[1]));
  Decoder #(.select(2), .enable("false")) decoder_1 (
    .out1(decoder_1_out1), .out2(decoder_1_out2), .out3(decoder_1_out3), .sel(\中断号_q ));  // open: out0
  Counter #(.width(16), .max('hffff)) counter_4 (
    .count(BAC), .Q(\条件分支成功数 ), .clk(CLK), .clr(RST));  // open: load, D, carry
  or or_10 (BAC, and_8_out, and_7_out, and_9_out);
  // MIPS_RAM mips_ram_1: pin names not known; wires that end beside it: mips_alu_1_result[11:2], mips_regifile_1_r2, \硬布线控制器_1_memwrite , CLK, RST, {mips_ram_1_p6_2, mips_ram_1_p6}
  assign bit_extender_4_out = {{16{multiplexer_15_out[15]}}, multiplexer_15_out};  // Bit_Extender bit_extender_4
  Multiplexer #(.width(32), .enable("false")) multiplexer_16 (
    .in0({mips_ram_1_p6_2, mips_ram_1_p6}), .in1(bit_extender_4_out), .out(multiplexer_16_out), .sel(LH));
  and and_10 (Rst1, decoder_1_out1, ERET);
  and and_11 (Rst2, decoder_1_out2, ERET);
  and and_12 (Rst3, decoder_1_out3, ERET);
  Multiplexer #(.width(32), .enable("false")) multiplexer_17 (
    .in0(mips_alu_1_result), .in1(multiplexer_16_out), .out(multiplexer_17_out), .sel(\硬布线控制器_1_memtoreg ));

  // Notes on the sheet:
  //   中断源
  //   中断等待指示
  //   数码管输出
  //   Reset 
  //   Reset 
  //   Reset 
  //   指令存储器
  //   contents of rom_1 (hex, n*v repeats v):
  //   8000d54 23bdfffc afa10000 23bdfffc afa20000 23bdfffc afa30000 23bdfffc afa40000 23bdfffc afa50000
  //   23bdfffc afa60000 23bdfffc afa70000 23bdfffc afa80000 23bdfffc afa90000 23bdfffc afaa0000 23bdfffc
  //   afab0000 23bdfffc afac0000 23bdfffc afad0000 23bdfffc afae0000 23bdfffc afaf0000 23bdfffc afb00000
  //   23bdfffc afb10000 23bdfffc afb20000 23bdfffc afb30000 23bdfffc afb40000 23bdfffc afb50000 23bdfffc
  //   afb60000 23bdfffc afb70000 23bdfffc afb80000 23bdfffc afb90000 20160001 20140006 20150001 168020
  //   108100 2149825 132020 20020022 c 1600fffa 295a022 1680fff7 8fb90000 23bd0004 8fb80000 23bd0004
  //   8fb70000 23bd0004 8fb60000 23bd0004 8fb50000 23bd0004 8fb40000 23bd0004 8fb30000 23bd0004 8fb20000
  //   23bd0004 8fb10000 23bd0004 8fb00000 23bd0004 8faf0000 23bd0004 8fae0000 23bd0004 8fad0000 23bd0004
  //   8fac0000 23bd0004 8fab0000 23bd0004 8faa0000 23bd0004 8fa90000 23bd0004 8fa80000 23bd0004 8fa70000
  //   23bd0004 8fa60000 23bd0004 8fa50000 23bd0004 8fa40000 23bd0004 8fa30000 23bd0004 8fa20000 23bd0004
  //   8fa10000 23bd0004 42000018 23bdfffc afa10000 23bdfffc afa20000 23bdfffc afa30000 23bdfffc afa40000
  //   23bdfffc afa50000 23bdfffc afa60000 23bdfffc afa70000 23bdfffc afa80000 23bdfffc afa90000 23bdfffc
  //   afaa0000 23bdfffc afab0000 23bdfffc afac0000 23bdfffc afad0000 23bdfffc afae0000 23bdfffc afaf0000
  //   23bdfffc afb00000 23bdfffc afb10000 23bdfffc afb20000 23bdfffc afb30000 23bdfffc afb40000 23bdfffc
  //   afb50000 23bdfffc afb60000 23bdfffc afb70000 23bdfffc afb80000 23bdfffc afb90000 20160002 20140006
  //   20150001 168020 108100 2149825 132020 20020022 c 1600fffa 295a022 1680fff7 8fb90000 23bd0004
  //   8fb80000 23bd0004 8fb70000 23bd0004 8fb60000 23bd0004 8fb50000 23bd0004 8fb40000 23bd0004 8fb30000
  //   23bd0004 8fb20000 23bd0004 8fb10000 23bd0004 8fb00000 23bd0004 8faf0000 23bd0004 8fae0000 23bd0004
  //   8fad0000 23bd0004 8fac0000 23bd0004 8fab0000 23bd0004 8faa0000 23bd0004 8fa90000 23bd0004 8fa80000
  //   23bd0004 8fa70000 23bd0004 8fa60000 23bd0004 8fa50000 23bd0004 8fa40000 23bd0004 8fa30000 23bd0004
  //   8fa20000 23bd0004 8fa10000 23bd0004 42000018 23bdfffc afa10000 23bdfffc afa20000 23bdfffc afa30000
  //   23bdfffc afa40000 23bdfffc afa50000 23bdfffc afa60000 23bdfffc afa70000 23bdfffc afa80000 23bdfffc
  //   afa90000 23bdfffc afaa0000 23bdfffc afab0000 23bdfffc afac0000 23bdfffc afad0000 23bdfffc afae0000
  //   23bdfffc afaf0000 23bdfffc afb00000 23bdfffc afb10000 23bdfffc afb20000 23bdfffc afb30000 23bdfffc
  //   afb40000 23bdfffc afb50000 23bdfffc afb60000 23bdfffc afb70000 23bdfffc afb80000 23bdfffc afb90000
  //   20160003 20140006 20150001 168020 108100 2149825 132020 20020022 c 1600fffa 295a022 1680fff7
  //   8fb90000 23bd0004 8fb80000 23bd0004 8fb70000 23bd0004 8fb60000 23bd0004 8fb50000 23bd0004 8fb40000
  //   23bd0004 8fb30000 23bd0004 8fb20000 23bd0004 8fb10000 23bd0004 8fb00000 23bd0004 8faf0000 23bd0004
  //   8fae0000 23bd0004 8fad0000 23bd0004 8fac0000 23bd0004 8fab0000 23bd0004 8faa0000 23bd0004 8fa90000
  //   23bd0004 8fa80000 23bd0004 8fa70000 23bd0004 8fa60000 23bd0004 8fa50000 23bd0004 8fa40000 23bd0004
  //   8fa30000 23bd0004 8fa20000 23bd0004 8fa10000 23bd0004 42000018 20110200 20020022 112020 c 2231ffff
  //   1620fffc 4*0 2002000a c 2002000a c
  //   BLEZ
  //   OP
  //   Func
  //   rs
  //   指令字
  //   rt
  //   rd
  //   Shamt
  //   JMP
  //   JR
  //   OP
  //   Func
  //   Syscall
  //   $a0
  //   $v0
  //   Beq
  //   Bne
  //   MemToReg
  //   MemWrite
  //   AluOP
  //   AluSrcB
  //   RegWrite
  //   JAL
  //   RegDst
  //   COP0
endmodule

module \多级中断  (
);

  wire and_1_out, and_2_out, and_3_out, and_4_out, and_5_out, and_9_out, and_10_out, and_11_out, and_12_out,
       and_13_out, and_14_out, and_15_out, and_17_out, and_18_out, and_19_out, BAC, CLK, comparator_1_eq,
       comparator_2_eq, comparator_3_eq, comparator_4_eq, comparator_5_eq, comparator_5_lt, counter_1_q,
       d_ff_1_q, d_ff_2_q, d_ff_3_q, d_ff_4_qn, d_ff_5_qn, d_ff_6_qn, d_ff_7_qn, decoder_1_out1,
       decoder_1_out2, decoder_1_out3, Enable, ERET, Go, IE_q, Interr, Interr1, Interr2, Interr3, IR, IR1,
       IR2, IR3, JMP, LH, MFC0, mips_alu_1_equal, MTC0, multiplexer_6_out, multiplexer_7_out,
       multiplexer_8_out, multiplexer_9_out, multiplexer_18_out, not_2_out, not_4_out, not_5_out, or_4_out,
       or_5_out, or_6_out, or_7_out, or_8_out, or_9_out, or_10_out, priority_encoder_1_gs, RST, Rst1, Rst2,
       Rst3, SignedExt, SRLV, Stop, W1, W2, W3, \硬布线控制器_1_alu_src , \硬布线控制器_1_beq , \硬布线控制器_1_blez ,
       \硬布线控制器_1_bne , \硬布线控制器_1_jal , \硬布线控制器_1_jr , \硬布线控制器_1_memtoreg , \硬布线控制器_1_memwrite ,
       \硬布线控制器_1_regdst , \硬布线控制器_1_regwrite , \硬布线控制器_1_syscall ;
  wire [1:0] priority_encoder_1_out, priority_encoder_2_out;
  wire [3:0] \屏蔽字 , \硬布线控制器_1_alu_op ;
  wire [4:0] multiplexer_10_out, multiplexer_11_out, multiplexer_12_out, multiplexer_13_out,
       multiplexer_23_out, rd, rt;
  wire [15:0] mips_ram_1_p6, mips_ram_1_p6_2, multiplexer_24_out, \总周期数 , \无条件分支数 , \条件分支成功数 ;
  wire [31:0] adder_1_out, adder_2_out, bit_extender_1_out, bit_extender_2_out, bit_extender_3_out,
       bit_extender_4_out, COP0_Data, EPC, EPC_out, IE_out, InterruptAddr, LedData, mips_alu_1_result,
       mips_regifile_1_r1, mips_regifile_1_r2, multiplexer_1_out, multiplexer_2_out, multiplexer_3_out,
       multiplexer_4_out, multiplexer_5_out, multiplexer_14_out, multiplexer_15_out, multiplexer_16_out,
       multiplexer_17_out, multiplexer_20_out, multiplexer_25_out, multiplexer_26_out, PC, R2, rom_1_data,
       shifter_1_out, shifter_2_out, \屏蔽字_out ;

  Button \u_总复位  (.out(RST));
  Button \u_继续运行  (.out(Go));
  Clock clock_1 (.out(CLK));
  Button _1 (.out(IR1));
  Button _2 (.out(IR2));
  Button _3 (.out(IR3));
  LED led_1 (.in(W1));
  LED led_2 (.in(W2));
  LED led_3 (.in(W3));
  Multiplexer #(.width(32), .enable("false")) multiplexer_1 (
    .in0(adder_1_out), .in1(adder_2_out), .out(multiplexer_1_out), .sel(BAC));
  // Probe on multiplexer_2_out[11:0]
  Multiplexer #(.width(32), .enable("false")) multiplexer_2 (
    .in0(shifter_1_out), .in1(mips_regifile_1_r1), .out(multiplexer_2_out), .sel(\硬布线控制器_1_jr ));
  Hex_Digit_Display hex_digit_display_1 (.value(LedData[27:24]));  // open: dp
  Hex_Digit_Display hex_digit_display_2 (.value(LedData[31:28]));  // open: dp
  Multiplexer #(.width(32), .enable("false")) multiplexer_3 (
    .in0(multiplexer_1_out), .in1(multiplexer_2_out), .out(multiplexer_3_out), .sel(JMP));
  or or_1 (W1, Interr1, d_ff_1_q);
  or or_2 (W2, Interr2, d_ff_2_q);
  or or_3 (W3, Interr3, d_ff_3_q);
  Hex_Digit_Display hex_digit_display_3 (.value(LedData[23:20]));  // open: dp
  Hex_Digit_Display hex_digit_display_4 (.value(LedData[19:16]));  // open: dp
  Multiplexer #(.width(32), .enable("false")) multiplexer_4 (
    .in0(multiplexer_3_out), .in1(InterruptAddr), .out(multiplexer_4_out), .sel(IR));
  Multiplexer #(.width(32), .enable("false")) multiplexer_5 (
    .in0(multiplexer_4_out), .in1(EPC), .out(multiplexer_5_out), .sel(ERET));
  D_Flip_Flop d_ff_1 (.clk(IR1), .D(1'b1), .Q(d_ff_1_q), .reset(Interr1));  // open: Qn, preset, en
  D_Flip_Flop d_ff_2 (.clk(IR2), .D(1'b1), .Q(d_ff_2_q), .reset(Interr2));  // open: Qn, preset, en
  D_Flip_Flop d_ff_3 (.clk(IR3), .D(1'b1), .Q(d_ff_3_q), .reset(Interr3));  // open: Qn, preset, en
  Priority_Encoder #(.select(2)) priority_encoder_1 (
    .in0(1'b0), .in1(Interr1), .in2(Interr2), .in3(Interr3), .out(priority_encoder_1_out),
    .gs(priority_encoder_1_gs));  // open: en_out, en_in
  Hex_Digit_Display hex_digit_display_5 (.value(LedData[11:8]));  // open: dp
  Hex_Digit_Display hex_digit_display_6 (.value(LedData[15:12]));  // open: dp
  Register #(.width(32)) u_PC (.D(multiplexer_5_out), .en(Enable), .Q(PC), .clk(CLK), .clr(RST));
  // Probe on PC[11:0]
  or or_4 (or_4_out, d_ff_1_q, Interr1);
  or or_5 (or_5_out, d_ff_2_q, Interr2);
  or or_6 (or_6_out, d_ff_3_q, Interr3);
  Decoder #(.select(2), .disabled(0)) decoder_1 (
    .out1(decoder_1_out1), .out2(decoder_1_out2), .out3(decoder_1_out3), .sel(priority_encoder_1_out),
    .en(priority_encoder_1_gs));  // open: out0
  Hex_Digit_Display hex_digit_display_7 (.value(LedData[7:4]));  // open: dp
  Hex_Digit_Display hex_digit_display_8 (.value(LedData[3:0]));  // open: dp
  Counter #(.width(1), .max('h1)) counter_1 (
    .D(\硬布线控制器_1_syscall ), .count(and_1_out), .Q(counter_1_q), .clk(CLK), .clr(or_7_out));  // open: load, carry
  and and_1 (and_1_out, Stop, \硬布线控制器_1_syscall );
  and and_2 (and_2_out, or_4_out, ~Rst1);  // AND_Gate
  and and_3 (and_3_out, or_5_out, ~Rst2);  // AND_Gate
  and and_4 (and_4_out, or_6_out, ~Rst3);  // AND_Gate
  and and_5 (and_5_out, MTC0, comparator_1_eq);
  Comparator #(.width(5)) comparator_1 (.a(rd), .b(5'b00001), .eq(comparator_1_eq));  // open: gt, lt
  not not_1 (Enable, counter_1_q);
  or or_7 (or_7_out, RST, Go);
  ROM #(.addrWidth(10), .dataWidth(32)) rom_1 (
    .addr(PC[11:2]), .data({rom_1_data[31:21], rt, rd, rom_1_data[10:0]}));  // open: sel
  Adder #(.width(32)) adder_1 (.a(PC), .b(32'h4), .out(adder_1_out));  // open: cin, cout
  D_Flip_Flop u_IR1 (.clk(CLK), .D(and_2_out), .Q(Interr1));  // open: Qn, preset, en, reset
  D_Flip_Flop u_IR2 (.clk(CLK), .D(and_3_out), .Q(Interr2));  // open: Qn, preset, en, reset
  D_Flip_Flop u_IR3 (.clk(CLK), .D(and_4_out), .Q(Interr3));  // open: Qn, preset, en, reset
  and and_6 (Rst1, decoder_1_out1, ERET);
  and and_7 (Rst2, decoder_1_out2, ERET);
  and and_8 (Rst3, decoder_1_out3, ERET);
  Multiplexer #(.enable("false")) multiplexer_6 (
    .in0(1'b0), .in1(\屏蔽字_out [0]), .out(multiplexer_6_out), .sel(and_5_out));
  Multiplexer #(.enable("false")) multiplexer_7 (
    .in0(1'b0), .in1(\屏蔽字_out [1]), .out(multiplexer_7_out), .sel(and_5_out));
  Multiplexer #(.enable("false")) multiplexer_8 (
    .in0(1'b0), .in1(\屏蔽字_out [2]), .out(multiplexer_8_out), .sel(and_5_out));
  Multiplexer #(.enable("false")) multiplexer_9 (
    .in0(1'b0), .in1(\屏蔽字_out [3]), .out(multiplexer_9_out), .sel(and_5_out));
  D_Flip_Flop d_ff_4 (
    .clk(CLK), .D(multiplexer_6_out), .Q(\屏蔽字 [0]), .Qn(d_ff_4_qn), .en(and_5_out));  // open: preset, reset
  D_Flip_Flop d_ff_5 (
    .clk(CLK), .D(multiplexer_7_out), .Q(\屏蔽字 [1]), .Qn(d_ff_5_qn), .en(and_5_out));  // open: preset, reset
  D_Flip_Flop d_ff_6 (
    .clk(CLK), .D(multiplexer_8_out), .Q(\屏蔽字 [2]), .Qn(d_ff_6_qn), .en(and_5_out));  // open: preset, reset
  D_Flip_Flop d_ff_7 (
    .clk(CLK), .D(multiplexer_9_out), .Q(\屏蔽字 [3]), .Qn(d_ff_7_qn), .en(and_5_out));  // open: preset, reset
  // Probe on \总周期数 
  // Probe on \无条件分支数 
  // Probe on \条件分支成功数 
  \硬布线控制器  \u_硬布线控制器_1  (
    .Func(rom_1_data[5:0]), .OP(rom_1_data[31:26]), .ALU_OP(\硬布线控制器_1_alu_op ),
    .MemToReg(\硬布线控制器_1_memtoreg ), .MemWrite(\硬布线控制器_1_memwrite ), .ALU_SRC(\硬布线控制器_1_alu_src ),
    .RegWrite(\硬布线控制器_1_regwrite ), .SysCALL(\硬布线控制器_1_syscall ), .SignedExt(SignedExt),
    .RegDst(\硬布线控制器_1_regdst ), .JR(\硬布线控制器_1_jr ), .JMP(JMP), .Beq(\硬布线控制器_1_beq ), .JAL(\硬布线控制器_1_jal ),
    .Bne(\硬布线控制器_1_bne ), .LH(LH), .BLEZ(\硬布线控制器_1_blez ), .SRLV(SRLV), .ERET(ERET), .MFC0(MFC0),
    .MTC0(MTC0), .MF(rom_1_data[25:21]));
  assign bit_extender_1_out = {{16{1'b0}}, {rd, rom_1_data[10:0]}};  // Bit_Extender bit_extender_1
  assign bit_extender_2_out = {{16{rd[4]}}, {rd, rom_1_data[10:0]}};  // Bit_Extender bit_extender_2
  assign bit_extender_3_out = {{6{rom_1_data[25]}}, {rom_1_data[25:21], rt, rd, rom_1_data[10:0]}};  // Bit_Extender bit_extender_3
  Multiplexer #(.width(5), .enable("false")) multiplexer_10 (
    .in0(rom_1_data[25:21]), .in1(5'b00100), .out(multiplexer_10_out), .sel(\硬布线控制器_1_syscall ));
  Multiplexer #(.width(5), .enable("false")) multiplexer_11 (
    .in0(rt), .in1(5'b00010), .out(multiplexer_11_out), .sel(\硬布线控制器_1_syscall ));
  Multiplexer #(.width(5), .enable("false")) multiplexer_12 (
    .in0(rt), .in1(rd), .out(multiplexer_12_out), .sel(\硬布线控制器_1_regdst ));
  Multiplexer #(.width(5), .enable("false")) multiplexer_13 (
    .in0(multiplexer_12_out), .in1({5{1'b1}}), .out(multiplexer_13_out), .sel(\硬布线控制器_1_jal ));
  Multiplexer #(.width(32), .enable("false")) multiplexer_14 (
    .in0(bit_extender_1_out), .in1(bit_extender_2_out), .out(multiplexer_14_out), .sel(SignedExt));
  Multiplexer #(.width(32), .enable("false")) multiplexer_15 (
    .in0(multiplexer_26_out), .in1(adder_1_out), .out(multiplexer_15_out), .sel(\硬布线控制器_1_jal ));
  Shifter #(.width(32)) shifter_1 (.in(bit_extender_3_out), .\dist (5'b00010), .out(shifter_1_out));
  and and_9 (and_9_out, MTC0, comparator_2_eq);
  Comparator #(.width(5)) comparator_2 (.a(rd), .b(5'b00010), .eq(comparator_2_eq));  // open: gt, lt
  not not_2 (not_2_out, IE_out[0]);
  Comparator #(.width(5)) comparator_3 (.a(rd), .b(5'b00011), .eq(comparator_3_eq));  // open: gt, lt
  and and_10 (and_10_out, 1'b0, d_ff_4_qn);
  and and_11 (and_11_out, Interr1, d_ff_5_qn);
  and and_12 (and_12_out, Interr2, d_ff_6_qn);
  and and_13 (and_13_out, Interr3, d_ff_7_qn);
  Counter #(.width(16), .max('hffff)) counter_2 (
    .count(Enable), .Q(\总周期数 ), .clk(CLK), .clr(RST));  // open: load, D, carry
  Multiplexer #(.width(32), .enable("false")) multiplexer_16 (
    .in0(multiplexer_15_out), .in1(COP0_Data), .out(multiplexer_16_out), .sel(MFC0));
  Multiplexer #(.width(32), .enable("false")) multiplexer_17 (
    .in0(PC), .in1(EPC_out), .out(multiplexer_17_out), .sel(and_9_out));
  Multiplexer #(.enable("false")) multiplexer_18 (
    .in0(IR), .in1(not_2_out), .out(multiplexer_18_out), .sel(and_14_out));
  and and_14 (and_14_out, MTC0, comparator_3_eq);
  Demultiplexer #(.select(2), .width(32), .enable("false")) demultiplexer_1 (
    .out1(\屏蔽字_out ), .out2(EPC_out), .out3(IE_out), .in(R2), .sel(rd[1:0]));  // open: out0
  Priority_Encoder #(.select(2)) priority_encoder_2 (
    .in0(and_10_out), .in1(and_11_out), .in2(and_12_out), .in3(and_13_out), .out(priority_encoder_2_out),
    .gs(Interr));  // open: en_out, en_in
  not not_3 (Stop, comparator_4_eq);
  and and_15 (and_15_out, comparator_4_eq, \硬布线控制器_1_syscall );
  MIPS_Regifile mips_regifile_1 (
    .Din(multiplexer_16_out), .Clk(CLK), .R1(mips_regifile_1_r1), .R2(mips_regifile_1_r2),
    .WE(\硬布线控制器_1_regwrite ), .W_num(multiplexer_13_out), .R1_num(multiplexer_10_out),
    .R2_num(multiplexer_11_out));
  Shifter #(.width(32)) shifter_2 (.in(multiplexer_14_out), .\dist (5'b00010), .out(shifter_2_out));
  Register #(.width(32)) u_EPC (.D(multiplexer_17_out), .en(or_8_out), .Q(EPC), .clk(CLK));  // open: clr
  or or_8 (or_8_out, and_9_out, IR);
  Register #(.width(1)) IE (.D(multiplexer_18_out), .en(or_9_out), .Q(IE_q), .clk(CLK));  // open: clr
  or or_9 (or_9_out, and_14_out, ERET, IR);
  Multiplexer #(.select(2), .width(32), .enable("false")) multiplexer_19 (
    .in1({{28{1'b0}}, \屏蔽字 }), .in2(EPC), .out(COP0_Data), .sel(rd[1:0]));  // open: in0, in3
  Register #(.width(32)) register_1 (.D(mips_regifile_1_r1), .en(and_15_out), .Q(LedData), .clk(CLK), .clr(RST));
  Comparator #(.width(32)) comparator_4 (.a(32'h22), .b(mips_regifile_1_r2), .eq(comparator_4_eq));  // open: gt, lt
  Multiplexer #(.width(32), .enable("false")) multiplexer_20 (
    .in0(mips_regifile_1_r2), .in1(multiplexer_14_out), .out(multiplexer_20_out), .sel(\硬布线控制器_1_alu_src ));
  Multiplexer #(.width(32), .enable("false")) multiplexer_21 (
    .in0({32{1'b0}}), .in1(mips_regifile_1_r2), .out(R2), .sel(MTC0));
  Adder #(.width(32)) adder_2 (.a(shifter_2_out), .b(adder_1_out), .out(adder_2_out));  // open: cin, cout
  not not_4 (not_4_out, IE_q);
  Multiplexer #(.select(2), .width(32), .enable("false")) multiplexer_22 (
    .in1(32'h4), .in2(32'h20c), .in3(32'h414), .out(InterruptAddr), .sel(priority_encoder_2_out));  // open: in0
  Counter #(.width(16), .max('hffff)) counter_3 (
    .count(JMP), .Q(\无条件分支数 ), .clk(CLK), .clr(RST));  // open: load, D, carry
  Multiplexer #(.width(5), .enable("false")) multiplexer_23 (
    .in0(rom_1_data[10:6]), .in1(mips_regifile_1_r1[4:0]), .out(multiplexer_23_out), .sel(SRLV));
  and and_16 (IR, not_4_out, Interr);
  Comparator #(.width(32)) comparator_5 (
    .a(mips_regifile_1_r1), .b({32{1'b0}}), .eq(comparator_5_eq), .lt(comparator_5_lt));  // open: gt
  or or_10 (or_10_out, comparator_5_eq, comparator_5_lt);
  not not_5 (not_5_out, mips_alu_1_equal);
  MIPS_ALU mips_alu_1 (
    .X(mips_regifile_1_r1), .Y(multiplexer_20_out), .AluOP(\硬布线控制器_1_alu_op ), .Equal(mips_alu_1_equal),
    .Result(mips_alu_1_result), .shamt(multiplexer_23_out));  // open: Result_2
  Counter #(.width(16), .max('hffff)) counter_4 (
    .count(BAC), .Q(\条件分支成功数 ), .clk(CLK), .clr(RST));  // open: load, D, carry
  and and_17 (and_17_out, or_10_out, \硬布线控制器_1_blez );
  and and_18 (and_18_out, mips_alu_1_equal, \硬布线控制器_1_beq );
  and and_19 (and_19_out, not_5_out, \硬布线控制器_1_bne );
  or or_11 (BAC, and_18_out, and_17_out, and_19_out);
  Multiplexer #(.width(16), .enable("false")) multiplexer_24 (
    .in0(mips_ram_1_p6), .in1(mips_ram_1_p6_2), .out(multiplexer_24_out), .sel(mips_alu_1_result[1]));
  assign bit_extender_4_out = {{16{multiplexer_24_out[15]}}, multiplexer_24_out};  // Bit_Extender bit_extender_4
  // MIPS_RAM mips_ram_1: pin names not known; wires that end beside it: mips_alu_1_result[11:2], mips_regifile_1_r2, \硬布线控制器_1_memwrite , CLK, RST, {mips_ram_1_p6_2, mips_ram_1_p6}
  Multiplexer #(.width(32), .enable("false")) multiplexer_25 (
    .in0({mips_ram_1_p6_2, mips_ram_1_p6}), .in1(bit_extender_4_out), .out(multiplexer_25_out), .sel(LH));
  Multiplexer #(.width(32), .enable("false")) multiplexer_26 (
    .in0(mips_alu_1_result), .in1(multiplexer_25_out), .out(multiplexer_26_out), .sel(\硬布线控制器_1_memtoreg ));

  // Notes on the sheet:
  //   中断源
  //   中断等待指示
  //   设中断屏蔽字为1号寄存器
  //   数码管输出
  //   Reset 
  //   Reset 
  //   Reset 
  //   指令存储器
  //   contents of rom_1 (hex, n*v repeats v):
  //   8000d87 23bdfffc afa10000 23bdfffc afa20000 23bdfffc afa30000 23bdfffc afa40000 23bdfffc afa50000
  //   23bdfffc afa60000 23bdfffc afa70000 23bdfffc afa80000 23bdfffc afa90000 23bdfffc afaa0000 23bdfffc
  //   afab0000 23bdfffc afac0000 23bdfffc afad0000 23bdfffc afae0000 23bdfffc afaf0000 23bdfffc afb00000
  //   23bdfffc afb10000 23bdfffc afb20000 23bdfffc afb30000 23bdfffc afb40000 23bdfffc afb50000 23bdfffc
  //   afb60000 23bdfffc afb70000 23bdfffc afb80000 23bdfffc afb90000 40010800 23bdfffc afa10000 40021000
  //   23bdfffc afa20000 20010003 40810800 20030001 40831800 20160001 20140006 20150001 168020 108100
  //   2149825 132020 20020022 c 1600fffa 295a022 1680fff7 40801800 8fa20000 23bd0004 40821000 8fa10000
  //   23bd0004 40810800 8fb90000 23bd0004 8fb80000 23bd0004 8fb70000 23bd0004 8fb60000 23bd0004 8fb50000
  //   23bd0004 8fb40000 23bd0004 8fb30000 23bd0004 8fb20000 23bd0004 8fb10000 23bd0004 8fb00000 23bd0004
  //   8faf0000 23bd0004 8fae0000 23bd0004 8fad0000 23bd0004 8fac0000 23bd0004 8fab0000 23bd0004 8faa0000
  //   23bd0004 8fa90000 23bd0004 8fa80000 23bd0004 8fa70000 23bd0004 8fa60000 23bd0004 8fa50000 23bd0004
  //   8fa40000 23bd0004 8fa30000 23bd0004 8fa20000 23bd0004 8fa10000 23bd0004 42000018 23bdfffc afa10000
  //   23bdfffc afa20000 23bdfffc afa30000 23bdfffc afa40000 23bdfffc afa50000 23bdfffc afa60000 23bdfffc
  //   afa70000 23bdfffc afa80000 23bdfffc afa90000 23bdfffc afaa0000 23bdfffc afab0000 23bdfffc afac0000
  //   23bdfffc afad0000 23bdfffc afae0000 23bdfffc afaf0000 23bdfffc afb00000 23bdfffc afb10000 23bdfffc
  //   afb20000 23bdfffc afb30000 23bdfffc afb40000 23bdfffc afb50000 23bdfffc afb60000 23bdfffc afb70000
  //   23bdfffc afb80000 23bdfffc afb90000 40010800 23bdfffc afa10000 40021000 23bdfffc afa20000 20010007
  //   40810800 20030001 40831800 20160002 20140006 20150001 168020 108100 2149825 132020 20020022 c
  //   1600fffa 295a022 1680fff7 40801800 8fa20000 23bd0004 40821000 8fa10000 23bd0004 40810800 8fb90000
  //   23bd0004 8fb80000 23bd0004 8fb70000 23bd0004 8fb60000 23bd0004 8fb50000 23bd0004 8fb40000 23bd0004
  //   8fb30000 23bd0004 8fb20000 23bd0004 8fb10000 23bd0004 8fb00000 23bd0004 8faf0000 23bd0004 8fae0000
  //   23bd0004 8fad0000 23bd0004 8fac0000 23bd0004 8fab0000 23bd0004 8faa0000 23bd0004 8fa90000 23bd0004
  //   8fa80000 23bd0004 8fa70000 23bd0004 8fa60000 23bd0004 8fa50000 23bd0004 8fa40000 23bd0004 8fa30000
  //   23bd0004 8fa20000 23bd0004 8fa10000 23bd0004 42000018 23bdfffc afa10000 23bdfffc afa20000 23bdfffc
  //   afa30000 23bdfffc afa40000 23bdfffc afa50000 23bdfffc afa60000 23bdfffc afa70000 23bdfffc afa80000
  //   23bdfffc afa90000 23bdfffc afaa0000 23bdfffc afab0000 23bdfffc afac0000 23bdfffc afad0000 23bdfffc
  //   afae0000 23bdfffc afaf0000 23bdfffc afb00000 23bdfffc afb10000 23bdfffc afb20000 23bdfffc afb30000
  //   23bdfffc afb40000 23bdfffc afb50000 23bdfffc afb60000 23bdfffc afb70000 23bdfffc afb80000 23bdfffc
  //   afb90000 40010800 23bdfffc afa10000 40021000 23bdfffc afa20000 2001000f 40810800 20030001 40831800
  //   20160003 20140006 20150001 168020 108100 2149825 132020 20020022 c 1600fffa 295a022 1680fff7
  //   40801800 8fa20000 23bd0004 40821000 8fa10000 23bd0004 40810800 8fb90000 23bd0004 8fb80000 23bd0004
  //   8fb70000 23bd0004 8fb60000 23bd0004 8fb50000 23bd0004 8fb40000 23bd0004 8fb30000 23bd0004 8fb20000
  //   23bd0004 8fb10000 23bd0004 8fb00000 23bd0004 8faf0000 23bd0004 8fae0000 23bd0004 8fad0000 23bd0004
  //   8fac0000 23bd0004 8fab0000 23bd0004 8faa0000 23bd0004 8fa90000 23bd0004 8fa80000 23bd0004 8fa70000
  //   23bd0004 8fa60000 23bd0004 8fa50000 23bd0004 8fa40000 23bd0004 8fa30000 23bd0004 8fa20000 23bd0004
  //   8fa10000 23bd0004 42000018 20110200 20020022 112020 c 2231ffff 1620fffc 4*0 2002000a c 2002000a c
  //   BLEZ
  //   OP
  //   Func
  //   rs
  //   指令字
  //   rt
  //   rd
  //   Shamt
  //   JMP
  //   JR
  //   OP
  //   Func
  //   Syscall
  //   Beq
  //   Bne
  //   MemToReg
  //   MemWrite
  //   AluOP
  //   AluSrcB
  //   RegWrite
  //   JAL
  //   RegDst
  //   $a0
  //   $v0
  //   设EPC为2号寄存器
  //   设IE为3号寄存器
  //   COP0
endmodule

module \流水中断  (
);

  wire and_1_out, and_2_out, and_3_out, and_4_out, and_5_out, and_6_out, and_10_out, and_11_out, and_12_out,
       and_13_out, and_14_out, and_15_out, and_16_out, and_17_out, and_18_out, and_20_out, and_21_out,
       and_22_out, and_23_out, BAC, CLK, comparator_1_eq, comparator_2_eq, comparator_3_eq, comparator_4_eq,
       comparator_5_eq, comparator_6_eq, comparator_6_lt, d_ff_1_q, d_ff_2_q, d_ff_3_q, d_ff_4_qn, d_ff_5_qn,
       d_ff_6_qn, d_ff_7_qn, decoder_1_out1, decoder_1_out2, decoder_1_out3, ERET, ex_mem_1_halt_out,
       ex_mem_1_jal_out, ex_mem_1_lh_out, ex_mem_1_memtoreg_out, ex_mem_1_memwrite_out, ex_mem_1_regdst_out,
       ex_mem_1_syscall_out, EX_RegWrite, Go, Halt, id_ex_1_alusrcb_out, id_ex_1_beq_out, id_ex_1_blez_out,
       id_ex_1_bne_out, id_ex_1_jal_out, id_ex_1_lh_out, id_ex_1_memtoreg_out, id_ex_1_memwrite_out,
       id_ex_1_regdst_out, id_ex_1_syscall_out, IE_q, Interr, Interr1, Interr2, Interr3, IR, IR1, IR2, IR3,
       JMP, JR, LoadUse, MEM_RegWrite, mem_wb_1_halt_out, mem_wb_1_jal_out, mem_wb_1_memtoreg_out,
       mem_wb_1_regdst_out, mips_alu_1_equal, MTC0, multiplexer_6_out, multiplexer_7_out, multiplexer_8_out,
       multiplexer_9_out, multiplexer_18_out, not_1_out, not_2_out, not_3_out, not_4_out, not_5_out,
       not_6_out, not_7_out, not_8_out, or_4_out, or_5_out, or_6_out, or_7_out, or_8_out, or_9_out,
       or_10_out, or_11_out, or_13_out, priority_encoder_1_gs, RegW, RST, Rst1, Rst2, Rst3, SignedExt, SRLV,
       SysC, W1, W2, W3, \数据相关 , \硬布线控制器_1_alu_src , \硬布线控制器_1_beq , \硬布线控制器_1_blez , \硬布线控制器_1_bne ,
       \硬布线控制器_1_jal , \硬布线控制器_1_jmp , \硬布线控制器_1_jr , \硬布线控制器_1_lh , \硬布线控制器_1_memtoreg ,
       \硬布线控制器_1_memwrite , \硬布线控制器_1_regdst , \硬布线控制器_1_regwrite , \硬布线控制器_1_srlv , \硬布线控制器_1_syscall ;
  wire [1:0] priority_encoder_1_out, priority_encoder_2_out, R1_Forward, R2_Forward, \数据相关检测_1_r1_forward ,
       \数据相关检测_1_r2_forward ;
  wire [1:1] mem_wb_1_interrupt_out;
  wire [2:0] ex_mem_1_interrupt_out, id_ex_1_interrupt_out, \中断信号 ;
  wire [3:0] id_ex_1_aluop_out, \屏蔽字 , \硬布线控制器_1_alu_op ;
  wire [4:0] EX_WriteReg_num, id_ex_1_shamt_out, ID_R1_num, ID_R2_num, if_id_1_ir_out, MEM_WriteReg_num,
       multiplexer_10_out, multiplexer_14_out, multiplexer_15_out, multiplexer_22_out, multiplexer_26_out,
       multiplexer_28_out, rd;
  wire [5:0] EX_OP, Func, MEM_OP, OP;
  wire [15:0] adder_3_out, \LoadUse次数 , multiplexer_23_out, multiplier_1_out, \总周期数 , \插入气泡数 , \无条件分支数 ,
       \条件分支成功数 ;
  wire [25:0] ex_mem_1_ir_out, id_ex_1_ir_out;
  wire [25:11] if_id_1_ir_out_2;
  wire [31:0] adder_1_out, adder_2_out, bit_extender_1_out, bit_extender_2_out, bit_extender_3_out,
       bit_extender_4_out, COP0_Data, EPC, EPC_out, ex_mem_1_alur_out, ex_mem_1_pc_out, ex_mem_1_r2_out,
       EX_PC, id_ex_1_address_out, id_ex_1_imm_out, id_ex_1_pc_out, id_ex_1_r1_out, id_ex_1_r2_out, ID_PC,
       IE_out, if_id_1_pc_out, IF_PC, InterruptAddr, LedData, MEM_PC, mem_wb_1_alur_out, mem_wb_1_ir_out,
       mem_wb_1_memd_out, mem_wb_1_pc_out, mem_wb_1_r2_out, mips_alu_1_result, mips_ram_1_p6,
       mips_regifile_1_r1, mips_regifile_1_r2, multiplexer_1_out, multiplexer_2_out, multiplexer_3_out,
       multiplexer_4_out, multiplexer_5_out, multiplexer_11_out, multiplexer_16_out, multiplexer_17_out,
       multiplexer_21_out, multiplexer_24_out, multiplexer_25_out, multiplexer_27_out, multiplexer_29_out,
       R2, rom_1_data, shifter_1_out, shifter_2_out, WB_PC, \屏蔽字_out ;
  wire [31:5] multiplexer_15_out_2;

  Button \u_总复位  (.out(RST));
  Button _1 (.out(IR1));
  Button _2 (.out(IR2));
  Button _3 (.out(IR3));
  Button \u_继续运行  (.out(Go));
  LED led_1 (.in(W1));
  LED led_2 (.in(W2));
  LED led_3 (.in(W3));
  Multiplexer #(.width(32), .enable("false")) multiplexer_1 (
    .in0(adder_1_out), .in1(adder_2_out), .out(multiplexer_1_out), .sel(BAC));
  Multiplexer #(.width(32), .enable("false")) multiplexer_2 (
    .in0(multiplexer_1_out), .in1(multiplexer_3_out), .out(multiplexer_2_out), .sel(JMP));
  Multiplexer #(.width(32), .enable("false")) multiplexer_3 (
    .in0(id_ex_1_address_out), .in1({multiplexer_15_out_2, multiplexer_15_out}), .out(multiplexer_3_out),
    .sel(JR));
  Hex_Digit_Display hex_digit_display_1 (.value(LedData[31:28]));  // open: dp
  Multiplexer #(.width(32), .enable("false")) multiplexer_4 (
    .in0(multiplexer_2_out), .in1(InterruptAddr), .out(multiplexer_4_out), .sel(IR));
  Hex_Digit_Display hex_digit_display_2 (.value(LedData[27:24]));  // open: dp
  Hex_Digit_Display hex_digit_display_3 (.value(LedData[23:20]));  // open: dp
  not not_1 (not_1_out, LoadUse);
  and and_1 (and_1_out, not_1_out, Halt);
  Multiplexer #(.width(32), .enable("false")) multiplexer_5 (
    .in0(multiplexer_4_out), .in1(EPC), .out(multiplexer_5_out), .sel(ERET));
  // Probe on multiplexer_5_out[11:0]
  Hex_Digit_Display hex_digit_display_4 (.value(LedData[19:16]));  // open: dp
  Hex_Digit_Display hex_digit_display_5 (.value(LedData[15:12]));  // open: dp
  Counter #(.width(16), .max('hffff)) counter_1 (
    .count(Halt), .Q(\总周期数 ), .clk(CLK), .clr(RST));  // open: load, D, carry
  Register #(.width(32)) PC_2 (.D(multiplexer_5_out), .en(and_1_out), .Q(IF_PC), .clk(CLK), .clr(RST));
  or or_1 (W1, Interr1, d_ff_1_q);
  or or_2 (W2, Interr2, d_ff_2_q);
  or or_3 (W3, Interr3, d_ff_3_q);
  Hex_Digit_Display hex_digit_display_6 (.value(LedData[7:4]));  // open: dp
  Hex_Digit_Display hex_digit_display_7 (.value(LedData[11:8]));  // open: dp
  Clock clock_1 (.out(CLK));
  Adder #(.width(32)) adder_1 (.a(IF_PC), .b(32'h4), .out(adder_1_out));  // open: cin, cout
  not not_2 (not_2_out, LoadUse);
  D_Flip_Flop d_ff_1 (.clk(IR1), .D(1'b1), .Q(d_ff_1_q), .reset(Interr1));  // open: Qn, preset, en
  D_Flip_Flop d_ff_2 (.clk(IR2), .D(1'b1), .Q(d_ff_2_q), .reset(Interr2));  // open: Qn, preset, en
  D_Flip_Flop d_ff_3 (.clk(IR3), .D(1'b1), .Q(d_ff_3_q), .reset(Interr3));  // open: Qn, preset, en
  Priority_Encoder #(.select(2)) priority_encoder_1 (
    .in0(1'b0), .in1(Interr1), .in2(Interr2), .in3(Interr3), .out(priority_encoder_1_out),
    .gs(priority_encoder_1_gs));  // open: en_out, en_in
  Hex_Digit_Display hex_digit_display_8 (.value(LedData[3:0]));  // open: dp
  IF_ID if_id_1 (
    .PC_in(adder_1_out), .IR_in(rom_1_data), .PC_out(if_id_1_pc_out),
    .IR_out({OP, if_id_1_ir_out_2, if_id_1_ir_out, Func}), .Reset(or_7_out), .CLK(CLK), .Enable(and_2_out),
    .PCr_in(IF_PC), .PCr_out(ID_PC));  // open: PC_G_in, PC_G_out, HG_in, HG_out
  ROM #(.addrWidth(10), .dataWidth(32)) rom_1 (.addr(IF_PC[11:2]), .data(rom_1_data));  // open: sel
  and and_2 (and_2_out, not_2_out, Halt);
  or or_4 (or_4_out, d_ff_1_q, Interr1);
  or or_5 (or_5_out, d_ff_2_q, Interr2);
  or or_6 (or_6_out, d_ff_3_q, Interr3);
  Decoder #(.select(2), .disabled(0)) decoder_1 (
    .out1(decoder_1_out1), .out2(decoder_1_out2), .out3(decoder_1_out3), .sel(priority_encoder_1_out),
    .en(priority_encoder_1_gs));  // open: out0
  Comparator #(.width(5)) comparator_1 (.a(rd), .b(5'b00001), .eq(comparator_1_eq));  // open: gt, lt
  and and_3 (and_3_out, or_4_out, ~Rst1);  // AND_Gate
  and and_4 (and_4_out, or_5_out, ~Rst2);  // AND_Gate
  and and_5 (and_5_out, or_6_out, ~Rst3);  // AND_Gate
  and and_6 (and_6_out, MTC0, comparator_1_eq);
  // Probe on \总周期数 
  // Probe on \无条件分支数 
  // Probe on \条件分支成功数 
  // Probe on \插入气泡数 
  // Probe on \LoadUse次数 
  assign bit_extender_1_out = {{16{1'b0}}, {if_id_1_ir_out_2[15:11], if_id_1_ir_out, Func}};  // Bit_Extender bit_extender_1
  assign bit_extender_2_out = {{16{if_id_1_ir_out_2[15]}}, {if_id_1_ir_out_2[15:11], if_id_1_ir_out, Func}};  // Bit_Extender bit_extender_2
  assign bit_extender_3_out = {{6{if_id_1_ir_out_2[25]}}, {if_id_1_ir_out_2, if_id_1_ir_out, Func}};  // Bit_Extender bit_extender_3
  D_Flip_Flop u_IR1 (.clk(CLK), .D(and_3_out), .Q(Interr1), .en(not_3_out));  // open: Qn, preset, reset
  D_Flip_Flop u_IR2 (.clk(CLK), .D(and_4_out), .Q(Interr2), .en(not_3_out));  // open: Qn, preset, reset
  D_Flip_Flop u_IR3 (.clk(CLK), .D(and_5_out), .Q(Interr3), .en(not_3_out));  // open: Qn, preset, reset
  and and_7 (Rst1, decoder_1_out1, ERET);
  and and_8 (Rst2, decoder_1_out2, ERET);
  and and_9 (Rst3, decoder_1_out3, ERET);
  Multiplexer #(.enable("false")) multiplexer_6 (
    .in0(1'b0), .in1(\屏蔽字_out [0]), .out(multiplexer_6_out), .sel(and_6_out));
  Multiplexer #(.enable("false")) multiplexer_7 (
    .in0(1'b0), .in1(\屏蔽字_out [1]), .out(multiplexer_7_out), .sel(and_6_out));
  Multiplexer #(.enable("false")) multiplexer_8 (
    .in0(1'b0), .in1(\屏蔽字_out [2]), .out(multiplexer_8_out), .sel(and_6_out));
  Multiplexer #(.enable("false")) multiplexer_9 (
    .in0(1'b0), .in1(\屏蔽字_out [3]), .out(multiplexer_9_out), .sel(and_6_out));
  // Probe on IF_PC[11:0]
  \硬布线控制器  \u_硬布线控制器_1  (
    .Func(Func), .OP(OP), .ALU_OP(\硬布线控制器_1_alu_op ), .MemToReg(\硬布线控制器_1_memtoreg ),
    .MemWrite(\硬布线控制器_1_memwrite ), .ALU_SRC(\硬布线控制器_1_alu_src ), .RegWrite(\硬布线控制器_1_regwrite ),
    .SysCALL(\硬布线控制器_1_syscall ), .SignedExt(SignedExt), .RegDst(\硬布线控制器_1_regdst ), .JR(\硬布线控制器_1_jr ),
    .JMP(\硬布线控制器_1_jmp ), .Beq(\硬布线控制器_1_beq ), .JAL(\硬布线控制器_1_jal ), .Bne(\硬布线控制器_1_bne ),
    .LH(\硬布线控制器_1_lh ), .BLEZ(\硬布线控制器_1_blez ), .SRLV(\硬布线控制器_1_srlv ), .ERET(\中断信号 [0]), .MFC0(\中断信号 [1]),
    .MTC0(\中断信号 [2]), .MF(if_id_1_ir_out_2[25:21]));
  Multiplexer #(.width(5), .enable("false")) multiplexer_10 (
    .in0(if_id_1_ir_out_2[20:16]), .in1(if_id_1_ir_out_2[15:11]), .out(multiplexer_10_out),
    .sel(\硬布线控制器_1_regdst ));
  Multiplexer #(.width(32), .enable("false")) multiplexer_11 (
    .in0(bit_extender_1_out), .in1(bit_extender_2_out), .out(multiplexer_11_out), .sel(SignedExt));
  Shifter #(.width(32)) shifter_1 (.in(bit_extender_3_out), .\dist (5'b00010), .out(shifter_1_out));
  D_Flip_Flop d_ff_4 (
    .clk(CLK), .D(multiplexer_6_out), .Q(\屏蔽字 [0]), .Qn(d_ff_4_qn), .en(and_6_out));  // open: preset, reset
  D_Flip_Flop d_ff_5 (
    .clk(CLK), .D(multiplexer_7_out), .Q(\屏蔽字 [1]), .Qn(d_ff_5_qn), .en(and_6_out));  // open: preset, reset
  D_Flip_Flop d_ff_6 (
    .clk(CLK), .D(multiplexer_8_out), .Q(\屏蔽字 [2]), .Qn(d_ff_6_qn), .en(and_6_out));  // open: preset, reset
  D_Flip_Flop d_ff_7 (
    .clk(CLK), .D(multiplexer_9_out), .Q(\屏蔽字 [3]), .Qn(d_ff_7_qn), .en(and_6_out));  // open: preset, reset
  // Probe on ID_PC[11:0]
  Multiplexer #(.width(5), .enable("false")) multiplexer_12 (
    .in0(if_id_1_ir_out_2[25:21]), .in1(5'b00100), .out(ID_R1_num), .sel(\硬布线控制器_1_syscall ));
  Multiplexer #(.width(5), .enable("false")) multiplexer_13 (
    .in0(if_id_1_ir_out_2[20:16]), .in1(5'b00010), .out(ID_R2_num), .sel(\硬布线控制器_1_syscall ));
  Multiplexer #(.width(5), .enable("false")) multiplexer_14 (
    .in0(multiplexer_10_out), .in1({5{1'b1}}), .out(multiplexer_14_out), .sel(\硬布线控制器_1_jal ));
  // Probe on EX_PC[11:0]
  // Probe on MEM_PC[11:0]
  Comparator #(.width(32)) comparator_2 (.a(EX_PC), .b({32{1'b0}}), .eq(comparator_2_eq));  // open: gt, lt
  not not_3 (not_3_out, comparator_2_eq);
  // Probe on WB_PC[11:0]
  or or_7 (or_7_out, JMP, IR, RST, ERET, BAC);
  MIPS_Regifile mips_regifile_1 (
    .Din(multiplexer_29_out), .Clk(CLK), .R1(mips_regifile_1_r1), .R2(mips_regifile_1_r2), .WE(RegW),
    .W_num(multiplexer_28_out), .R1_num(ID_R1_num), .R2_num(ID_R2_num));
  and and_10 (and_10_out, 1'b0, d_ff_4_qn);
  and and_11 (and_11_out, Interr1, d_ff_5_qn);
  and and_12 (and_12_out, Interr2, d_ff_6_qn);
  and and_13 (and_13_out, Interr3, d_ff_7_qn);
  or or_8 (or_8_out, or_7_out, LoadUse);
  ID_EX id_ex_1 (
    .BNE_in(\硬布线控制器_1_bne ), .IR_in({OP, if_id_1_ir_out_2, if_id_1_ir_out, Func}),
    .MemToReg_in(\硬布线控制器_1_memtoreg ), .PC_in(if_id_1_pc_out), .MemWrite_in(\硬布线控制器_1_memwrite ),
    .R1_in(mips_regifile_1_r1), .AluSrcB_in(\硬布线控制器_1_alu_src ), .R2_in(mips_regifile_1_r2),
    .RegWrite_in(\硬布线控制器_1_regwrite ), .Imm_in(multiplexer_11_out), .JAL_in(\硬布线控制器_1_jal ),
    .Address_in(shifter_1_out), .RegDst_in(\硬布线控制器_1_regdst ), .AluOP_in(\硬布线控制器_1_alu_op ),
    .Syscall_in(\硬布线控制器_1_syscall ), .Shamt_in(if_id_1_ir_out), .JMP_in(\硬布线控制器_1_jmp ),
    .JR_in(\硬布线控制器_1_jr ), .LH_in(\硬布线控制器_1_lh ), .SRLV_in(\硬布线控制器_1_srlv ), .BNE_out(id_ex_1_bne_out),
    .IR_out({EX_OP, id_ex_1_ir_out}), .MemToReg_out(id_ex_1_memtoreg_out), .PC_out(id_ex_1_pc_out),
    .MemWrite_out(id_ex_1_memwrite_out), .R1_out(id_ex_1_r1_out), .AluSrcB_out(id_ex_1_alusrcb_out),
    .R2_out(id_ex_1_r2_out), .RegWrite_out(EX_RegWrite), .Imm_out(id_ex_1_imm_out),
    .JAL_out(id_ex_1_jal_out), .Address_out(id_ex_1_address_out), .RegDst_out(id_ex_1_regdst_out),
    .AluOP_out(id_ex_1_aluop_out), .Syscall_out(id_ex_1_syscall_out), .Shamt_out(id_ex_1_shamt_out),
    .JMP_out(JMP), .JR_out(JR), .LH_out(id_ex_1_lh_out), .SRLV_out(SRLV), .Reset(or_8_out), .Enable(Halt),
    .CLK(CLK), .BEQ_in(\硬布线控制器_1_beq ), .BEQ_out(id_ex_1_beq_out), .BLEZ_in(\硬布线控制器_1_blez ),
    .BLEZ_out(id_ex_1_blez_out), .W__in(multiplexer_14_out), .W__out(EX_WriteReg_num), .PCr_in(ID_PC),
    .PCr_out(EX_PC), .Interrupt_in(\中断信号 ), .Interrupt_out(id_ex_1_interrupt_out));  // open: Halt_in, Halt_out, HG_in, HG_out, PCG_in, PCG_out
  Comparator #(.width(5)) comparator_3 (.a(rd), .b(5'b00010), .eq(comparator_3_eq));  // open: gt, lt
  Comparator #(.width(5)) comparator_4 (.a(rd), .b(5'b00011), .eq(comparator_4_eq));  // open: gt, lt
  Priority_Encoder #(.select(2)) priority_encoder_2 (
    .in0(and_10_out), .in1(and_11_out), .in2(and_12_out), .in3(and_13_out), .out(priority_encoder_2_out),
    .gs(Interr));  // open: en_out, en_in
  and and_14 (and_14_out, MTC0, comparator_3_eq);
  not not_4 (not_4_out, IE_out[0]);
  and and_15 (and_15_out, MTC0, comparator_4_eq);
  Demultiplexer #(.select(2), .width(32), .enable("false")) demultiplexer_1 (
    .out1(\屏蔽字_out ), .out2(EPC_out), .out3(IE_out), .in(R2), .sel(rd[1:0]));  // open: out0
  Multiplexer #(.select(2), .width(32), .enable("false")) multiplexer_15 (
    .in0(id_ex_1_r1_out), .in1(mem_wb_1_alur_out), .in2(mem_wb_1_memd_out), .in3(ex_mem_1_alur_out),
    .out({multiplexer_15_out_2, multiplexer_15_out}), .sel(R1_Forward));
  Multiplexer #(.select(2), .width(32), .enable("false")) multiplexer_16 (
    .in0(id_ex_1_r2_out), .in1(mem_wb_1_alur_out), .in2(mem_wb_1_memd_out), .in3(ex_mem_1_alur_out),
    .out(multiplexer_16_out), .sel(R2_Forward));
  Multiplexer #(.width(32), .enable("false")) multiplexer_17 (
    .in0(MEM_PC), .in1(EPC_out), .out(multiplexer_17_out), .sel(and_14_out));
  or or_9 (or_9_out, and_14_out, IR);
  and and_16 (and_16_out, or_9_out, not_3_out);
  Multiplexer #(.enable("false")) multiplexer_18 (
    .in0(IR), .in1(not_4_out), .out(multiplexer_18_out), .sel(and_15_out));
  or or_10 (or_10_out, and_15_out, ERET, IR);
  Multiplexer #(.select(2), .width(32), .enable("false")) multiplexer_19 (
    .in1({{28{1'b0}}, \屏蔽字 }), .in2(EPC), .out(COP0_Data), .sel(rd[1:0]));  // open: in0, in3
  Multiplexer #(.select(2), .width(32), .enable("false")) multiplexer_20 (
    .in1(32'h4), .in2(32'h20c), .in3(32'h414), .out(InterruptAddr), .sel(priority_encoder_2_out));  // open: in0
  Counter #(.width(16), .max('hffff)) counter_2 (
    .count(JMP), .Q(\无条件分支数 ), .clk(CLK), .clr(RST));  // open: load, D, carry
  Comparator #(.width(32)) comparator_5 (.a(32'h22), .b(multiplexer_21_out), .eq(comparator_5_eq));  // open: gt, lt
  Multiplexer #(.width(32), .enable("false")) multiplexer_21 (
    .in0(multiplexer_16_out), .in1(id_ex_1_imm_out), .out(multiplexer_21_out), .sel(id_ex_1_alusrcb_out));
  Register #(.width(32)) u_EPC (.D(multiplexer_17_out), .en(and_16_out), .Q(EPC), .clk(CLK));  // open: clr
  Register #(.width(1)) IE (.D(multiplexer_18_out), .en(or_10_out), .Q(IE_q), .clk(CLK));  // open: clr
  and and_17 (and_17_out, id_ex_1_syscall_out, comparator_5_eq);
  not not_5 (not_5_out, comparator_5_eq);
  and and_18 (and_18_out, not_5_out, id_ex_1_syscall_out);
  not not_6 (not_6_out, IE_q);
  and and_19 (IR, not_6_out, Interr);
  Counter #(.width(16), .max('hffff)) counter_3 (
    .count(BAC), .Q(\条件分支成功数 ), .clk(CLK), .clr(RST));  // open: load, D, carry
  Register #(.width(32)) register_1 (
    .D({multiplexer_15_out_2, multiplexer_15_out}), .en(and_17_out), .Q(LedData), .clk(CLK), .clr(RST));
  Multiplexer #(.width(5), .enable("false")) multiplexer_22 (
    .in0(id_ex_1_shamt_out), .in1(multiplexer_15_out), .out(multiplexer_22_out), .sel(SRLV));
  Comparator #(.width(32)) comparator_6 (
    .a({multiplexer_15_out_2, multiplexer_15_out}), .b({32{1'b0}}), .eq(comparator_6_eq), .lt(comparator_6_lt));  // open: gt
  or or_11 (or_11_out, comparator_6_eq, comparator_6_lt);
  not not_7 (not_7_out, mips_alu_1_equal);
  MIPS_ALU mips_alu_1 (
    .X({multiplexer_15_out_2, multiplexer_15_out}), .Y(multiplexer_21_out), .AluOP(id_ex_1_aluop_out),
    .Equal(mips_alu_1_equal), .Result(mips_alu_1_result), .shamt(multiplexer_22_out));  // open: Result_2
  Shifter #(.width(32)) shifter_2 (.in(id_ex_1_imm_out), .\dist (5'b00010), .out(shifter_2_out));
  and and_20 (and_20_out, or_11_out, id_ex_1_blez_out);
  and and_21 (and_21_out, mips_alu_1_equal, id_ex_1_beq_out);
  and and_22 (and_22_out, not_7_out, id_ex_1_bne_out);
  Adder #(.width(32)) adder_2 (.a(shifter_2_out), .b(id_ex_1_pc_out), .out(adder_2_out));  // open: cin, cout
  or or_12 (BAC, and_21_out, and_20_out, and_22_out);
  or or_13 (or_13_out, IR, ERET);
  EX_MEM ex_mem_1 (
    .MemToReg_in(id_ex_1_memtoreg_out), .IR_in({EX_OP, id_ex_1_ir_out}), .MemWrite_in(id_ex_1_memwrite_out),
    .PC_in(id_ex_1_pc_out), .RegWrite_in(EX_RegWrite), .R2_in(multiplexer_16_out), .JAL_in(id_ex_1_jal_out),
    .AluR_in(mips_alu_1_result), .RegDst_in(id_ex_1_regdst_out), .Halt_in(and_18_out),
    .Syscall_in(id_ex_1_syscall_out), .LH_in(id_ex_1_lh_out), .MemToReg_out(ex_mem_1_memtoreg_out),
    .IR_out({MEM_OP, ex_mem_1_ir_out}), .MemWrite_out(ex_mem_1_memwrite_out), .PC_out(ex_mem_1_pc_out),
    .RegWrite_out(MEM_RegWrite), .R2_out(ex_mem_1_r2_out), .JAL_out(ex_mem_1_jal_out),
    .AluR_out(ex_mem_1_alur_out), .RegDst_out(ex_mem_1_regdst_out), .Halt_out(ex_mem_1_halt_out),
    .Syscall_out(ex_mem_1_syscall_out), .LH_out(ex_mem_1_lh_out), .Reset(or_13_out), .Enable(Halt),
    .CLK(CLK), .W__in(EX_WriteReg_num), .W__out(MEM_WriteReg_num), .PCr_in(EX_PC), .PCr_out(MEM_PC),
    .Interrupt_in(id_ex_1_interrupt_out), .Interrupt_out(ex_mem_1_interrupt_out));
  Adder #(.width(16)) adder_3 (.a(\无条件分支数 ), .b(\条件分支成功数 ), .out(adder_3_out));  // open: cin, cout
  Multiplier #(.width(16)) multiplier_1 (.a(adder_3_out), .b(16'h2), .out(multiplier_1_out));  // open: cin, cout
  Adder #(.width(16)) adder_4 (.a(multiplier_1_out), .b(\LoadUse次数 ), .out(\插入气泡数 ));  // open: cin, cout
  Multiplexer #(.width(16), .enable("false")) multiplexer_23 (
    .in0(mips_ram_1_p6[15:0]), .in1(mips_ram_1_p6[31:16]), .out(multiplexer_23_out),
    .sel(ex_mem_1_alur_out[1]));
  // MIPS_RAM mips_ram_1: pin names not known; wires that end beside it: ex_mem_1_alur_out[11:2], ex_mem_1_r2_out, ex_mem_1_memwrite_out, CLK, RST, mips_ram_1_p6
  assign bit_extender_4_out = {{16{multiplexer_23_out[15]}}, multiplexer_23_out};  // Bit_Extender bit_extender_4
  \数据相关检测  \u_数据相关检测_1  (
    .OP(OP), .EX_WriteReg_num(EX_WriteReg_num), .EX_RegWrite(EX_RegWrite), .\数据相关 (\数据相关 ),
    .MEM_WriteReg_num(MEM_WriteReg_num), .MEM_RegWrite(MEM_RegWrite), .Func(Func), .Load_Use(LoadUse),
    .ID_R1_num(ID_R1_num), .ID_R2_num(ID_R2_num), .R1_Forward(\数据相关检测_1_r1_forward ),
    .R2_Forward(\数据相关检测_1_r2_forward ), .EX_OP(EX_OP), .MEM_OP(MEM_OP));
  Multiplexer #(.width(32), .enable("false")) multiplexer_24 (
    .in0(mips_ram_1_p6), .in1(bit_extender_4_out), .out(multiplexer_24_out), .sel(ex_mem_1_lh_out));
  MEM_WB mem_wb_1 (
    .MemToReg_in(ex_mem_1_memtoreg_out), .IR_in({MEM_OP, ex_mem_1_ir_out}), .RegWrite_in(MEM_RegWrite),
    .PC_in(ex_mem_1_pc_out), .JAL_in(ex_mem_1_jal_out), .MemD_in(multiplexer_24_out),
    .RegDst_in(ex_mem_1_regdst_out), .AluR_in(ex_mem_1_alur_out), .Syscall_in(ex_mem_1_syscall_out),
    .Halt_in(ex_mem_1_halt_out), .MemToReg_out(mem_wb_1_memtoreg_out),
    .IR_out({mem_wb_1_ir_out[31:16], rd, mem_wb_1_ir_out[10:0]}), .RegWrite_out(RegW),
    .PC_out(mem_wb_1_pc_out), .JAL_out(mem_wb_1_jal_out), .MemD_out(mem_wb_1_memd_out),
    .RegDst_out(mem_wb_1_regdst_out), .AluR_out(mem_wb_1_alur_out), .Syscall_out(SysC),
    .Halt_out(mem_wb_1_halt_out), .Reset(ERET), .Enable(Halt), .CLK(CLK), .W__in(MEM_WriteReg_num),
    .PCr_in(MEM_PC), .PCr_out(WB_PC), .Interrupt_in(ex_mem_1_interrupt_out),
    .Interrupt_out({MTC0, mem_wb_1_interrupt_out[1], ERET}), .R2_in(ex_mem_1_r2_out), .R2_out(mem_wb_1_r2_out));  // open: W__out
  Counter #(.width(16), .max('hffff)) counter_4 (
    .count(and_23_out), .Q(\LoadUse次数 ), .clk(CLK), .clr(RST));  // open: load, D, carry
  and and_23 (and_23_out, Halt, LoadUse);
  Register #(.width(4)) register_2 (
    .D({\数据相关检测_1_r2_forward , \数据相关检测_1_r1_forward }), .Q({R2_Forward, R1_Forward}), .clk(CLK), .clr(RST));  // open: en
  or or_14 (Halt, Go, RST, not_8_out);
  not not_8 (not_8_out, mem_wb_1_halt_out);
  Multiplexer #(.width(32), .enable("false")) multiplexer_25 (
    .in0(mem_wb_1_alur_out), .in1(mem_wb_1_memd_out), .out(multiplexer_25_out), .sel(mem_wb_1_memtoreg_out));
  Multiplexer #(.width(5), .enable("false")) multiplexer_26 (
    .in0(mem_wb_1_ir_out[20:16]), .in1(rd), .out(multiplexer_26_out), .sel(mem_wb_1_regdst_out));
  Multiplexer #(.width(32), .enable("false")) multiplexer_27 (
    .in0(multiplexer_25_out), .in1(mem_wb_1_pc_out), .out(multiplexer_27_out), .sel(mem_wb_1_jal_out));
  Multiplexer #(.width(5), .enable("false")) multiplexer_28 (
    .in0(multiplexer_26_out), .in1({5{1'b1}}), .out(multiplexer_28_out), .sel(mem_wb_1_jal_out));
  Multiplexer #(.width(32), .enable("false")) multiplexer_29 (
    .in0(multiplexer_27_out), .in1(COP0_Data), .out(multiplexer_29_out), .sel(mem_wb_1_interrupt_out[1]));
  Multiplexer #(.width(32), .enable("false")) multiplexer_30 (
    .in0({32{1'b0}}), .in1(mem_wb_1_r2_out), .out(R2), .sel(MTC0));

  // Notes on the sheet:
  //   中断源
  //   中断等待指示
  //   数码管输出
  //   指令存储器
  //   contents of rom_1 (hex, n*v repeats v):
  //   8000d87 23bdfffc afa10000 23bdfffc afa20000 23bdfffc afa30000 23bdfffc afa40000 23bdfffc afa50000
  //   23bdfffc afa60000 23bdfffc afa70000 23bdfffc afa80000 23bdfffc afa90000 23bdfffc afaa0000 23bdfffc
  //   afab0000 23bdfffc afac0000 23bdfffc afad0000 23bdfffc afae0000 23bdfffc afaf0000 23bdfffc afb00000
  //   23bdfffc afb10000 23bdfffc afb20000 23bdfffc afb30000 23bdfffc afb40000 23bdfffc afb50000 23bdfffc
  //   afb60000 23bdfffc afb70000 23bdfffc afb80000 23bdfffc afb90000 40010800 40021000 23bdfffc afa10000
  //   23bdfffc afa20000 20010003 40810800 20030001 40831800 20160001 20140006 20150001 168020 108100
  //   2149825 132020 20020022 c 1600fffa 295a022 1680fff7 40801800 8fa20000 23bd0004 8fa10000 23bd0004
  //   40821000 40810800 8fb90000 23bd0004 8fb80000 23bd0004 8fb70000 23bd0004 8fb60000 23bd0004 8fb50000
  //   23bd0004 8fb40000 23bd0004 8fb30000 23bd0004 8fb20000 23bd0004 8fb10000 23bd0004 8fb00000 23bd0004
  //   8faf0000 23bd0004 8fae0000 23bd0004 8fad0000 23bd0004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
  //   设中断屏蔽字为1号寄存器
  //   OP
  //   rs
  //   指令字
  //   rt
  //   Reset 
  //   Reset 
  //   Reset 
  //   Func
  //   rd
  //   Shamt
  //   JMP
  //   JR
  //   BLEZ
  //   $a0
  //   $v0
  //   Beq
  //   Bne
  //   MemToReg
  //   MemWrite
  //   AluOP
  //   AluSrcB
  //   RegWrite
  //   JAL
  //   RegDst
  //   不是气泡
  //   流水调试日志用
  //   设EPC为2号寄存器
  //   设IE为3号寄存器
  //   COP0
  //   rt
  //   rd
  //   W#
  //   Din
endmodule
